// Logisim project base.circ as structural Verilog: 5 circuits, main circuit player
module main (
);

  wire Clk, comparator_3_eq, comparator_4_eq, comparator_5_eq, comparator_6_eq, d_ff_1_q, d_ff_2_q, dX, dY,
       game_active, L, or_1_out, or_4_out, or_5_out, or_6_out, or_7_out, or_8_out, R, Reset;
  wire [1:0] collisioncheck_2_event_hit, comparator_2_eq;
  wire [2:0] ai_1_ai_x, ai_1_ai_x_1, ball_1_ball_x, ball_1_ball_y, player_1_player_x, player_1_player_x_1;
  wire [3:0] adder_1_out, adder_2_out, register_1_q, register_2_q;
  wire [7:0] ai_1_ai_screen_pixel, ball_1_out_6, ball_1_out_7, ball_1_out_8, ball_1_out_9, ball_1_out_10,
       ball_1_out_11, ball_1_out_12, ball_1_out_13, or_2_out, or_3_out, player_1_player_screen_pixel;

  Clock clock_1 (.out(Clk));
  Comparator #(.width(3), .mode("unsigned")) comparator_1 (
    .a(ball_1_ball_x), .b(3'b000), .eq(comparator_2_eq[1]));  // open: gt, lt
  Comparator #(.width(3), .mode("unsigned")) comparator_2 (
    .a(ball_1_ball_x), .b(3'b111), .eq(comparator_2_eq[0]));  // open: gt, lt
  Comparator #(.width(3), .mode("unsigned")) comparator_3 (
    .a(ball_1_ball_y), .b(3'b000), .eq(comparator_3_eq));  // open: gt, lt
  or or_1 (or_1_out, comparator_3_eq, comparator_4_eq);
  Comparator #(.width(3), .mode("unsigned")) comparator_4 (
    .a(ball_1_ball_y), .b(3'b111), .eq(comparator_4_eq));  // open: gt, lt
  ai ai_1 (
    .ball_x(ball_1_ball_x), .game_active(game_active), .Clk(Clk), .ai_screen_pixel(ai_1_ai_screen_pixel),
    .ai_x(ai_1_ai_x), .ai_x_1(ai_1_ai_x_1));
  ball ball_1 (
    .dX(dX), .dY(dY), .game_active(game_active), .clk(Clk), .ball_x(ball_1_ball_x), .out_6(ball_1_out_6),
    .out_7(ball_1_out_7), .out_8(ball_1_out_8), .out_9(ball_1_out_9), .out_10(ball_1_out_10),
    .out_11(ball_1_out_11), .out_12(ball_1_out_12), .out_13(ball_1_out_13), .ball_y(ball_1_ball_y));
  assign or_2_out = ai_1_ai_screen_pixel | ball_1_out_6;  // OR_Gate or_2, 8 bits wide
  assign or_3_out = ball_1_out_13 | player_1_player_screen_pixel;  // OR_Gate or_3, 8 bits wide
  player player_1 (
    .btnLeft(L), .btnRight(R), .game_active(game_active), .Clk(Clk),
    .player_screen_pixel(player_1_player_screen_pixel), .player_x(player_1_player_x),
    .player_x_1(player_1_player_x_1));
  or or_4 (or_4_out, comparator_2_eq[1], comparator_2_eq[0]);
  D_Flip_Flop #(.trigger("falling")) d_ff_1 (.clk(or_4_out), .D(dX), .Q(d_ff_1_q));  // open: Qn, preset, en, reset
  or or_5 (or_5_out, L, R);
  or or_6 (or_6_out, or_1_out, Reset);
  collisionCheck collisioncheck_1 (
    .player_x(ai_1_ai_x), .player_x_1(ai_1_ai_x_1), .ball_x(ball_1_ball_x), .ball_y(ball_1_ball_y),
    .coordinateToCheck(3'b001), .EVENT_HIT(collisioncheck_2_event_hit[1]));
  DotMatrix #(.inputtype("row"), .matrixcols(8), .matrixrows(8)) dotmatrix_1 (
    .row0(or_2_out), .row1(ball_1_out_7), .row2(ball_1_out_8), .row3(ball_1_out_9), .row4(ball_1_out_10),
    .row5(ball_1_out_11), .row6(ball_1_out_12), .row7(or_3_out));
  Button button_1 (.out(L));
  collisionCheck collisioncheck_2 (
    .player_x(player_1_player_x), .player_x_1(player_1_player_x_1), .ball_x(ball_1_ball_x),
    .ball_y(ball_1_ball_y), .coordinateToCheck(3'b110), .EVENT_HIT(collisioncheck_2_event_hit[0]));
  Multiplexer #(.select(2), .enable("false")) multiplexer_1 (
    .in0(d_ff_1_q), .in1(1'b1), .in2(1'b0), .in3(1'b0), .out(dX), .sel(comparator_2_eq));
  S_R_Flip_Flop s_r_ff_1 (.S(or_5_out), .clk(Clk), .R(or_6_out), .Q(game_active));  // open: Qn, preset, reset, en
  Button button_2 (.out(Reset));
  Button button_3 (.out(R));
  Hex_Digit_Display hex_digit_display_1 (.value(register_1_q));  // open: dp
  Register #(.width(4)) register_1 (
    .D(adder_1_out), .en(game_active), .Q(register_1_q), .clk(comparator_3_eq), .clr(or_8_out));
  Register #(.width(4)) register_2 (
    .D(adder_2_out), .en(game_active), .Q(register_2_q), .clk(comparator_4_eq), .clr(or_8_out));
  LED led_1 ();  // open: in
  LED led_2 ();  // open: in
  Hex_Digit_Display hex_digit_display_2 (.value(register_2_q));  // open: dp
  Adder #(.width(4)) adder_1 (.a(register_1_q), .b(4'b0001), .out(adder_1_out));  // open: cin, cout
  Adder #(.width(4)) adder_2 (.a(register_2_q), .b(4'b0001), .out(adder_2_out));  // open: cin, cout
  D_Flip_Flop #(.trigger("falling")) d_ff_2 (.clk(or_7_out), .D(dY), .Q(d_ff_2_q));  // open: Qn, preset, en, reset
  or or_7 (or_7_out, collisioncheck_2_event_hit[1], collisioncheck_2_event_hit[0]);
  Comparator #(.width(4), .mode("unsigned")) comparator_5 (
    .a(register_1_q), .b(4'b0101), .eq(comparator_5_eq));  // open: gt, lt
  Comparator #(.width(4), .mode("unsigned")) comparator_6 (
    .a(register_2_q), .b(4'b0101), .eq(comparator_6_eq));  // open: gt, lt
  Multiplexer #(.select(2), .enable("false")) multiplexer_2 (
    .in0(d_ff_2_q), .in1(1'b1), .in2(1'b0), .in3(1'b0), .out(dY), .sel(collisioncheck_2_event_hit));
  or or_8 (or_8_out, comparator_5_eq, Reset, comparator_6_eq);

  // Notes on the sheet:
  //   EVENT_HIT_LEFT_WALL
  //   EVENT_HIT_TOP_WALL
  //   EVENT_HIT_BOTTOM_WALL
  //   EVENT_HIT_RIGHT_WALL
  //   EVENT_HIT_AI
  //   EVENT_HIT_PLAYER
  //   PLAYER
  //   AI
endmodule

module player (
  input  btnLeft,
  input  btnRight,
  input  game_active,
  input  Clk,
  output [7:0] player_screen_pixel,
  output [2:0] player_x,
  output [2:0] player_x_1
);

  wire and_1_out, and_2_out, comparator_1_eq, comparator_2_eq, not_1_out;
  wire [2:0] multiplexer_1_out, multiplexer_2_out, multiplexer_3_out, subtractor_1_out;
  wire [7:0] decoder_1_out0, shifter_1_out, shifter_2_out;

  Multiplexer #(.width(3), .enable("false")) multiplexer_1 (
    .in0(multiplexer_3_out), .in1(3'b011), .out(multiplexer_1_out), .sel(not_1_out));
  not not_1 (not_1_out, game_active);
  Decoder #(.select(3), .enable("false")) decoder_1 (
    .out0(decoder_1_out0[0]), .out1(decoder_1_out0[1]), .out2(decoder_1_out0[2]), .out3(decoder_1_out0[3]),
    .out4(decoder_1_out0[4]), .out5(decoder_1_out0[5]), .out6(decoder_1_out0[6]), .out7(decoder_1_out0[7]),
    .sel(player_x));
  Register #(.width(3), .trigger("falling")) X (.D(multiplexer_1_out), .Q(player_x), .clk(Clk));  // open: en, clr
  Adder #(.width(3)) adder_1 (.a(player_x), .b(3'b001), .out(player_x_1));  // open: cin, cout
  Subtractor #(.width(3)) subtractor_1 (.a(player_x), .b(3'b001), .out(subtractor_1_out));  // open: bin, bout
  Comparator #(.width(3), .mode("unsigned")) comparator_1 (
    .a(player_x), .b(3'b110), .eq(comparator_1_eq));  // open: gt, lt
  Comparator #(.width(3), .mode("unsigned")) comparator_2 (
    .a(player_x), .b(3'b000), .eq(comparator_2_eq));  // open: gt, lt
  Shifter shifter_1 (.in(decoder_1_out0), .\dist (3'b001), .out(shifter_1_out));
  assign player_screen_pixel = shifter_1_out | decoder_1_out0;  // OR_Gate or_1, 8 bits wide
  Shifter #(.shift("lr")) shifter_2 (.in(decoder_1_out0), .\dist (3'b001), .out(shifter_2_out));
  Multiplexer #(.width(3), .enable("false")) multiplexer_2 (
    .in0(player_x), .in1(player_x_1), .out(multiplexer_2_out), .sel(and_1_out));
  and and_1 (and_1_out, btnLeft, ~comparator_1_eq);  // AND_Gate
  and and_2 (and_2_out, btnRight, ~comparator_2_eq);  // AND_Gate
  Multiplexer #(.width(3), .enable("false")) multiplexer_3 (
    .in0(multiplexer_2_out), .in1(subtractor_1_out), .out(multiplexer_3_out), .sel(and_2_out));

  // Other names for the same wires on the sheet: Left = btnLeft; Right = btnRight
endmodule

module ai (
  input  [2:0] ball_x,
  input  game_active,
  input  Clk,
  output [7:0] ai_screen_pixel,
  output [2:0] ai_x,
  output [2:0] ai_x_1
);

  wire and_1_out, and_2_out, comparator_1_eq, comparator_2_eq, comparator_3_eq, comparator_3_lt,
       comparator_4_eq, comparator_4_gt, Left, not_1_out, Right;
  wire [2:0] multiplexer_1_out, multiplexer_2_out, multiplexer_3_out, subtractor_1_out;
  wire [7:0] decoder_1_out0, shifter_1_out, shifter_2_out;

  Multiplexer #(.width(3), .enable("false")) multiplexer_1 (
    .in0(multiplexer_3_out), .in1(3'b011), .out(multiplexer_1_out), .sel(not_1_out));
  not not_1 (not_1_out, game_active);
  Decoder #(.select(3), .enable("false")) decoder_1 (
    .out0(decoder_1_out0[0]), .out1(decoder_1_out0[1]), .out2(decoder_1_out0[2]), .out3(decoder_1_out0[3]),
    .out4(decoder_1_out0[4]), .out5(decoder_1_out0[5]), .out6(decoder_1_out0[6]), .out7(decoder_1_out0[7]),
    .sel(ai_x));
  Register #(.width(3), .trigger("falling")) X (.D(multiplexer_1_out), .Q(ai_x), .clk(Clk));  // open: en, clr
  Adder #(.width(3)) adder_1 (.a(ai_x), .b(3'b001), .out(ai_x_1));  // open: cin, cout
  Subtractor #(.width(3)) subtractor_1 (.a(ai_x), .b(3'b001), .out(subtractor_1_out));  // open: bin, bout
  Comparator #(.width(3), .mode("unsigned")) comparator_1 (.a(ai_x), .b(3'b110), .eq(comparator_1_eq));  // open: gt, lt
  Comparator #(.width(3), .mode("unsigned")) comparator_2 (.a(ai_x), .b(3'b000), .eq(comparator_2_eq));  // open: gt, lt
  Comparator #(.width(3), .mode("unsigned")) comparator_3 (
    .a(ball_x), .b(ai_x), .eq(comparator_3_eq), .lt(comparator_3_lt));  // open: gt
  Shifter shifter_1 (.in(decoder_1_out0), .\dist (3'b001), .out(shifter_1_out));
  assign ai_screen_pixel = shifter_1_out | decoder_1_out0;  // OR_Gate or_1, 8 bits wide
  Shifter #(.shift("lr")) shifter_2 (.in(decoder_1_out0), .\dist (3'b001), .out(shifter_2_out));
  Multiplexer #(.width(3), .enable("false")) multiplexer_2 (
    .in0(ai_x), .in1(ai_x_1), .out(multiplexer_2_out), .sel(and_1_out));
  and and_1 (and_1_out, Left, ~comparator_1_eq);  // AND_Gate
  and and_2 (and_2_out, Right, ~comparator_2_eq);  // AND_Gate
  or or_2 (Right, comparator_3_eq, comparator_3_lt);
  Multiplexer #(.width(3), .enable("false")) multiplexer_3 (
    .in0(multiplexer_2_out), .in1(subtractor_1_out), .out(multiplexer_3_out), .sel(and_2_out));
  or or_3 (Left, comparator_4_gt, comparator_4_eq);
  Comparator #(.width(3), .mode("unsigned")) comparator_4 (
    .a(ball_x), .b(ai_x_1), .gt(comparator_4_gt), .eq(comparator_4_eq));  // open: lt
endmodule

module ball (
  input  dX,
  input  dY,
  input  game_active,
  input  clk,
  output [2:0] ball_x,
  output [7:0] out_6,
  output [7:0] out_7,
  output [7:0] out_8,
  output [7:0] out_9,
  output [7:0] out_10,
  output [7:0] out_11,
  output [7:0] out_12,
  output [7:0] out_13,
  output [2:0] ball_y
);

  wire decoder_2_out0, decoder_2_out1, decoder_2_out2, decoder_2_out3, decoder_2_out4, decoder_2_out5,
       decoder_2_out6, decoder_2_out7, not_1_out, not_2_out, undriven, undriven_2;
  wire [2:0] adder_1_out, adder_2_out, multiplexer_1_out, multiplexer_2_out, multiplexer_3_out,
       multiplexer_4_out, subtractor_1_out, subtractor_2_out;
  wire [7:0] decoder_1_out0;

  Multiplexer #(.width(3), .enable("false")) multiplexer_1 (
    .in0(multiplexer_3_out), .in1(3'b100), .out(multiplexer_1_out), .sel(not_1_out));
  not not_1 (not_1_out, game_active);
  Multiplexer #(.width(3), .enable("false")) multiplexer_2 (
    .in0(multiplexer_4_out), .in1(3'b100), .out(multiplexer_2_out), .sel(not_2_out));
  not not_2 (not_2_out, game_active);
  Register #(.width(3)) X (.D(multiplexer_1_out), .en(undriven), .Q(ball_x), .clk(clk));  // open: clr
  Register #(.width(3)) Y (.D(multiplexer_2_out), .en(undriven_2), .Q(ball_y), .clk(clk));  // open: clr
  Adder #(.width(3)) adder_1 (.a(ball_x), .b(3'b001), .out(adder_1_out));  // open: cin, cout
  Multiplexer #(.width(3), .enable("false")) multiplexer_3 (
    .in0(adder_1_out), .in1(subtractor_1_out), .out(multiplexer_3_out), .sel(dX));
  Subtractor #(.width(3)) subtractor_1 (.a(ball_x), .b(3'b001), .out(subtractor_1_out));  // open: bin, bout
  Adder #(.width(3)) adder_2 (.a(ball_y), .b(3'b001), .out(adder_2_out));  // open: cin, cout
  Multiplexer #(.width(3), .enable("false")) multiplexer_4 (
    .in0(adder_2_out), .in1(subtractor_2_out), .out(multiplexer_4_out), .sel(dY));
  Subtractor #(.width(3)) subtractor_2 (.a(ball_y), .b(3'b001), .out(subtractor_2_out));  // open: bin, bout
  Decoder #(.select(3), .enable("false")) decoder_1 (
    .out0(decoder_1_out0[0]), .out1(decoder_1_out0[1]), .out2(decoder_1_out0[2]), .out3(decoder_1_out0[3]),
    .out4(decoder_1_out0[4]), .out5(decoder_1_out0[5]), .out6(decoder_1_out0[6]), .out7(decoder_1_out0[7]),
    .sel(ball_x));
  Decoder #(.select(3), .enable("false")) decoder_2 (
    .out0(decoder_2_out0), .out1(decoder_2_out1), .out2(decoder_2_out2), .out3(decoder_2_out3),
    .out4(decoder_2_out4), .out5(decoder_2_out5), .out6(decoder_2_out6), .out7(decoder_2_out7), .sel(ball_y));
  assign out_6 = decoder_2_out0 ? decoder_1_out0 : 8'bz;  // Controlled_Buffer controlled_buffer_1
  assign out_7 = decoder_2_out1 ? decoder_1_out0 : 8'bz;  // Controlled_Buffer controlled_buffer_2
  assign out_8 = decoder_2_out2 ? decoder_1_out0 : 8'bz;  // Controlled_Buffer controlled_buffer_3
  assign out_9 = decoder_2_out3 ? decoder_1_out0 : 8'bz;  // Controlled_Buffer controlled_buffer_4
  assign out_10 = decoder_2_out4 ? decoder_1_out0 : 8'bz;  // Controlled_Buffer controlled_buffer_5
  assign out_11 = decoder_2_out5 ? decoder_1_out0 : 8'bz;  // Controlled_Buffer controlled_buffer_6
  assign out_12 = decoder_2_out6 ? decoder_1_out0 : 8'bz;  // Controlled_Buffer controlled_buffer_7
  assign out_13 = decoder_2_out7 ? decoder_1_out0 : 8'bz;  // Controlled_Buffer controlled_buffer_8
  Pull_Resistor pull_resistor_1 (.node(out_13));
  Pull_Resistor pull_resistor_2 (.node(out_8));
  Pull_Resistor pull_resistor_3 (.node(out_10));
  Pull_Resistor pull_resistor_4 (.node(out_12));
  Pull_Resistor pull_resistor_5 (.node(out_6));
  Pull_Resistor pull_resistor_6 (.node(out_9));
  Pull_Resistor pull_resistor_7 (.node(out_11));
  Pull_Resistor pull_resistor_8 (.node(out_7));
endmodule

module collisionCheck (
  input  [2:0] player_x,
  input  [2:0] player_x_1,
  input  [2:0] ball_x,
  input  [2:0] ball_y,
  input  [2:0] coordinateToCheck,
  output EVENT_HIT
);

  wire comparator_1_eq, comparator_2_eq, comparator_3_eq, or_1_out;

  Comparator #(.width(3), .mode("unsigned")) comparator_1 (
    .a(ball_x), .b(player_x), .eq(comparator_1_eq));  // open: gt, lt
  Comparator #(.width(3), .mode("unsigned")) comparator_2 (
    .a(player_x_1), .b(ball_x), .eq(comparator_2_eq));  // open: gt, lt
  Comparator #(.width(3)) comparator_3 (.a(ball_y), .b(coordinateToCheck), .eq(comparator_3_eq));  // open: gt, lt
  or or_1 (or_1_out, comparator_1_eq, comparator_2_eq);
  and and_1 (EVENT_HIT, or_1_out, comparator_3_eq);
endmodule
