// Logisim project kbd_interrupt.circ as structural Verilog: 1 circuit, main circuit kbd_interrupt
module kbd_interrupt (
);

  wire and_3_out, and_4_out, and_5_out, and_6_out, and_7_out, and_8_out, and_9_out, and_10_out,
       arbiter_1_iack_2, arbiter_1_vec, cdm_8_mark5_1_data_inst, Clk, code, comparator_1_eq, comparator_2_eq,
       data, I_O_sel, IAck, IRQ, mem, not_1_out, RAM, rd_wr;
  wire [2:0] vec;
  wire [3:0] I_O_addr;
  wire [6:0] bit_extender_1_out, keyboard_1_data;
  wire [7:0] bit_extender_2_out, cdm_8_mark5_1_data_out, cdm_8_mark5_1_pc, cdm_8_mark5_1_ps,
       cdm_8_mark5_1_r0, cdm_8_mark5_1_r1, cdm_8_mark5_1_r2, cdm_8_mark5_1_r3, cdm_8_mark5_1_sp,
       controlled_buffer_2_out, d_ff_1_q, I_O_data;
  wire [7:4] cdm_8_mark5_1_addr;

  // Probe on cdm_8_mark5_1_r3
  // Probe on cdm_8_mark5_1_r2
  // Probe on cdm_8_mark5_1_r1
  // Probe on cdm_8_mark5_1_pc
  // Probe on cdm_8_mark5_1_r0
  Clock clock_1 (.out(Clk));
  // Probe on cdm_8_mark5_1_ps
  // Probe on cdm_8_mark5_1_sp
  Decoder decoder_1 (.out0(code), .out1(data), .sel(cdm_8_mark5_1_data_inst), .en(mem));
  CdM_8_mark5 cdm_8_mark5_1 (
    .clock(Clk), .addr({cdm_8_mark5_1_addr, I_O_addr}), .mem_read(rd_wr), .mem_cycle(mem),
    .data_inst(cdm_8_mark5_1_data_inst), .data_out(cdm_8_mark5_1_data_out),
    .data_in(controlled_buffer_2_out), .r0(cdm_8_mark5_1_r0), .r1(cdm_8_mark5_1_r1), .r2(cdm_8_mark5_1_r2),
    .r3(cdm_8_mark5_1_r3), .PC(cdm_8_mark5_1_pc), .SP(cdm_8_mark5_1_sp), .PS(cdm_8_mark5_1_ps), .IAck(IAck),
    .IRQ(IRQ), .vec(vec));
  assign I_O_data = not_1_out ? cdm_8_mark5_1_data_out : 8'bz;  // Controlled_Buffer controlled_buffer_1
  not not_1 (not_1_out, rd_wr);
  assign controlled_buffer_2_out = rd_wr ? I_O_data : 8'bz;  // Controlled_Buffer controlled_buffer_2
  and and_1 (I_O_sel, cdm_8_mark5_1_addr[4], cdm_8_mark5_1_addr[5], cdm_8_mark5_1_addr[6], cdm_8_mark5_1_addr[7], data);
  and and_2 (RAM, ~I_O_sel, data);  // AND_Gate
  ROM rom_1 (.addr({cdm_8_mark5_1_addr, I_O_addr}), .data(I_O_data), .sel(code));
  RAM ram_1 (.addr({cdm_8_mark5_1_addr, I_O_addr}), .data(I_O_data), .sel(RAM), .clk(Clk), .ld(rd_wr));  // open: clr
  Comparator #(.width(4), .mode("unsigned")) comparator_1 (
    .a(I_O_addr), .b(4'b0000), .eq(comparator_1_eq));  // open: gt, lt
  Comparator #(.width(4), .mode("unsigned")) comparator_2 (
    .a(I_O_addr), .b(4'b0001), .eq(comparator_2_eq));  // open: gt, lt
  LED led_1 (.in(and_3_out));
  and and_3 (and_3_out, comparator_1_eq, I_O_sel);
  LED led_2 (.in(and_4_out));
  and and_4 (and_4_out, comparator_2_eq, I_O_sel);
  and and_5 (and_5_out, ~rd_wr, and_3_out);  // AND_Gate
  D_Flip_Flop d_ff_1 (.clk(and_5_out), .D(I_O_data[0]), .Q(d_ff_1_q[0]));  // open: Qn, preset, en, reset
  and and_6 (and_6_out, rd_wr, and_3_out);
  Bit_Extender #(.out_width(7)) bit_extender_1 (.in(I_O_data), .out(bit_extender_1_out));
  TTY #(.rows(4), .cols(19), .trigger("falling")) tty_1 (.data(bit_extender_1_out), .clk(and_7_out));  // open: we, clr
  and and_7 (and_7_out, ~rd_wr, and_4_out);  // AND_Gate
  Keyboard #(.trigger("falling")) keyboard_1 (
    .clk(Clk), .re(and_8_out), .avail(d_ff_1_q[7]), .data(keyboard_1_data));  // open: clr
  and and_8 (and_8_out, rd_wr, and_4_out);
  assign I_O_data = and_6_out ? {d_ff_1_q[7], {6{1'b0}}, d_ff_1_q[0]} : 8'bz;  // Controlled_Buffer controlled_buffer_3
  and and_9 (and_9_out, d_ff_1_q[0], d_ff_1_q[7]);
  assign bit_extender_2_out = {{1{1'b0}}, keyboard_1_data};  // Bit_Extender bit_extender_2
  and and_10 (and_10_out, rd_wr, and_4_out);
  assign vec = arbiter_1_vec ? 3'b010 : 3'bz;  // Controlled_Buffer controlled_buffer_4
  arbiter arbiter_1 (
    .IReq_2(IRQ), .IAck(IAck), .IReq(arbiter_1_iack_2), .IAck_2(arbiter_1_iack_2), .vec(arbiter_1_vec),
    .req(and_9_out), .done(and_10_out), .clock(Clk));
  assign I_O_data = and_10_out ? bit_extender_2_out : 8'bz;  // Controlled_Buffer controlled_buffer_5
  // also tied to GND on the sheet: arbiter_1_iack_2

  // Notes on the sheet:
  //   instr_mem
  //   contents of rom_1 (hex, n*v repeats v):
  //   cd ef d0 29 d6 1e d0 f0 d1 1 a1 c1 d1 13 c1 d1 80 c1 d9 c5 d5 ee 14 ce d0 f1 b1 a1 cf d9 d1 f1 f2 8c
  //   a e0 28 a6 ee 20 d7 73 6d 69 6c 65 20 66 61 63 65 20 3a 33 d 189*0 17
  //   data_mem
  //   0xf1  -> data register 
  //   write => terminal
  //   0xf0  -> status register 
  //   read  => keyboard
  //   ld 0xF1 → клавиатура
  //   st 0xF1 → терминал
  //   ldi r0, 0xf0
  //   ldi r1, 1
  //   st r0, r1
  //   status = 10000000b  если символ готов 
  //   status = 00000001b  если прерывания разрешены 
  //   status = 10000001b  если и символ готов, и прерывания разрешены
  //   Чтобы разрешить прерывания от клавиатуры, программа должна записать 1 в бит 0 регистра 0xf0
endmodule
