// Logisim project table.circ as structural Verilog: 1 circuit, main circuit table
module \table  (
);

  wire and_3_out, and_4_out, and_5_out, and_6_out, and_7_out, and_8_out, and_9_out, and_10_out, and_11_out,
       arbiter_1_iack_2, arbiter_1_vec, buff_sel, button_1_out, cdm8_clk, cdm_8_mark5_1_data_inst, code,
       comparator_1_eq, comparator_2_eq, comparator_3_eq, comparator_4_eq, comparator_5_eq, counter_1_carry,
       counter_2_carry, d_ff_3_q, data, I_O_sel, IAck, IRQ, kbd_sel, mem, multiplexer_3_out, not_1_out,
       not_2_out, not_3_out, or_1_out, player_loser, RAM, rd_wr, s_r_ff_1_q, s_r_ff_1_qn, undriven;
  wire [0:0] d_ff_1_q;
  wire [2:0] vec;
  wire [3:0] counter_1_q, counter_2_q, I_O_addr;
  wire [6:0] bit_extender_1_out, keyboard_1_data;
  wire [7:0] bit_extender_2_out, bit_extender_4_out, buff_addr, buff_data, cdm_8_mark5_1_data_out,
       cdm_8_mark5_1_pc, cdm_8_mark5_1_ps, cdm_8_mark5_1_r0, cdm_8_mark5_1_r1, cdm_8_mark5_1_r2,
       cdm_8_mark5_1_r3, cdm_8_mark5_1_sp, controlled_buffer_2_out, I_O_data_read, kbd_addr, kbd_data,
       multiplexer_1_out, multiplexer_2_out, player_score;
  wire [7:4] cdm_8_mark5_1_addr;

  // Probe on cdm_8_mark5_1_r1
  // Probe on cdm_8_mark5_1_r0
  Clock clock_1 (.out(cdm8_clk));
  // Probe on cdm_8_mark5_1_r3
  // Probe on cdm_8_mark5_1_r2
  // Probe on cdm_8_mark5_1_sp
  // Probe on cdm_8_mark5_1_pc
  // Probe on cdm_8_mark5_1_ps
  Decoder decoder_1 (.out0(code), .out1(data), .sel(cdm_8_mark5_1_data_inst), .en(mem));
  CdM_8_mark5 cdm_8_mark5_1 (
    .clock(cdm8_clk), .addr({cdm_8_mark5_1_addr, I_O_addr}), .mem_read(rd_wr), .mem_cycle(mem),
    .data_inst(cdm_8_mark5_1_data_inst), .data_out(cdm_8_mark5_1_data_out),
    .data_in(controlled_buffer_2_out), .r0(cdm_8_mark5_1_r0), .r1(cdm_8_mark5_1_r1), .r2(cdm_8_mark5_1_r2),
    .r3(cdm_8_mark5_1_r3), .PC(cdm_8_mark5_1_pc), .SP(cdm_8_mark5_1_sp), .PS(cdm_8_mark5_1_ps), .IAck(IAck),
    .IRQ(IRQ), .vec(vec));
  assign I_O_data_read = not_1_out ? cdm_8_mark5_1_data_out : 8'bz;  // Controlled_Buffer controlled_buffer_1
  not not_1 (not_1_out, rd_wr);
  assign controlled_buffer_2_out = rd_wr ? I_O_data_read : 8'bz;  // Controlled_Buffer controlled_buffer_2
  Multiplexer #(.width(8), .enable("false")) multiplexer_1 (
    .in0({cdm_8_mark5_1_addr, I_O_addr}), .in1(buff_addr), .out(multiplexer_1_out), .sel(s_r_ff_1_q));
  Multiplexer #(.width(8), .enable("false")) multiplexer_2 (
    .in0(I_O_data_read), .in1(buff_data), .out(multiplexer_2_out), .sel(s_r_ff_1_q));
  not not_2 (not_2_out, rd_wr);
  and and_1 (I_O_sel, cdm_8_mark5_1_addr[4], cdm_8_mark5_1_addr[5], cdm_8_mark5_1_addr[6], cdm_8_mark5_1_addr[7], data);
  Pull_Resistor pull_resistor_1 (.node(data));
  Multiplexer #(.enable("false")) multiplexer_3 (.in0(RAM), .in1(buff_sel), .out(multiplexer_3_out), .sel(s_r_ff_1_q));
  and and_2 (RAM, ~I_O_sel, data);  // AND_Gate
  ROM rom_1 (.addr({cdm_8_mark5_1_addr, I_O_addr}), .data(I_O_data_read), .sel(code));
  RAM #(.bus("separate")) ram_1 (
    .addr(multiplexer_1_out), .din(multiplexer_2_out), .data(I_O_data_read), .str(not_2_out),
    .sel(multiplexer_3_out), .clk(cdm8_clk), .ld(rd_wr));  // open: clr
  Comparator #(.width(4), .mode("unsigned")) comparator_1 (
    .a(I_O_addr), .b(4'b0001), .eq(comparator_1_eq));  // open: gt, lt
  Comparator #(.width(4), .mode("unsigned")) comparator_2 (
    .a(I_O_addr), .b(4'b0010), .eq(comparator_2_eq));  // open: gt, lt
  and and_3 (and_3_out, comparator_2_eq, I_O_sel);
  Comparator #(.width(4), .mode("unsigned")) comparator_3 (
    .a(I_O_addr), .b(4'b0011), .eq(comparator_3_eq));  // open: gt, lt
  and and_4 (and_4_out, comparator_3_eq, I_O_sel);
  LED led_1 (.in(and_5_out));
  and and_5 (and_5_out, comparator_1_eq, I_O_sel);
  and and_6 (and_6_out, ~rd_wr, and_3_out);  // AND_Gate
  and and_7 (and_7_out, ~rd_wr, and_5_out);  // AND_Gate
  D_Flip_Flop #(.trigger("falling")) d_ff_1 (
    .clk(cdm8_clk), .D(I_O_data_read[0]), .Q(d_ff_1_q[0]), .en(and_6_out));  // open: Qn, preset, reset
  assign I_O_data_read = and_8_out ? player_score : 8'bz;  // Controlled_Buffer controlled_buffer_3
  and and_8 (and_8_out, rd_wr, and_4_out);
  Bit_Extender #(.out_width(7)) bit_extender_1 (.in(I_O_data_read), .out(bit_extender_1_out));
  TTY #(.rows(7), .cols(22), .trigger("falling")) tty_1 (
    .data(bit_extender_1_out), .clk(cdm8_clk), .we(and_7_out));  // open: clr
  TTY #(.rows(1), .cols(22)) tty_2 (.data(keyboard_1_data), .clk(cdm8_clk), .we(not_3_out), .clr(button_1_out));
  Keyboard keyboard_1 (.clk(cdm8_clk), .re(not_3_out), .clr(s_r_ff_1_qn), .avail(kbd_sel), .data(keyboard_1_data));
  not not_3 (not_3_out, s_r_ff_1_qn);
  assign I_O_data_read = and_9_out ? {player_loser, {6{1'b0}}, d_ff_1_q[0]} : 8'bz;  // Controlled_Buffer controlled_buffer_4
  and and_9 (and_9_out, rd_wr, and_3_out);
  and and_10 (and_10_out, d_ff_1_q[0], player_loser);
  assign bit_extender_2_out = {{1{1'b0}}, keyboard_1_data};  // Bit_Extender bit_extender_2
  Multiplexer #(.width(8), .enable("false")) multiplexer_4 (
    .in0(bit_extender_2_out), .in1({8{1'b0}}), .out(kbd_data), .sel(comparator_4_eq));
  Comparator #(.mode("unsigned")) comparator_4 (
    .a(bit_extender_2_out), .b(8'h8), .eq(comparator_4_eq));  // open: gt, lt
  Counter #(.width(4), .max('h8), .ongoal("stay"), .trigger("falling")) counter_1 (
    .load(comparator_4_eq), .Q(counter_1_q), .carry(counter_1_carry), .clk(kbd_sel), .clr(s_r_ff_1_qn));  // open: D, count
  assign vec = arbiter_1_vec ? 3'b100 : 3'bz;  // Controlled_Buffer controlled_buffer_5
  arbiter arbiter_1 (
    .IReq_2(IRQ), .IAck(IAck), .IReq(arbiter_1_iack_2), .IAck_2(arbiter_1_iack_2), .vec(arbiter_1_vec),
    .req(and_10_out), .done(and_8_out), .clock(cdm8_clk));
  Button button_1 (.out(button_1_out));
  Comparator #(.mode("unsigned")) comparator_5 (
    .a(bit_extender_2_out), .b(8'ha), .eq(comparator_5_eq));  // open: gt, lt
  assign kbd_addr = {{4{1'b0}}, counter_1_q};  // Bit_Extender bit_extender_3
  S_R_Flip_Flop s_r_ff_1 (
    .S(button_1_out), .clk(cdm8_clk), .R(comparator_5_eq), .Q(s_r_ff_1_q), .Qn(s_r_ff_1_qn), .reset(or_1_out));  // open: preset, en
  or or_1 (or_1_out, comparator_5_eq, player_loser, counter_1_carry);
  D_Flip_Flop d_ff_2 (.clk(undriven), .D(undriven), .Q(player_loser), .reset(and_11_out));  // open: Qn, preset, en
  and and_11 (and_11_out, IAck, arbiter_1_vec);
  D_Flip_Flop d_ff_3 (
    .clk(button_1_out), .D(button_1_out), .Q(d_ff_3_q), .reset(counter_2_carry));  // open: Qn, preset, en
  Counter #(.width(4), .max('h8), .ongoal("stay")) counter_2 (
    .count(button_1_out), .Q(counter_2_q), .carry(counter_2_carry), .clk(cdm8_clk), .clr(s_r_ff_1_qn));  // open: load, D
  assign bit_extender_4_out = {{4{1'b0}}, counter_2_q};  // Bit_Extender bit_extender_4
  Multiplexer #(.enable("false")) multiplexer_5 (.in0(kbd_sel), .in1(d_ff_3_q), .out(buff_sel), .sel(d_ff_3_q));
  Multiplexer #(.width(8), .enable("false")) multiplexer_6 (
    .in0(kbd_addr), .in1(bit_extender_4_out), .out(buff_addr), .sel(d_ff_3_q));
  Multiplexer #(.width(8), .enable("false")) multiplexer_7 (
    .in0(kbd_data), .in1({8{1'b0}}), .out(buff_data), .sel(d_ff_3_q));
  // also tied to GND on the sheet: arbiter_1_iack_2

  // Other names for the same wires on the sheet: I_O_data_write[7:0] = I_O_data_read

  // Notes on the sheet:
  //   instr_mem
  //   data_mem
  //   contents of rom_1 (hex, n*v repeats v):
  //   cd f0 d0 3d d1 10 d2 5 a e0 16 a1 d3 0 a7 8c d3 9 1d 8a ee 8 d0 f0 d1 1 a1 d0 f2 a1 c1 d1 26 c1 d1
  //   80 c1 d9 c5 d5 ee 27 d4 ce d0 f3 b1 d0 3d d2 42 72 e0 44 b2 bb 77 ec 3e 8c ee 42 d6 48 ee 44 ee 31
  //   d6 70 cf d9 d2 41 bb ad c0 c1 c2 c3 d 8d d0 0 d2 8 a e0 60 b3 a7 8c 8d 8a ee 56 c7 c6 c5 c4 78 e0 6e
  //   9 89 b5 a9 8a ee 64 a3 d7 d0 3d d3 5 f e0 9d b2 c2 ba c0 c3 d6 a1 c7 c4 d1 f1 d2 20 a6 c6 8e c0 c3
  //   d3 8 f e0 94 b8 a4 8e 8b ee 8b c7 c4 d2 a a6 8c 8b ee 74 d2 a a6 d7 d1 f1 d0 0 d3 64 7b eb af 3b e
  //   8c ee a5 d3 30 13 a7 d0 0 d3 a 7b eb bf 3b e 8c ee b5 d3 30 13 a7 d3 30 1b a7 d7 44*0 2a 0 0 0 2b
  //   0xf2  -> status register 
  //   0xf3  -> data register 
  //   status = 10000000b  если символ готов 
  //   status = 00000001b  если прерывания разрешены 
  //   status = 10000001b  если и символ готов, и прерывания разрешены
  //   с f3 читаем счёт игрока
  //   терминал просто для отображения имени
  //   терминал, на который выводится таблица
  //   ВВЕСТИ ИМЯ
  //   vec == 4
  //   сюда подаём какой-нибудь сигнал, что игра окончина и надо запустить сортировку таблицы
  //   cleaning
endmodule
