// Logisim project Ьase17_11.0.circ as structural Verilog: 15 circuits, main circuit GAME
module GAME (
);

  wire L, R, Reset;
  wire [31:0] main_1_out_4, main_1_out_5, main_1_out_6, main_1_out_7, main_1_out_8, main_1_out_9,
       main_1_out_10, main_1_out_11, main_1_out_12, main_1_out_13, main_1_out_14, main_1_out_15,
       main_1_out_16, main_1_out_17, main_1_out_18, main_1_out_19, main_1_out_20, main_1_out_21,
       main_1_out_22, main_1_out_23, main_1_out_24, main_1_out_25, main_1_out_26, main_1_out_27,
       main_1_out_28, main_1_out_29, main_1_out_30, main_1_out_31, main_1_out_32, main_1_out_33,
       main_1_out_34, main_1_out_35;

  main main_1 (
    .btn_left(L), .btn_right(R), .btn_reset(Reset), .out_4(main_1_out_4), .out_5(main_1_out_5),
    .out_6(main_1_out_6), .out_7(main_1_out_7), .out_8(main_1_out_8), .out_9(main_1_out_9),
    .out_10(main_1_out_10), .out_11(main_1_out_11), .out_12(main_1_out_12), .out_13(main_1_out_13),
    .out_14(main_1_out_14), .out_15(main_1_out_15), .out_16(main_1_out_16), .out_17(main_1_out_17),
    .out_18(main_1_out_18), .out_19(main_1_out_19), .out_20(main_1_out_20), .out_21(main_1_out_21),
    .out_22(main_1_out_22), .out_23(main_1_out_23), .out_24(main_1_out_24), .out_25(main_1_out_25),
    .out_26(main_1_out_26), .out_27(main_1_out_27), .out_28(main_1_out_28), .out_29(main_1_out_29),
    .out_30(main_1_out_30), .out_31(main_1_out_31), .out_32(main_1_out_32), .out_33(main_1_out_33),
    .out_34(main_1_out_34), .out_35(main_1_out_35));
  DotMatrix #(.inputtype("row"), .matrixcols(32), .matrixrows(1)) dotmatrix_1 (.row0(main_1_out_4));
  DotMatrix #(.inputtype("row"), .matrixcols(32), .matrixrows(30)) dotmatrix_2 (
    .row0(main_1_out_5), .row1(main_1_out_6), .row2(main_1_out_7), .row3(main_1_out_8), .row4(main_1_out_9),
    .row5(main_1_out_10), .row6(main_1_out_11), .row7(main_1_out_12), .row8(main_1_out_13),
    .row9(main_1_out_14), .row10(main_1_out_15), .row11(main_1_out_16), .row12(main_1_out_17),
    .row13(main_1_out_18), .row14(main_1_out_19), .row15(main_1_out_20), .row16(main_1_out_21),
    .row17(main_1_out_22), .row18(main_1_out_23), .row19(main_1_out_24), .row20(main_1_out_25),
    .row21(main_1_out_26), .row22(main_1_out_27), .row23(main_1_out_28), .row24(main_1_out_29),
    .row25(main_1_out_30), .row26(main_1_out_31), .row27(main_1_out_32), .row28(main_1_out_33),
    .row29(main_1_out_34));
  DotMatrix #(.inputtype("row"), .matrixcols(32), .matrixrows(1)) dotmatrix_3 (.row0(main_1_out_35));
  Button button_1 (.out(L));
  Button button_2 (.out(R));
  Button button_3 (.out(Reset));
  LED led_1 ();  // open: in
  LED led_2 ();  // open: in
  Hex_Digit_Display hex_digit_display_1 ();  // open: value, dp
  Hex_Digit_Display hex_digit_display_2 ();  // open: value, dp
  Hex_Digit_Display hex_digit_display_3 ();  // open: value, dp
  Hex_Digit_Display hex_digit_display_4 ();  // open: value, dp
  Hex_Digit_Display hex_digit_display_5 ();  // open: value, dp
  TTY #(.rows(7), .cols(22), .trigger("falling")) tty_1 ();  // open: data, clk, we, clr
  TTY #(.rows(1), .cols(22)) tty_2 ();  // open: data, clk, we, clr
  Keyboard keyboard_1 ();  // open: clk, re, clr, avail, data

  // Notes on the sheet:
  //   START / RESET
  //   PLAYER
  //   PLAYER_SCORE
  //   AI
endmodule

module main (
  input  btn_left,
  input  btn_right,
  input  btn_reset,
  output [31:0] out_4,
  output [31:0] out_5,
  output [31:0] out_6,
  output [31:0] out_7,
  output [31:0] out_8,
  output [31:0] out_9,
  output [31:0] out_10,
  output [31:0] out_11,
  output [31:0] out_12,
  output [31:0] out_13,
  output [31:0] out_14,
  output [31:0] out_15,
  output [31:0] out_16,
  output [31:0] out_17,
  output [31:0] out_18,
  output [31:0] out_19,
  output [31:0] out_20,
  output [31:0] out_21,
  output [31:0] out_22,
  output [31:0] out_23,
  output [31:0] out_24,
  output [31:0] out_25,
  output [31:0] out_26,
  output [31:0] out_27,
  output [31:0] out_28,
  output [31:0] out_29,
  output [31:0] out_30,
  output [31:0] out_31,
  output [31:0] out_32,
  output [31:0] out_33,
  output [31:0] out_34,
  output [31:0] out_35
);

  wire and_3_out, and_4_out, and_5_out, and_6_out, and_7_out, and_8_out, and_9_out, and_10_out, and_12_out,
       and_13_out, arbiter_1_iack_2, arbiter_1_vec, buff_sel, button_1_out, cdm8_clk,
       cdm_8_mark5_1_data_inst, code, comparator_1_eq, comparator_2_eq, comparator_3_eq, comparator_4_eq,
       comparator_5_eq, counter_1_carry, counter_2_carry, counter_3_carry, d_ff_2_q, data, dX, dY,
       dy_1_hit_any, EVENT_HIT_AI_hit_x, EVENT_HIT_AI_hit_x_1, EVENT_HIT_AI_hit_x_1_2, EVENT_HIT_AI_hit_x_2,
       EVENT_HIT_AI_hit_x_2_2, EVENT_HIT_PLAYER_hit_x, EVENT_HIT_PLAYER_hit_x_1, EVENT_HIT_PLAYER_hit_x_1_2,
       EVENT_HIT_PLAYER_hit_x_2, EVENT_HIT_PLAYER_hit_x_2_2, freeze, game_active, game_clk, hit_ai,
       hit_player, I_O_sel, IAck, init_table, IRQ, is_valid, kbd_sel, keyboard_1_avail, mem,
       multiplexer_3_out, name, not_1_out, not_2_out, not_3_out, not_4_out, or_5_out, player_loser, RAM,
       rd_wr, s_r_ff_1_qn, xnor_1_out;
  wire [0:0] d_ff_1_q;
  wire [1:0] priority_encoder_1_out;
  wire [2:0] vec;
  wire [3:0] bit_extender_6_out, bit_extender_7_out, bit_extender_8_out, counter_1_q, counter_2_q,
       game_active_1_ai_fails, game_active_1_player_fails, I_O_addr;
  wire [4:0] ai_1_ai_x, ai_1_ai_x_1, ai_1_ai_x_1_2, ball_x, ball_y, player_1_player_x_1,
       player_1_player_x_1_2, player_x, slope_x, slope_y;
  wire [5:0] counter_3_q;
  wire [6:0] bit_extender_1_out, keyboard_1_data;
  wire [7:0] bit_extender_2_out, bit_extender_4_out, bit_extender_5_out, buff_addr, buff_data,
       cdm_8_mark5_1_data_out, cdm_8_mark5_1_pc, cdm_8_mark5_1_ps, cdm_8_mark5_1_r0, cdm_8_mark5_1_r1,
       cdm_8_mark5_1_r2, cdm_8_mark5_1_r3, cdm_8_mark5_1_sp, controlled_buffer_2_out, divider_1_out,
       divider_1_rem, divider_2_out, divider_2_rem, I_O_data_read, init_addr, init_data, kbd_addr, kbd_data,
       multiplexer_1_out, multiplexer_2_out, player_score, speed;
  wire [7:4] cdm_8_mark5_1_addr;
  wire [31:0] ai_1_ai_screen_pixel, ball_1_out_10, ball_1_out_41, player_1_player_screen_pixel;

  clock_frequency_divider clock_frequency_divider_1 (.speed(speed), .game_clk(game_clk), .cdm8_clk(cdm8_clk));
  ai ai_1 (
    .game_clk(game_clk), .game_active(game_active), .ball_x(ball_x), .ball_y(ball_y), .ball_dx(dX),
    .ball_dy(dY), .player_x(player_x), .ai_screen_pixel(ai_1_ai_screen_pixel), .ai_x(ai_1_ai_x),
    .ai_x_1(ai_1_ai_x_1), .ai_x_1_2(ai_1_ai_x_1_2));
  ball ball_1 (
    .dX(dX), .dY(dY), .game_active(game_active), .game_clk(game_clk), .ball_x(ball_x), .out_18(out_12),
    .out_19(out_13), .out_20(out_14), .out_21(out_15), .out_22(out_16), .out_23(out_17), .out_24(out_18),
    .out_25(out_19), .ball_y(ball_y), .slope_x(slope_x), .slope_y(slope_y), .out_26(out_20), .out_27(out_21),
    .out_28(out_22), .out_29(out_23), .out_30(out_24), .out_31(out_25), .out_32(out_26), .out_33(out_27),
    .out_34(out_28), .out_35(out_29), .out_36(out_30), .out_37(out_31), .out_38(out_32), .out_39(out_33),
    .out_40(out_34), .out_41(ball_1_out_41), .out_10(ball_1_out_10), .out_11(out_5), .out_12(out_6),
    .out_13(out_7), .out_14(out_8), .out_15(out_9), .out_16(out_10), .out_17(out_11), .freeze(freeze),
    .player_x(player_x));
  player player_1 (
    .btn_left(btn_left), .btn_right(btn_right), .game_active(game_active), .game_clk(game_clk),
    .player_screen_pixel(player_1_player_screen_pixel), .player_x(player_x),
    .player_x_1(player_1_player_x_1), .player_x_1_2(player_1_player_x_1_2));
  collision_check EVENT_HIT_AI (
    .player_x(ai_1_ai_x), .player_x_1(ai_1_ai_x_1), .player_x_1_2(ai_1_ai_x_1_2), .ball_x(ball_x),
    .ball_y(ball_y), .coordinate_to_check(5'b00001), .hit_x(EVENT_HIT_AI_hit_x),
    .hit_x_1(EVENT_HIT_AI_hit_x_1), .hit_x_1_2(EVENT_HIT_AI_hit_x_1_2), .hit_x_2(EVENT_HIT_AI_hit_x_2),
    .hit_x_2_2(EVENT_HIT_AI_hit_x_2_2));
  assign out_4 = ai_1_ai_screen_pixel | ball_1_out_10;  // OR_Gate or_1, 32 bits wide
  assign out_35 = ball_1_out_41 | player_1_player_screen_pixel;  // OR_Gate or_2, 32 bits wide
  collision_check EVENT_HIT_PLAYER (
    .player_x(player_x), .player_x_1(player_1_player_x_1), .player_x_1_2(player_1_player_x_1_2),
    .ball_x(ball_x), .ball_y(ball_y), .coordinate_to_check(5'b11110), .hit_x(EVENT_HIT_PLAYER_hit_x),
    .hit_x_1(EVENT_HIT_PLAYER_hit_x_1), .hit_x_1_2(EVENT_HIT_PLAYER_hit_x_1_2),
    .hit_x_2(EVENT_HIT_PLAYER_hit_x_2), .hit_x_2_2(EVENT_HIT_PLAYER_hit_x_2_2));
  // Probe on cdm_8_mark5_1_r3
  // Probe on cdm_8_mark5_1_r2
  // Probe on cdm_8_mark5_1_r1
  // Probe on cdm_8_mark5_1_pc
  // Probe on cdm_8_mark5_1_r0
  or or_3 (hit_ai, EVENT_HIT_AI_hit_x, EVENT_HIT_AI_hit_x_1, EVENT_HIT_AI_hit_x_1_2, EVENT_HIT_AI_hit_x_2, EVENT_HIT_AI_hit_x_2_2);
  // Probe on cdm_8_mark5_1_ps
  Decoder decoder_1 (.out0(code), .out1(data), .sel(cdm_8_mark5_1_data_inst), .en(mem));
  // Probe on cdm_8_mark5_1_sp
  CdM_8_mark5 cdm_8_mark5_1 (
    .clock(cdm8_clk), .addr({cdm_8_mark5_1_addr, I_O_addr}), .mem_read(rd_wr), .mem_cycle(mem),
    .data_inst(cdm_8_mark5_1_data_inst), .data_out(cdm_8_mark5_1_data_out),
    .data_in(controlled_buffer_2_out), .r0(cdm_8_mark5_1_r0), .r1(cdm_8_mark5_1_r1), .r2(cdm_8_mark5_1_r2),
    .r3(cdm_8_mark5_1_r3), .PC(cdm_8_mark5_1_pc), .SP(cdm_8_mark5_1_sp), .PS(cdm_8_mark5_1_ps), .IAck(IAck),
    .IRQ(IRQ), .vec(vec));
  assign I_O_data_read = not_1_out ? cdm_8_mark5_1_data_out : 8'bz;  // Controlled_Buffer controlled_buffer_1
  not not_1 (not_1_out, rd_wr);
  assign controlled_buffer_2_out = rd_wr ? I_O_data_read : 8'bz;  // Controlled_Buffer controlled_buffer_2
  Pull_Resistor pull_resistor_1 (.node(data));
  Pull_Resistor pull_resistor_2 (.node(code));
  or or_4 (hit_player, EVENT_HIT_PLAYER_hit_x, EVENT_HIT_PLAYER_hit_x_1, EVENT_HIT_PLAYER_hit_x_1_2, EVENT_HIT_PLAYER_hit_x_2, EVENT_HIT_PLAYER_hit_x_2_2);
  freeze freeze_1 (
    .game_clk(game_clk), .hit_x(EVENT_HIT_PLAYER_hit_x), .hit_x_1(EVENT_HIT_PLAYER_hit_x_1),
    .hit_x_1_2(EVENT_HIT_PLAYER_hit_x_1_2), .btn_left(btn_left), .btn_right(btn_right), .freeze(freeze));
  Priority_Encoder #(.select(2)) priority_encoder_1 (
    .in0(1'b1), .in1(init_table), .in2(name), .out(priority_encoder_1_out));  // open: in3, gs, en_out, en_in
  dY dy_1 (.hit_ai(hit_ai), .hit_player(hit_player), .game_active(game_active), .hit_any(dy_1_hit_any), .dY(dY));
  Multiplexer #(.select(2), .width(8), .enable("false")) multiplexer_1 (
    .in0({cdm_8_mark5_1_addr, I_O_addr}), .in1(init_addr), .in2(buff_addr), .out(multiplexer_1_out),
    .sel(priority_encoder_1_out));  // open: in3
  dX dx_1 (
    .game_clk(game_clk), .hit_ai_x(EVENT_HIT_AI_hit_x), .hit_ai_x_1(EVENT_HIT_AI_hit_x_1),
    .hit_ai_x_1_2(EVENT_HIT_AI_hit_x_1_2), .hit_ai_x_2(EVENT_HIT_AI_hit_x_2),
    .hit_ai_x_2_2(EVENT_HIT_AI_hit_x_2_2), .hit_player_x(EVENT_HIT_PLAYER_hit_x),
    .hit_player_x_1(EVENT_HIT_PLAYER_hit_x_1), .hit_player_x_1_2(EVENT_HIT_PLAYER_hit_x_1_2),
    .hit_player_x_2(EVENT_HIT_PLAYER_hit_x_2), .hit_player_x_2_2(EVENT_HIT_PLAYER_hit_x_2_2),
    .btn_left(btn_left), .btn_right(btn_right), .freeze(freeze), .ball_x(ball_x), .dX(dX));
  Bresenham bresenham_1 (
    .hit_ai_x_1(EVENT_HIT_AI_hit_x_1), .hit_ai_x_1_2(EVENT_HIT_AI_hit_x_1_2),
    .hit_ai_x_2(EVENT_HIT_AI_hit_x_2), .hit_ai_x_2_2(EVENT_HIT_AI_hit_x_2_2),
    .hit_player_x_1(EVENT_HIT_PLAYER_hit_x_1), .hit_player_x_1_2(EVENT_HIT_PLAYER_hit_x_1_2),
    .hit_player_x_2(EVENT_HIT_PLAYER_hit_x_2), .hit_player_x_2_2(EVENT_HIT_PLAYER_hit_x_2_2),
    .hit_any(dy_1_hit_any), .game_clk(game_clk), .game_active(game_active), .slope_x(slope_x),
    .slope_y(slope_y));
  Multiplexer #(.select(2), .width(8), .enable("false")) multiplexer_2 (
    .in0(I_O_data_read), .in1(init_data), .in2(buff_data), .out(multiplexer_2_out),
    .sel(priority_encoder_1_out));  // open: in3
  not not_2 (not_2_out, rd_wr);
  Multiplexer #(.select(2), .enable("false")) multiplexer_3 (
    .in0(RAM), .in1(init_table), .in2(buff_sel), .out(multiplexer_3_out), .sel(priority_encoder_1_out));  // open: in3
  and and_1 (I_O_sel, cdm_8_mark5_1_addr[4], cdm_8_mark5_1_addr[5], cdm_8_mark5_1_addr[6], cdm_8_mark5_1_addr[7], data);
  and and_2 (RAM, ~I_O_sel, data);  // AND_Gate
  ROM rom_1 (.addr({cdm_8_mark5_1_addr, I_O_addr}), .data(I_O_data_read), .sel(code));
  RAM #(.bus("separate")) ram_1 (
    .addr(multiplexer_1_out), .din(multiplexer_2_out), .data(I_O_data_read), .str(not_2_out),
    .sel(multiplexer_3_out), .clk(cdm8_clk), .ld(rd_wr));  // open: clr
  Comparator #(.width(4), .mode("unsigned")) comparator_1 (
    .a(I_O_addr), .b(4'b0001), .eq(comparator_1_eq));  // open: gt, lt
  Comparator #(.width(4), .mode("unsigned")) comparator_2 (
    .a(I_O_addr), .b(4'b0010), .eq(comparator_2_eq));  // open: gt, lt
  Comparator #(.width(4), .mode("unsigned")) comparator_3 (
    .a(I_O_addr), .b(4'b0011), .eq(comparator_3_eq));  // open: gt, lt
  LED led_1 (.in(and_3_out));
  and and_3 (and_3_out, comparator_1_eq, I_O_sel);
  and and_4 (and_4_out, comparator_2_eq, I_O_sel);
  and and_5 (and_5_out, comparator_3_eq, I_O_sel);
  and and_6 (and_6_out, ~rd_wr, and_3_out);  // AND_Gate
  and and_7 (and_7_out, ~rd_wr, and_4_out);  // AND_Gate
  assign I_O_data_read = and_8_out ? player_score : 8'bz;  // Controlled_Buffer controlled_buffer_3
  and and_8 (and_8_out, rd_wr, and_5_out);
  Bit_Extender #(.out_width(7)) bit_extender_1 (.in(I_O_data_read), .out(bit_extender_1_out));
  TTY #(.rows(7), .cols(22), .trigger("falling")) tty_1 (
    .data(bit_extender_1_out), .clk(cdm8_clk), .we(and_6_out));  // open: clr
  TTY #(.rows(1), .cols(22)) tty_2 (.data(keyboard_1_data), .clk(cdm8_clk), .we(and_9_out), .clr(button_1_out));
  and and_9 (and_9_out, not_3_out, is_valid);
  Keyboard keyboard_1 (
    .clk(cdm8_clk), .re(not_3_out), .clr(s_r_ff_1_qn), .avail(keyboard_1_avail), .data(keyboard_1_data));
  not not_3 (not_3_out, s_r_ff_1_qn);
  D_Flip_Flop #(.trigger("falling")) d_ff_1 (
    .clk(cdm8_clk), .D(I_O_data_read[0]), .Q(d_ff_1_q[0]), .en(and_7_out));  // open: Qn, preset, reset
  player_score_speed player_score_speed_1 (
    .hit_player(hit_player), .f1_wrtie(and_6_out), .game_clk(game_clk), .speed(speed),
    .player_score(player_score));
  assign I_O_data_read = and_10_out ? {player_loser, {6{1'b0}}, d_ff_1_q[0]} : 8'bz;  // Controlled_Buffer controlled_buffer_4
  and and_10 (and_10_out, rd_wr, and_4_out);
  is_valid is_valid_1 (.kbd_symbol(keyboard_1_data), .is_valid(is_valid));
  and and_11 (kbd_sel, keyboard_1_avail, is_valid);
  assign bit_extender_2_out = {{1{1'b0}}, keyboard_1_data};  // Bit_Extender bit_extender_2
  and and_12 (and_12_out, d_ff_1_q[0], player_loser);
  Multiplexer #(.width(8), .enable("false")) multiplexer_4 (
    .in0(bit_extender_2_out), .in1({8{1'b0}}), .out(kbd_data), .sel(comparator_4_eq));
  Comparator #(.mode("unsigned")) comparator_4 (
    .a(bit_extender_2_out), .b(8'h8), .eq(comparator_4_eq));  // open: gt, lt
  Counter #(.width(4), .max('h8), .ongoal("stay"), .trigger("falling")) counter_1 (
    .load(comparator_4_eq), .Q(counter_1_q), .carry(counter_1_carry), .clk(kbd_sel), .clr(s_r_ff_1_qn));  // open: D, count
  xnor xnor_1 (xnor_1_out, btn_reset, not_4_out);
  not not_4 (not_4_out, btn_reset);
  Button button_1 (.out(button_1_out));
  Comparator #(.mode("unsigned")) comparator_5 (
    .a(bit_extender_2_out), .b(8'ha), .eq(comparator_5_eq));  // open: gt, lt
  assign kbd_addr = {{4{1'b0}}, counter_1_q};  // Bit_Extender bit_extender_3
  assign vec = arbiter_1_vec ? 3'b100 : 3'bz;  // Controlled_Buffer controlled_buffer_5
  S_R_Flip_Flop s_r_ff_1 (
    .S(button_1_out), .clk(cdm8_clk), .R(comparator_5_eq), .Q(name), .Qn(s_r_ff_1_qn), .reset(or_5_out));  // open: preset, en
  or or_5 (or_5_out, comparator_5_eq, player_loser, counter_1_carry);
  arbiter arbiter_1 (
    .IReq_2(IRQ), .IAck(IAck), .IReq(arbiter_1_iack_2), .IAck_2(arbiter_1_iack_2), .vec(arbiter_1_vec),
    .req(and_12_out), .done(and_8_out), .clock(cdm8_clk));
  S_R_Flip_Flop #(.trigger("high")) s_r_ff_2 (
    .S(xnor_1_out), .clk(cdm8_clk), .R(counter_3_carry), .Q(init_table), .reset(counter_3_carry));  // open: Qn, preset, en
  D_Flip_Flop d_ff_2 (
    .clk(button_1_out), .D(button_1_out), .Q(d_ff_2_q), .reset(counter_2_carry));  // open: Qn, preset, en
  Counter #(.width(4), .max('h8), .ongoal("stay")) counter_2 (
    .count(button_1_out), .Q(counter_2_q), .carry(counter_2_carry), .clk(cdm8_clk), .clr(s_r_ff_1_qn));  // open: load, D
  Counter #(.width(6), .max('h2c), .ongoal("stay")) counter_3 (
    .count(init_table), .Q(counter_3_q), .carry(counter_3_carry), .clk(cdm8_clk), .clr(xnor_1_out));  // open: load, D
  assign bit_extender_4_out = {{4{1'b0}}, counter_2_q};  // Bit_Extender bit_extender_4
  assign bit_extender_5_out = {{2{1'b0}}, counter_3_q};  // Bit_Extender bit_extender_5
  Adder adder_1 (.a(bit_extender_5_out), .b(8'h10), .out(init_addr));  // open: cin, cout
  Multiplexer #(.enable("false")) multiplexer_5 (.in0(kbd_sel), .in1(d_ff_2_q), .out(buff_sel), .sel(d_ff_2_q));
  Multiplexer #(.width(8), .enable("false")) multiplexer_6 (
    .in0(kbd_addr), .in1(bit_extender_4_out), .out(buff_addr), .sel(d_ff_2_q));
  Multiplexer #(.width(8), .enable("false")) multiplexer_7 (
    .in0(kbd_data), .in1({8{1'b0}}), .out(buff_data), .sel(d_ff_2_q));
  ROM rom_2 (.addr(bit_extender_5_out), .data(init_data), .sel(1'b1));
  and and_13 (and_13_out, IAck, arbiter_1_vec);
  Hex_Digit_Display hex_digit_display_1 (.value(game_active_1_player_fails));  // open: dp
  game_active game_active_1 (
    .ball_y(ball_y), .btn_left(btn_left), .btn_right(btn_right), .btn_reset(btn_reset), .game_clk(game_clk),
    .interrupt(and_13_out), .player_fails(game_active_1_player_fails), .ai_fails(game_active_1_ai_fails),
    .player_loser(player_loser), .game_active(game_active));
  LED led_2 ();  // open: in
  LED led_3 ();  // open: in
  Hex_Digit_Display hex_digit_display_2 (.value(game_active_1_ai_fails));  // open: dp
  Hex_Digit_Display hex_digit_display_3 (.value(bit_extender_6_out));  // open: dp
  Divider divider_1 (.a(player_score), .b(8'h64), .out(divider_1_out), .rem(divider_1_rem));  // open: upper
  Bit_Extender #(.out_width(4)) bit_extender_6 (.in(divider_1_out), .out(bit_extender_6_out));
  Divider divider_2 (.a(divider_1_rem), .b(8'ha), .out(divider_2_out), .rem(divider_2_rem));  // open: upper
  Hex_Digit_Display hex_digit_display_4 (.value(bit_extender_8_out));  // open: dp
  Hex_Digit_Display hex_digit_display_5 (.value(bit_extender_7_out));  // open: dp
  Bit_Extender #(.out_width(4)) bit_extender_7 (.in(divider_2_out), .out(bit_extender_7_out));
  Bit_Extender #(.out_width(4)) bit_extender_8 (.in(divider_2_rem), .out(bit_extender_8_out));
  // also tied to GND on the sheet: arbiter_1_iack_2

  // Other names for the same wires on the sheet: I_O_data_write[7:0] = I_O_data_read; L = btn_left; R = btn_right;
  //   Reset = btn_reset

  // Notes on the sheet:
  //   hit_any
  //   ldi r0, 0xf0
  //   ldi r1, 1
  //   st r0, r1
  //   status = 10000000b  если символ готов 
  //   status = 00000001b  если прерывания разрешены 
  //   status = 10000001b  если и символ готов, и прерывания разрешены
  //   Чтобы разрешить прерывания от клавиатуры, программа должна записать 1 в бит 0 регистра 0xf0
  //   instr_mem
  //   contents of rom_1 (hex, n*v repeats v):
  //   cd f0 d0 3d d1 10 d2 5 a e0 16 a1 d3 0 a7 8c d3 9 1d 8a ee 8 d0 f0 d1 1 a1 d0 f2 a1 c1 d1 26 c1 d1
  //   80 c1 d9 c5 d5 ee 27 d4 ce d0 f3 b1 d0 3d d2 42 72 e0 44 b2 bb 77 ec 3e 8c ee 42 d6 48 ee 44 ee 31
  //   d6 70 cf d9 d2 41 bb ad c0 c1 c2 c3 d 8d d0 0 d2 8 a e0 60 b3 a7 8c 8d 8a ee 56 c7 c6 c5 c4 78 e0 6e
  //   9 89 b5 a9 8a ee 64 a3 d7 d0 3d d3 5 f e0 9d b2 c2 ba c0 c3 d6 a1 c7 c4 d1 f1 d2 20 a6 c6 8e c0 c3
  //   d3 8 f e0 94 b8 a4 8e 8b ee 8b c7 c4 d2 a a6 8c 8b ee 74 d2 a a6 d7 d1 f1 d0 0 d3 64 7b eb af 3b e
  //   8c ee a5 d3 30 13 a7 d0 0 d3 a 7b eb bf 3b e 8c ee b5 d3 30 13 a7 d3 30 1b a7 d7 44*0 2a 0 0 0 2b
  //   data_mem
  //   0xf2  -> status register 
  //   0xf3  -> data register 
  //   ВВЕСТИ ИМЯ
  //   cleaning
  //   contents of rom_2 (hex, n*v repeats v):
  //   0 49 72 74 65 67 6f 76 0 0 4e 61 7a 61 72 6f 76 0 0 42 6f 6e 64 61 72 65 76 0 49 76 61 6e 6f 76 0 0
  //   0 50 65 74 72 6f 76
  //   vec == 4
  //   PLAYER
  //   AI
  //   PLAYER_SCORE
endmodule

module clock_frequency_divider (
  input  [7:0] speed,
  output game_clk,
  output cdm8_clk
);

  wire counter_1_carry, d_ff_1_q, undriven;

  Clock clock_1 (.out(cdm8_clk));
  Counter #(.ongoal("load")) counter_1 (
    .load(1'b1), .D(speed), .count(1'b1), .carry(counter_1_carry), .clk(cdm8_clk));  // open: Q, clr
  D_Flip_Flop d_ff_1 (.clk(cdm8_clk), .D(1'b1), .Q(d_ff_1_q), .en(undriven));  // open: Qn, preset, reset
  T_Flip_Flop t_ff_1 (.clk(counter_1_carry), .T(1'b1), .Q(game_clk), .en(1'b1));  // open: Qn, preset, reset
  LED led_1 (.in(game_clk));
endmodule

module player (
  input  btn_left,
  input  btn_right,
  input  game_clk,
  input  game_active,
  output [31:0] player_screen_pixel,
  output [4:0] player_x,
  output [4:0] player_x_1,
  output [4:0] player_x_1_2
);

  wire and_1_out, and_2_out, comparator_1_eq, comparator_2_eq, not_1_out;
  wire [4:0] multiplexer_1_out, multiplexer_2_out, multiplexer_3_out;
  wire [31:0] decoder_1_out0, shifter_1_out, shifter_2_out;

  Multiplexer #(.width(5), .enable("false")) multiplexer_1 (
    .in0(multiplexer_3_out), .in1(5'b01111), .out(multiplexer_1_out), .sel(not_1_out));
  not not_1 (not_1_out, game_active);
  Register #(.width(5), .trigger("falling")) X (.D(multiplexer_1_out), .Q(player_x), .clk(game_clk));  // open: en, clr
  Decoder #(.select(5), .enable("false")) decoder_1 (
    .out0(decoder_1_out0[0]), .out1(decoder_1_out0[1]), .out2(decoder_1_out0[2]), .out3(decoder_1_out0[3]),
    .out4(decoder_1_out0[4]), .out5(decoder_1_out0[5]), .out6(decoder_1_out0[6]), .out7(decoder_1_out0[7]),
    .out8(decoder_1_out0[8]), .out9(decoder_1_out0[9]), .out10(decoder_1_out0[10]),
    .out11(decoder_1_out0[11]), .out12(decoder_1_out0[12]), .out13(decoder_1_out0[13]),
    .out14(decoder_1_out0[14]), .out15(decoder_1_out0[15]), .out16(decoder_1_out0[16]),
    .out17(decoder_1_out0[17]), .out18(decoder_1_out0[18]), .out19(decoder_1_out0[19]),
    .out20(decoder_1_out0[20]), .out21(decoder_1_out0[21]), .out22(decoder_1_out0[22]),
    .out23(decoder_1_out0[23]), .out24(decoder_1_out0[24]), .out25(decoder_1_out0[25]),
    .out26(decoder_1_out0[26]), .out27(decoder_1_out0[27]), .out28(decoder_1_out0[28]),
    .out29(decoder_1_out0[29]), .out30(decoder_1_out0[30]), .out31(decoder_1_out0[31]), .sel(player_x));
  Shifter #(.width(32)) shifter_1 (.in(decoder_1_out0), .\dist (5'b00001), .out(shifter_1_out));
  Shifter #(.width(32), .shift("lr")) shifter_2 (.in(decoder_1_out0), .\dist (5'b00001), .out(shifter_2_out));
  Adder #(.width(5)) adder_1 (.a(player_x), .b(5'b00001), .out(player_x_1));  // open: cin, cout
  Subtractor #(.width(5)) subtractor_1 (.a(player_x), .b(5'b00001), .out(player_x_1_2));  // open: bin, bout
  Comparator #(.width(5), .mode("unsigned")) comparator_1 (
    .a(player_x), .b(5'b11110), .eq(comparator_1_eq));  // open: gt, lt
  Comparator #(.width(5), .mode("unsigned")) comparator_2 (
    .a(player_x), .b(5'b00001), .eq(comparator_2_eq));  // open: gt, lt
  assign player_screen_pixel = shifter_1_out | decoder_1_out0 | shifter_2_out;  // OR_Gate or_1, 32 bits wide
  Multiplexer #(.width(5), .enable("false")) multiplexer_2 (
    .in0(player_x), .in1(player_x_1), .out(multiplexer_2_out), .sel(and_1_out));
  and and_1 (and_1_out, btn_left, ~comparator_1_eq);  // AND_Gate
  and and_2 (and_2_out, btn_right, ~comparator_2_eq);  // AND_Gate
  Multiplexer #(.width(5), .enable("false")) multiplexer_3 (
    .in0(multiplexer_2_out), .in1(player_x_1_2), .out(multiplexer_3_out), .sel(and_2_out));
endmodule

module ai (
  input  [4:0] ball_x,
  input  [4:0] ball_y,
  input  ball_dx,
  input  ball_dy,
  input  [4:0] player_x,
  input  game_clk,
  input  game_active,
  output [31:0] ai_screen_pixel,
  output [4:0] ai_x,
  output [4:0] ai_x_1,
  output [4:0] ai_x_1_2
);

  wire and_1_out, and_2_out, btn_left, btn_right, comparator_1_eq, comparator_2_eq, comparator_4_gt,
       comparator_5_lt, not_1_out;
  wire [4:0] adder_3_out, bit_extender_3_out, multiplexer_2_out, multiplexer_5_out, multiplexer_6_out,
       multiplexer_7_out, multiplexer_8_out, subtractor_5_out;
  wire [7:0] adder_1_out, bit_extender_1_out, bit_extender_2_out, multiplexer_1_out, multiplexer_3_out,
       multiplexer_4_out, subtractor_1_out, subtractor_2_out, subtractor_4_out;
  wire [31:0] decoder_1_out0, shifter_1_out, shifter_2_out;

  assign bit_extender_1_out = {{3{1'b0}}, ball_x};  // Bit_Extender bit_extender_1
  assign bit_extender_2_out = {{3{1'b0}}, ball_y};  // Bit_Extender bit_extender_2
  Adder adder_1 (.a(bit_extender_1_out), .b(bit_extender_2_out), .out(adder_1_out));  // open: cin, cout
  Subtractor subtractor_1 (.a(bit_extender_1_out), .b(bit_extender_2_out), .out(subtractor_1_out));  // open: bin, bout
  not not_1 (not_1_out, game_active);
  Multiplexer #(.width(8), .enable("false")) multiplexer_1 (
    .in0(adder_1_out), .in1(subtractor_1_out), .out(multiplexer_1_out), .sel(ball_dx));
  Multiplexer #(.width(5), .enable("false")) multiplexer_2 (
    .in0(multiplexer_6_out), .in1(5'b01111), .out(multiplexer_2_out), .sel(not_1_out));
  Subtractor subtractor_2 (.a({8{1'b0}}), .b(multiplexer_1_out), .out(subtractor_2_out));  // open: bin, bout
  Decoder #(.select(5), .enable("false")) decoder_1 (
    .out0(decoder_1_out0[0]), .out1(decoder_1_out0[1]), .out2(decoder_1_out0[2]), .out3(decoder_1_out0[3]),
    .out4(decoder_1_out0[4]), .out5(decoder_1_out0[5]), .out6(decoder_1_out0[6]), .out7(decoder_1_out0[7]),
    .out8(decoder_1_out0[8]), .out9(decoder_1_out0[9]), .out10(decoder_1_out0[10]),
    .out11(decoder_1_out0[11]), .out12(decoder_1_out0[12]), .out13(decoder_1_out0[13]),
    .out14(decoder_1_out0[14]), .out15(decoder_1_out0[15]), .out16(decoder_1_out0[16]),
    .out17(decoder_1_out0[17]), .out18(decoder_1_out0[18]), .out19(decoder_1_out0[19]),
    .out20(decoder_1_out0[20]), .out21(decoder_1_out0[21]), .out22(decoder_1_out0[22]),
    .out23(decoder_1_out0[23]), .out24(decoder_1_out0[24]), .out25(decoder_1_out0[25]),
    .out26(decoder_1_out0[26]), .out27(decoder_1_out0[27]), .out28(decoder_1_out0[28]),
    .out29(decoder_1_out0[29]), .out30(decoder_1_out0[30]), .out31(decoder_1_out0[31]), .sel(ai_x));
  Register #(.width(5), .trigger("falling")) register_1 (
    .D(multiplexer_2_out), .Q(ai_x), .clk(game_clk));  // open: en, clr
  Multiplexer #(.width(8), .enable("false")) multiplexer_3 (
    .in0(multiplexer_1_out), .in1(subtractor_2_out), .out(multiplexer_3_out), .sel(multiplexer_1_out[7]));
  Shifter #(.width(32)) shifter_1 (.in(decoder_1_out0), .\dist (5'b00001), .out(shifter_1_out));
  Shifter #(.width(32), .shift("lr")) shifter_2 (.in(decoder_1_out0), .\dist (5'b00001), .out(shifter_2_out));
  Adder #(.width(5)) adder_2 (.a(ai_x), .b(5'b00001), .out(ai_x_1));  // open: cin, cout
  Subtractor #(.width(5)) subtractor_3 (.a(ai_x), .b(5'b00001), .out(ai_x_1_2));  // open: bin, bout
  Comparator #(.width(5), .mode("unsigned")) comparator_1 (
    .a(ai_x), .b(5'b11110), .eq(comparator_1_eq));  // open: gt, lt
  Comparator #(.width(5), .mode("unsigned")) comparator_2 (
    .a(ai_x), .b(5'b00001), .eq(comparator_2_eq));  // open: gt, lt
  Comparator #(.width(5), .mode("unsigned")) comparator_3 (
    .a(multiplexer_8_out), .b(ai_x), .lt(btn_right));  // open: gt, eq
  Multiplexer #(.width(8), .enable("false")) multiplexer_4 (
    .in0(multiplexer_3_out), .in1(subtractor_4_out), .out(multiplexer_4_out), .sel(comparator_4_gt));
  Subtractor subtractor_4 (.a(8'h3e), .b(multiplexer_3_out), .out(subtractor_4_out));  // open: bin, bout
  Comparator #(.mode("unsigned")) comparator_4 (
    .a(multiplexer_3_out), .b(8'h1f), .gt(comparator_4_gt));  // open: eq, lt
  assign ai_screen_pixel = shifter_1_out | decoder_1_out0 | shifter_2_out;  // OR_Gate or_1, 32 bits wide
  Multiplexer #(.width(5), .enable("false")) multiplexer_5 (
    .in0(ai_x), .in1(ai_x_1), .out(multiplexer_5_out), .sel(and_1_out));
  and and_1 (and_1_out, btn_left, ~comparator_1_eq);  // AND_Gate
  and and_2 (and_2_out, btn_right, ~comparator_2_eq);  // AND_Gate
  Bit_Extender #(.out_width(5)) bit_extender_3 (.in(multiplexer_4_out), .out(bit_extender_3_out));
  Multiplexer #(.width(5), .enable("false")) multiplexer_6 (
    .in0(multiplexer_5_out), .in1(ai_x_1_2), .out(multiplexer_6_out), .sel(and_2_out));
  Subtractor #(.width(5)) subtractor_5 (
    .a(bit_extender_3_out), .b(5'b00001), .out(subtractor_5_out));  // open: bin, bout
  Adder #(.width(5)) adder_3 (.a(bit_extender_3_out), .b(5'b00001), .out(adder_3_out));  // open: cin, cout
  Comparator #(.width(5), .mode("unsigned")) comparator_5 (
    .a(bit_extender_3_out), .b(player_x), .lt(comparator_5_lt));  // open: gt, eq
  Comparator #(.width(5), .mode("unsigned")) comparator_6 (
    .a(multiplexer_8_out), .b(ai_x_1), .gt(btn_left));  // open: eq, lt
  Multiplexer #(.width(5), .enable("false")) multiplexer_7 (
    .in0(subtractor_5_out), .in1(adder_3_out), .out(multiplexer_7_out), .sel(comparator_5_lt));
  Multiplexer #(.width(5), .enable("false")) multiplexer_8 (
    .in0(5'b01111), .in1(multiplexer_7_out), .out(multiplexer_8_out), .sel(ball_dy));

  // Notes on the sheet:
  //   Ricochet off the RIGHT wall
  //   Ricochet off the LEFT wall
  //   Pred_X
endmodule

module collision_check (
  input  [4:0] player_x,
  input  [4:0] player_x_1,
  input  [4:0] player_x_1_2,
  input  [4:0] ball_x,
  input  [4:0] ball_y,
  input  [4:0] coordinate_to_check,
  output hit_x,
  output hit_x_1,
  output hit_x_1_2,
  output hit_x_2,
  output hit_x_2_2
);

  wire comparator_1_eq, comparator_2_eq, comparator_3_eq, comparator_4_eq, comparator_5_lt, comparator_6_eq,
       comparator_7_eq, comparator_8_gt;
  wire [4:0] adder_1_out, subtractor_1_out;

  Adder #(.width(5)) adder_1 (.a(player_x), .b(5'b00010), .out(adder_1_out));  // open: cin, cout
  Subtractor #(.width(5)) subtractor_1 (.a(player_x), .b(5'b00010), .out(subtractor_1_out));  // open: bin, bout
  Comparator #(.width(5), .mode("unsigned")) comparator_1 (
    .a(player_x), .b(ball_x), .eq(comparator_1_eq));  // open: gt, lt
  Comparator #(.width(5), .mode("unsigned")) comparator_2 (
    .a(player_x_1), .b(ball_x), .eq(comparator_2_eq));  // open: gt, lt
  Comparator #(.width(5), .mode("unsigned")) comparator_3 (
    .a(player_x_1_2), .b(ball_x), .eq(comparator_3_eq));  // open: gt, lt
  Comparator #(.width(5)) comparator_4 (.a(ball_y), .b(coordinate_to_check), .eq(comparator_4_eq));  // open: gt, lt
  Comparator #(.width(5), .mode("unsigned")) comparator_5 (
    .a(player_x), .b(5'b11110), .lt(comparator_5_lt));  // open: gt, eq
  Comparator #(.width(5), .mode("unsigned")) comparator_6 (
    .a(adder_1_out), .b(ball_x), .eq(comparator_6_eq));  // open: gt, lt
  Comparator #(.width(5), .mode("unsigned")) comparator_7 (
    .a(subtractor_1_out), .b(ball_x), .eq(comparator_7_eq));  // open: gt, lt
  Comparator #(.width(5), .mode("unsigned")) comparator_8 (
    .a(player_x), .b(5'b00001), .gt(comparator_8_gt));  // open: eq, lt
  and and_1 (hit_x, comparator_1_eq, comparator_4_eq);
  and and_2 (hit_x_1, comparator_2_eq, comparator_4_eq);
  and and_3 (hit_x_1_2, comparator_3_eq, comparator_4_eq);
  and and_4 (hit_x_2, comparator_5_lt, comparator_6_eq, comparator_4_eq);
  and and_5 (hit_x_2_2, comparator_7_eq, comparator_4_eq);
endmodule

module ball (
  input  dX,
  input  dY,
  input  [4:0] slope_x,
  input  [4:0] slope_y,
  input  freeze,
  input  [4:0] player_x,
  input  game_clk,
  input  game_active,
  output [4:0] ball_x,
  output [31:0] out_10,
  output [31:0] out_11,
  output [31:0] out_12,
  output [31:0] out_13,
  output [31:0] out_14,
  output [31:0] out_15,
  output [31:0] out_16,
  output [31:0] out_17,
  output [31:0] out_18,
  output [31:0] out_19,
  output [31:0] out_20,
  output [31:0] out_21,
  output [31:0] out_22,
  output [31:0] out_23,
  output [31:0] out_24,
  output [31:0] out_25,
  output [31:0] out_26,
  output [31:0] out_27,
  output [31:0] out_28,
  output [31:0] out_29,
  output [31:0] out_30,
  output [31:0] out_31,
  output [31:0] out_32,
  output [31:0] out_33,
  output [31:0] out_34,
  output [31:0] out_35,
  output [31:0] out_36,
  output [31:0] out_37,
  output [31:0] out_38,
  output [31:0] out_39,
  output [31:0] out_40,
  output [31:0] out_41,
  output [4:0] ball_y
);

  wire adder_1_cout, adder_2_cout, and_1_out, decoder_2_out0, decoder_2_out1, decoder_2_out2, decoder_2_out3,
       decoder_2_out4, decoder_2_out5, decoder_2_out6, decoder_2_out7, decoder_2_out8, decoder_2_out9,
       decoder_2_out10, decoder_2_out11, decoder_2_out12, decoder_2_out13, decoder_2_out14, decoder_2_out15,
       decoder_2_out16, decoder_2_out17, decoder_2_out18, decoder_2_out19, decoder_2_out20, decoder_2_out21,
       decoder_2_out22, decoder_2_out23, decoder_2_out24, decoder_2_out25, decoder_2_out26, decoder_2_out27,
       decoder_2_out28, decoder_2_out29, decoder_2_out30, decoder_2_out31, not_1_out, not_2_out, or_1_out,
       or_2_out;
  wire [4:0] adder_1_out, adder_2_out, adder_3_out, adder_4_out, Error_Reg_X_q, Error_Reg_Y_q,
       multiplexer_1_out, multiplexer_2_out, multiplexer_3_out, multiplexer_4_out, multiplexer_5_out,
       subtractor_1_out, subtractor_2_out;
  wire [31:0] decoder_1_out0;

  not not_1 (not_1_out, game_active);
  not not_2 (not_2_out, game_active);
  Register #(.width(5)) Error_Reg_X (.D(adder_1_out), .Q(Error_Reg_X_q), .clk(game_clk), .clr(not_1_out));  // open: en
  Register #(.width(5)) Error_Reg_Y (.D(adder_2_out), .Q(Error_Reg_Y_q), .clk(game_clk), .clr(not_2_out));  // open: en
  Multiplexer #(.width(5), .enable("false")) multiplexer_1 (
    .in0(multiplexer_4_out), .in1(5'b01111), .out(multiplexer_1_out), .sel(not_1_out));
  or or_1 (or_1_out, not_1_out, adder_1_cout);
  Adder #(.width(5)) adder_1 (.a(Error_Reg_X_q), .b(slope_x), .out(adder_1_out), .cout(adder_1_cout));  // open: cin
  Multiplexer #(.width(5), .enable("false")) multiplexer_2 (
    .in0(multiplexer_5_out), .in1(5'b01111), .out(multiplexer_2_out), .sel(not_2_out));
  or or_2 (or_2_out, not_2_out, adder_2_cout);
  Adder #(.width(5)) adder_2 (.a(Error_Reg_Y_q), .b(slope_y), .out(adder_2_out), .cout(adder_2_cout));  // open: cin
  Multiplexer #(.width(5), .enable("false")) multiplexer_3 (
    .in0(multiplexer_1_out), .in1(player_x), .out(multiplexer_3_out), .sel(freeze));
  and and_1 (and_1_out, or_2_out, ~freeze);  // AND_Gate
  Register #(.width(5)) X (.D(multiplexer_3_out), .en(or_1_out), .Q(ball_x), .clk(game_clk));  // open: clr
  Register #(.width(5)) Y (.D(multiplexer_2_out), .en(and_1_out), .Q(ball_y), .clk(game_clk));  // open: clr
  Adder #(.width(5)) adder_3 (.a(ball_x), .b(5'b00001), .out(adder_3_out));  // open: cin, cout
  Subtractor #(.width(5)) subtractor_1 (.a(ball_x), .b(5'b00001), .out(subtractor_1_out));  // open: bin, bout
  Adder #(.width(5)) adder_4 (.a(ball_y), .b(5'b00001), .out(adder_4_out));  // open: cin, cout
  Subtractor #(.width(5)) subtractor_2 (.a(ball_y), .b(5'b00001), .out(subtractor_2_out));  // open: bin, bout
  Multiplexer #(.width(5), .enable("false")) multiplexer_4 (
    .in0(adder_3_out), .in1(subtractor_1_out), .out(multiplexer_4_out), .sel(dX));
  Multiplexer #(.width(5), .enable("false")) multiplexer_5 (
    .in0(adder_4_out), .in1(subtractor_2_out), .out(multiplexer_5_out), .sel(dY));
  Decoder #(.select(5), .enable("false")) decoder_1 (
    .out0(decoder_1_out0[0]), .out1(decoder_1_out0[1]), .out2(decoder_1_out0[2]), .out3(decoder_1_out0[3]),
    .out4(decoder_1_out0[4]), .out5(decoder_1_out0[5]), .out6(decoder_1_out0[6]), .out7(decoder_1_out0[7]),
    .out8(decoder_1_out0[8]), .out9(decoder_1_out0[9]), .out10(decoder_1_out0[10]),
    .out11(decoder_1_out0[11]), .out12(decoder_1_out0[12]), .out13(decoder_1_out0[13]),
    .out14(decoder_1_out0[14]), .out15(decoder_1_out0[15]), .out16(decoder_1_out0[16]),
    .out17(decoder_1_out0[17]), .out18(decoder_1_out0[18]), .out19(decoder_1_out0[19]),
    .out20(decoder_1_out0[20]), .out21(decoder_1_out0[21]), .out22(decoder_1_out0[22]),
    .out23(decoder_1_out0[23]), .out24(decoder_1_out0[24]), .out25(decoder_1_out0[25]),
    .out26(decoder_1_out0[26]), .out27(decoder_1_out0[27]), .out28(decoder_1_out0[28]),
    .out29(decoder_1_out0[29]), .out30(decoder_1_out0[30]), .out31(decoder_1_out0[31]), .sel(ball_x));
  Decoder #(.select(5), .enable("false")) decoder_2 (
    .out0(decoder_2_out0), .out1(decoder_2_out1), .out2(decoder_2_out2), .out3(decoder_2_out3),
    .out4(decoder_2_out4), .out5(decoder_2_out5), .out6(decoder_2_out6), .out7(decoder_2_out7),
    .out8(decoder_2_out8), .out9(decoder_2_out9), .out10(decoder_2_out10), .out11(decoder_2_out11),
    .out12(decoder_2_out12), .out13(decoder_2_out13), .out14(decoder_2_out14), .out15(decoder_2_out15),
    .out16(decoder_2_out16), .out17(decoder_2_out17), .out18(decoder_2_out18), .out19(decoder_2_out19),
    .out20(decoder_2_out20), .out21(decoder_2_out21), .out22(decoder_2_out22), .out23(decoder_2_out23),
    .out24(decoder_2_out24), .out25(decoder_2_out25), .out26(decoder_2_out26), .out27(decoder_2_out27),
    .out28(decoder_2_out28), .out29(decoder_2_out29), .out30(decoder_2_out30), .out31(decoder_2_out31),
    .sel(ball_y));
  assign out_10 = decoder_2_out0 ? decoder_1_out0 : 32'bz;  // Controlled_Buffer controlled_buffer_1
  assign out_11 = decoder_2_out1 ? decoder_1_out0 : 32'bz;  // Controlled_Buffer controlled_buffer_2
  assign out_12 = decoder_2_out2 ? decoder_1_out0 : 32'bz;  // Controlled_Buffer controlled_buffer_3
  assign out_13 = decoder_2_out3 ? decoder_1_out0 : 32'bz;  // Controlled_Buffer controlled_buffer_4
  assign out_14 = decoder_2_out4 ? decoder_1_out0 : 32'bz;  // Controlled_Buffer controlled_buffer_5
  assign out_15 = decoder_2_out5 ? decoder_1_out0 : 32'bz;  // Controlled_Buffer controlled_buffer_6
  assign out_16 = decoder_2_out6 ? decoder_1_out0 : 32'bz;  // Controlled_Buffer controlled_buffer_7
  assign out_17 = decoder_2_out7 ? decoder_1_out0 : 32'bz;  // Controlled_Buffer controlled_buffer_8
  assign out_18 = decoder_2_out8 ? decoder_1_out0 : 32'bz;  // Controlled_Buffer controlled_buffer_9
  assign out_19 = decoder_2_out9 ? decoder_1_out0 : 32'bz;  // Controlled_Buffer controlled_buffer_10
  assign out_20 = decoder_2_out10 ? decoder_1_out0 : 32'bz;  // Controlled_Buffer controlled_buffer_11
  assign out_21 = decoder_2_out11 ? decoder_1_out0 : 32'bz;  // Controlled_Buffer controlled_buffer_12
  assign out_22 = decoder_2_out12 ? decoder_1_out0 : 32'bz;  // Controlled_Buffer controlled_buffer_13
  assign out_23 = decoder_2_out13 ? decoder_1_out0 : 32'bz;  // Controlled_Buffer controlled_buffer_14
  assign out_24 = decoder_2_out14 ? decoder_1_out0 : 32'bz;  // Controlled_Buffer controlled_buffer_15
  assign out_25 = decoder_2_out15 ? decoder_1_out0 : 32'bz;  // Controlled_Buffer controlled_buffer_16
  assign out_26 = decoder_2_out16 ? decoder_1_out0 : 32'bz;  // Controlled_Buffer controlled_buffer_17
  assign out_27 = decoder_2_out17 ? decoder_1_out0 : 32'bz;  // Controlled_Buffer controlled_buffer_18
  assign out_28 = decoder_2_out18 ? decoder_1_out0 : 32'bz;  // Controlled_Buffer controlled_buffer_19
  assign out_29 = decoder_2_out19 ? decoder_1_out0 : 32'bz;  // Controlled_Buffer controlled_buffer_20
  assign out_30 = decoder_2_out20 ? decoder_1_out0 : 32'bz;  // Controlled_Buffer controlled_buffer_21
  assign out_31 = decoder_2_out21 ? decoder_1_out0 : 32'bz;  // Controlled_Buffer controlled_buffer_22
  assign out_32 = decoder_2_out22 ? decoder_1_out0 : 32'bz;  // Controlled_Buffer controlled_buffer_23
  assign out_33 = decoder_2_out23 ? decoder_1_out0 : 32'bz;  // Controlled_Buffer controlled_buffer_24
  assign out_34 = decoder_2_out24 ? decoder_1_out0 : 32'bz;  // Controlled_Buffer controlled_buffer_25
  assign out_35 = decoder_2_out25 ? decoder_1_out0 : 32'bz;  // Controlled_Buffer controlled_buffer_26
  assign out_36 = decoder_2_out26 ? decoder_1_out0 : 32'bz;  // Controlled_Buffer controlled_buffer_27
  assign out_37 = decoder_2_out27 ? decoder_1_out0 : 32'bz;  // Controlled_Buffer controlled_buffer_28
  assign out_38 = decoder_2_out28 ? decoder_1_out0 : 32'bz;  // Controlled_Buffer controlled_buffer_29
  assign out_39 = decoder_2_out29 ? decoder_1_out0 : 32'bz;  // Controlled_Buffer controlled_buffer_30
  assign out_40 = decoder_2_out30 ? decoder_1_out0 : 32'bz;  // Controlled_Buffer controlled_buffer_31
  assign out_41 = decoder_2_out31 ? decoder_1_out0 : 32'bz;  // Controlled_Buffer controlled_buffer_32
  Pull_Resistor pull_resistor_1 (.node(out_38));
  Pull_Resistor pull_resistor_2 (.node(out_39));
  Pull_Resistor pull_resistor_3 (.node(out_36));
  Pull_Resistor pull_resistor_4 (.node(out_34));
  Pull_Resistor pull_resistor_5 (.node(out_40));
  Pull_Resistor pull_resistor_6 (.node(out_37));
  Pull_Resistor pull_resistor_7 (.node(out_41));
  Pull_Resistor pull_resistor_8 (.node(out_35));
  Pull_Resistor pull_resistor_9 (.node(out_26));
  Pull_Resistor pull_resistor_10 (.node(out_33));
  Pull_Resistor pull_resistor_11 (.node(out_27));
  Pull_Resistor pull_resistor_12 (.node(out_32));
  Pull_Resistor pull_resistor_13 (.node(out_31));
  Pull_Resistor pull_resistor_14 (.node(out_30));
  Pull_Resistor pull_resistor_15 (.node(out_29));
  Pull_Resistor pull_resistor_16 (.node(out_28));
  Pull_Resistor pull_resistor_17 (.node(out_23));
  Pull_Resistor pull_resistor_18 (.node(out_25));
  Pull_Resistor pull_resistor_19 (.node(out_24));
  Pull_Resistor pull_resistor_20 (.node(out_21));
  Pull_Resistor pull_resistor_21 (.node(out_19));
  Pull_Resistor pull_resistor_22 (.node(out_18));
  Pull_Resistor pull_resistor_23 (.node(out_22));
  Pull_Resistor pull_resistor_24 (.node(out_20));
  Pull_Resistor pull_resistor_25 (.node(out_17));
  Pull_Resistor pull_resistor_26 (.node(out_14));
  Pull_Resistor pull_resistor_27 (.node(out_10));
  Pull_Resistor pull_resistor_28 (.node(out_13));
  Pull_Resistor pull_resistor_29 (.node(out_16));
  Pull_Resistor pull_resistor_30 (.node(out_15));
  Pull_Resistor pull_resistor_31 (.node(out_11));
  Pull_Resistor pull_resistor_32 (.node(out_12));

  // Other names for the same wires on the sheet: player_y[4:0] = player_x
endmodule

module dX (
  input  hit_ai_x,
  input  hit_ai_x_1,
  input  hit_ai_x_1_2,
  input  hit_ai_x_2,
  input  hit_ai_x_2_2,
  input  hit_player_x,
  input  hit_player_x_1,
  input  hit_player_x_1_2,
  input  hit_player_x_2,
  input  hit_player_x_2_2,
  input  btn_left,
  input  btn_right,
  input  freeze,
  input  [4:0] ball_x,
  input  game_clk,
  output dX
);

  wire and_1_out, and_2_out, comparator_1_eq, comparator_2_eq, d_ff_1_q, not_1_out, or_1_out, or_2_out,
       or_3_out, or_4_out, or_5_out, or_6_out, s_r_ff_1_q, s_r_ff_2_q;
  wire [2:0] priority_encoder_1_out;

  or or_1 (or_1_out, hit_ai_x, hit_player_x);
  or or_2 (or_2_out, hit_ai_x_1, hit_ai_x_2, hit_player_x_1, hit_player_x_2);
  or or_3 (or_3_out, hit_ai_x_1_2, hit_ai_x_2_2, hit_player_x_1_2, hit_player_x_2_2);
  or or_4 (or_4_out, or_2_out, or_3_out);
  and and_1 (and_1_out, btn_left, freeze);
  not not_1 (not_1_out, freeze);
  and and_2 (and_2_out, freeze, btn_right);
  S_R_Flip_Flop #(.trigger("falling")) s_r_ff_1 (
    .S(and_1_out), .clk(game_clk), .R(not_1_out), .Q(s_r_ff_1_q));  // open: Qn, preset, reset, en
  S_R_Flip_Flop #(.trigger("falling")) s_r_ff_2 (
    .S(and_2_out), .clk(game_clk), .R(not_1_out), .Q(s_r_ff_2_q));  // open: Qn, preset, reset, en
  Comparator #(.width(5), .mode("unsigned")) comparator_1 (
    .a(ball_x), .b({5{1'b0}}), .eq(comparator_1_eq));  // open: gt, lt
  or or_5 (or_5_out, comparator_1_eq, comparator_2_eq);
  Comparator #(.width(5), .mode("unsigned")) comparator_2 (
    .a(ball_x), .b({5{1'b1}}), .eq(comparator_2_eq));  // open: gt, lt
  or or_6 (or_6_out, or_1_out, or_4_out, s_r_ff_1_q, s_r_ff_2_q, or_5_out);
  D_Flip_Flop #(.trigger("falling")) d_ff_1 (.clk(or_6_out), .D(dX), .Q(d_ff_1_q));  // open: Qn, preset, en, reset
  Priority_Encoder priority_encoder_1 (
    .in0(1'b1), .in1(or_2_out), .in2(or_3_out), .in3(s_r_ff_1_q), .in4(s_r_ff_2_q), .in5(comparator_2_eq),
    .in6(comparator_1_eq), .out(priority_encoder_1_out));  // open: in7, en_in, gs, en_out
  Multiplexer #(.select(3), .enable("false")) multiplexer_1 (
    .in0(d_ff_1_q), .in1(1'b0), .in2(1'b1), .in3(1'b0), .in4(1'b1), .in5(1'b1), .in6(1'b0), .out(dX),
    .sel(priority_encoder_1_out));  // open: in7

  // Notes on the sheet:
  //   right_hit_any
  //   center_hit_any
  //   left_hit_any
  //   EVENT_HIT_RIGHT_WALL
  //   EVENT_HIT_LEFT_WALL
endmodule

module dY (
  input  hit_ai,
  input  hit_player,
  input  game_active,
  output hit_any,
  output dY
);

  wire d_ff_1_q, not_1_out;

  or or_1 (hit_any, hit_ai, hit_player);
  D_Flip_Flop #(.trigger("falling")) d_ff_1 (
    .clk(hit_any), .D(dY), .Q(d_ff_1_q), .en(game_active), .reset(not_1_out));  // open: Qn, preset
  not not_1 (not_1_out, game_active);
  Multiplexer #(.select(2), .enable("false")) multiplexer_1 (
    .in0(d_ff_1_q), .in1(1'b0), .in2(1'b1), .in3(1'b0), .out(dY), .sel({hit_player, hit_ai}));
endmodule

module Bresenham (
  input  hit_ai_x_1,
  input  hit_ai_x_1_2,
  input  hit_ai_x_2,
  input  hit_ai_x_2_2,
  input  hit_player_x_1,
  input  hit_player_x_1_2,
  input  hit_player_x_2,
  input  hit_player_x_2_2,
  input  hit_any,
  input  game_clk,
  input  game_active,
  output [4:0] slope_x,
  output [4:0] slope_y
);

  wire not_1_out;
  wire [1:0] Angle_Reg_q, or_1_out;

  or or_1 (or_1_out[0], hit_ai_x_1, hit_ai_x_1_2, hit_player_x_1, hit_player_x_1_2);
  or or_2 (or_1_out[1], hit_ai_x_2, hit_ai_x_2_2, hit_player_x_2, hit_player_x_2_2);
  Register #(.width(2)) Angle_Reg (.D(or_1_out), .en(hit_any), .Q(Angle_Reg_q), .clk(game_clk), .clr(not_1_out));
  not not_1 (not_1_out, game_active);
  Multiplexer #(.select(2), .width(5), .enable("false")) multiplexer_1 (
    .in0(5'b01000), .in1(5'b10000), .in2({5{1'b1}}), .out(slope_x), .sel(Angle_Reg_q));  // open: in3
  Multiplexer #(.select(2), .width(5), .enable("false")) multiplexer_2 (
    .in0({5{1'b1}}), .in1(5'b10000), .in2(5'b01000), .out(slope_y), .sel(Angle_Reg_q));  // open: in3

  // Notes on the sheet:
  //   border_hit
  //   corner_hit
endmodule

module freeze (
  input  game_clk,
  input  hit_x,
  input  hit_x_1,
  input  hit_x_1_2,
  input  btn_left,
  input  btn_right,
  output freeze
);

  wire and_1_out, and_2_out, d_ff_1_qn, or_1_out, or_2_out, shift_register_1_q0, shift_register_1_q1,
       shift_register_1_q2, shift_register_1_q3, shift_register_1_q4, shift_register_1_q5,
       shift_register_1_q6, shift_register_1_q7;

  or or_1 (or_1_out, hit_x, hit_x_1, hit_x_1_2);
  and and_1 (and_1_out, or_1_out, or_2_out);
  or or_2 (or_2_out, btn_left, btn_right);
  D_Flip_Flop #(.trigger("falling")) d_ff_1 (
    .clk(game_clk), .D(and_1_out), .Qn(d_ff_1_qn));  // open: Q, preset, en, reset
  and and_2 (and_2_out, d_ff_1_qn, and_1_out);
  Shift_Register #(.trigger("falling")) shift_register_1 (
    .shift(1'b1), .in(and_2_out), .clk(game_clk), .q0(shift_register_1_q0), .q1(shift_register_1_q1),
    .q2(shift_register_1_q2), .q3(shift_register_1_q3), .q4(shift_register_1_q4), .q5(shift_register_1_q5),
    .q6(shift_register_1_q6), .q7(shift_register_1_q7));  // open: out, load, clr, d0, d1, d2, d3, d4, d5, d6, d7
  or or_3 (freeze, shift_register_1_q7, shift_register_1_q6, shift_register_1_q5, shift_register_1_q4, shift_register_1_q3, shift_register_1_q2, shift_register_1_q1, shift_register_1_q0);
endmodule

module is_valid (
  input  [6:0] kbd_symbol,
  output is_valid
);

  wire and_1_out, and_2_out, comparator_1_eq, comparator_2_eq, comparator_3_eq, comparator_4_gt,
       comparator_5_lt, comparator_6_gt, comparator_7_lt;

  Comparator #(.width(7), .mode("unsigned")) comparator_1 (
    .a(kbd_symbol), .b(7'b0100000), .eq(comparator_1_eq));  // open: gt, lt
  Comparator #(.width(7), .mode("unsigned")) comparator_2 (
    .a(kbd_symbol), .b(7'b1011111), .eq(comparator_2_eq));  // open: gt, lt
  Comparator #(.width(7), .mode("unsigned")) comparator_3 (
    .a(kbd_symbol), .b(7'b0001000), .eq(comparator_3_eq));  // open: gt, lt
  Comparator #(.width(7), .mode("unsigned")) comparator_4 (
    .a(kbd_symbol), .b(7'b1000000), .gt(comparator_4_gt));  // open: eq, lt
  Comparator #(.width(7), .mode("unsigned")) comparator_5 (
    .a(kbd_symbol), .b(7'b1011011), .lt(comparator_5_lt));  // open: gt, eq
  Comparator #(.width(7), .mode("unsigned")) comparator_6 (
    .a(kbd_symbol), .b(7'b1100000), .gt(comparator_6_gt));  // open: eq, lt
  Comparator #(.width(7), .mode("unsigned")) comparator_7 (
    .a(kbd_symbol), .b(7'b1111011), .lt(comparator_7_lt));  // open: gt, eq
  and and_1 (and_1_out, comparator_4_gt, comparator_5_lt);
  and and_2 (and_2_out, comparator_6_gt, comparator_7_lt);
  or or_1 (is_valid, comparator_1_eq, comparator_2_eq, comparator_3_eq, and_1_out, and_2_out);

  // Notes on the sheet:
  //   Пробел
  //   Нижнее подчеркивание
  //   Стереть
  //   A-Z
  //   a-z
endmodule

module game_active (
  input  [4:0] ball_y,
  input  btn_left,
  input  btn_right,
  input  btn_reset,
  input  game_clk,
  input  interrupt,
  output [3:0] player_fails,
  output [3:0] ai_fails,
  output player_loser,
  output game_active
);

  wire comparator_1_eq, comparator_2_eq, comparator_3_eq, comparator_4_eq, not_1_out, not_2_out, or_1_out,
       or_2_out, or_3_out, or_4_out, or_5_out, xnor_1_out, xnor_2_out;

  Comparator #(.width(5), .mode("unsigned")) comparator_1 (
    .a(ball_y), .b({5{1'b0}}), .eq(comparator_1_eq));  // open: gt, lt
  Comparator #(.width(5), .mode("unsigned")) comparator_2 (
    .a(ball_y), .b({5{1'b1}}), .eq(comparator_2_eq));  // open: gt, lt
  or or_1 (or_1_out, comparator_1_eq, comparator_2_eq);
  not not_1 (not_1_out, btn_left);
  not not_2 (not_2_out, btn_right);
  or or_2 (or_2_out, or_1_out, btn_reset);
  xnor xnor_1 (xnor_1_out, btn_left, not_1_out);
  or or_3 (or_3_out, xnor_1_out, xnor_2_out);
  xnor xnor_2 (xnor_2_out, btn_right, not_2_out);
  S_R_Flip_Flop #(.trigger("high")) s_r_ff_1 (
    .S(or_3_out), .clk(game_clk), .R(or_2_out), .Q(game_active));  // open: Qn, preset, reset, en
  Counter #(.width(4), .max('hf)) counter_1 (
    .Q(player_fails), .clk(comparator_1_eq), .clr(or_5_out));  // open: load, D, count, carry
  Counter #(.width(4), .max('hf)) counter_2 (
    .Q(ai_fails), .clk(comparator_2_eq), .clr(or_5_out));  // open: load, D, count, carry
  Comparator #(.width(4), .mode("unsigned")) comparator_3 (
    .a(player_fails), .b(4'b0101), .eq(comparator_3_eq));  // open: gt, lt
  Comparator #(.width(4), .mode("unsigned")) comparator_4 (
    .a(4'b0101), .b(ai_fails), .eq(comparator_4_eq));  // open: gt, lt
  or or_4 (or_4_out, comparator_3_eq, comparator_4_eq);
  D_Flip_Flop d_ff_1 (.clk(or_4_out), .D(or_4_out), .Q(player_loser), .reset(interrupt));  // open: Qn, preset, en
  or or_5 (or_5_out, btn_reset, or_4_out);

  // Other names for the same wires on the sheet: L = btn_left; R = btn_right; Reset = btn_reset

  // Notes on the sheet:
  //   EVENT_HIT_TOP_WALL
  //   EVENT_HIT_BOTTOM_WALL
endmodule

module test (
);

  wire and_1_out, and_2_out, and_3_out, button_1_out, cdm8_clk, comparator_1_eq, counter_1_carry, init_table,
       not_1_out, not_2_out, or_1_out, R, rd_wr, undriven_2, xnor_1_out, xnor_2_out;
  wire [0:0] I_O_data_read;
  wire [3:0] undriven;
  wire [5:0] counter_1_q;
  wire [7:0] bit_extender_1_out, bit_extender_2_out, I_O_data_write, init_addr, init_data;

  Comparator #(.width(4), .mode("unsigned")) comparator_1 (
    .a(undriven), .b(4'b0100), .eq(comparator_1_eq));  // open: gt, lt
  Button button_1 (.out(button_1_out));
  not not_1 (not_1_out, button_1_out);
  not not_2 (not_2_out, R);
  and and_1 (and_1_out, undriven_2, comparator_1_eq);
  xnor xnor_1 (xnor_1_out, button_1_out, not_1_out);
  or or_1 (or_1_out, xnor_1_out, xnor_2_out);
  xnor xnor_2 (xnor_2_out, R, not_2_out);
  and and_2 (and_2_out, ~rd_wr, and_1_out);  // AND_Gate
  S_R_Flip_Flop s_r_ff_1 (
    .S(I_O_data_read[0]), .clk(cdm8_clk), .R(counter_1_carry), .Q(init_table), .reset(counter_1_carry),
    .en(and_2_out));  // open: Qn, preset
  assign I_O_data_write = and_3_out ? bit_extender_1_out : 8'bz;  // Controlled_Buffer controlled_buffer_1
  assign bit_extender_1_out = {{7{1'b0}}, init_table};  // Bit_Extender bit_extender_1
  and and_3 (and_3_out, rd_wr, and_1_out);
  Counter #(.width(6), .max('h2c), .ongoal("stay")) counter_1 (
    .count(init_table), .Q(counter_1_q), .carry(counter_1_carry), .clk(cdm8_clk), .clr(or_1_out));  // open: load, D
  assign bit_extender_2_out = {{2{1'b0}}, counter_1_q};  // Bit_Extender bit_extender_2
  Adder adder_1 (.a(bit_extender_2_out), .b(8'h10), .out(init_addr));  // open: cin, cout
  ROM rom_1 (.addr(bit_extender_2_out), .data(init_data), .sel(1'b1));

  // Notes on the sheet:
  //   DMA_ACTIVE
  //   contents of rom_1 (hex, n*v repeats v):
  //   0 49 72 74 65 67 6f 76 0 0 4e 61 7a 61 72 6f 76 0 0 42 6f 6e 64 61 72 65 76 0 49 76 61 6e 6f 76 0 0
  //   0 50 65 74 72 6f 76
endmodule

module player_score_speed (
  input  [7:0] speed,
  input  [7:0] player_score,
  input  hit_player,
  input  f1_wrtie,
  input  game_clk
);

  wire and_1_out, counter_2_carry, d_ff_1_qn, not_1_out, s_r_ff_1_q;
  wire [2:0] counter_3_q;

  not not_1 (not_1_out, hit_player);
  S_R_Flip_Flop #(.trigger("falling")) s_r_ff_1 (
    .S(hit_player), .clk(game_clk), .R(not_1_out), .Q(s_r_ff_1_q));  // open: Qn, preset, reset, en
  Counter counter_1 (.Q(player_score), .clk(s_r_ff_1_q), .clr(f1_wrtie));  // open: load, D, count, carry
  Counter #(.width(4), .max('h5)) counter_2 (
    .carry(counter_2_carry), .clk(s_r_ff_1_q), .clr(f1_wrtie));  // open: load, D, count, Q
  D_Flip_Flop #(.trigger("falling")) d_ff_1 (
    .clk(game_clk), .D(counter_2_carry), .Qn(d_ff_1_qn));  // open: Q, preset, en, reset
  and and_1 (and_1_out, d_ff_1_qn, counter_2_carry);
  Counter #(.width(3), .max('h7), .ongoal("stay")) counter_3 (
    .count(and_1_out), .Q(counter_3_q), .clk(game_clk), .clr(f1_wrtie));  // open: load, D, carry
  Multiplexer #(.select(3), .width(8), .enable("false")) multiplexer_1 (
    .in0(8'h40), .in1(8'h38), .in2(8'h35), .in3(8'h30), .in4(8'h28), .in5(8'h25), .in6(8'h20), .in7(8'h15),
    .out(speed), .sel(counter_3_q));
endmodule
