// Logisim project Ьase17_14.0.circ as structural Verilog
module GAME (
);

  wire button_1_out, keyboard_1_avail, L, main_1_cdm8_clk, main_1_clear_kbd, main_1_clear_name_screen,
       main_1_f1_write, main_1_is_valid, main_1_kbd_enable, R, Reset;
  wire [3:0] main_1_ai_fails, main_1_hundred, main_1_one, main_1_player_fails, main_1_ten;
  wire [6:0] keyboard_1_data, main_1_i_o_data_read;
  wire [31:0] main_1_out_7, main_1_out_8, main_1_out_10, main_1_out_11, main_1_out_13, main_1_out_14,
       main_1_out_15, main_1_out_16, main_1_out_17, main_1_out_18, main_1_out_19, main_1_out_20,
       main_1_out_21, main_1_out_22, main_1_out_23, main_1_out_24, main_1_out_25, main_1_out_26,
       main_1_out_27, main_1_out_28, main_1_out_29, main_1_out_30, main_1_out_31, main_1_out_32,
       main_1_out_33, main_1_out_34, main_1_out_35, main_1_out_36, main_1_out_37, main_1_out_38,
       main_1_out_39, main_1_out_40;

  DotMatrix #(.inputtype("row"), .matrixcols(32), .matrixrows(1)) dotmatrix_1 (.row0(main_1_out_7));
  main main_1 (
    .btn_left(L), .btn_right(R), .btn_reset(Reset), .out_7(main_1_out_7), .out_8(main_1_out_8),
    .out_10(main_1_out_10), .out_11(main_1_out_11), .out_13(main_1_out_13), .out_14(main_1_out_14),
    .out_15(main_1_out_15), .out_16(main_1_out_16), .out_17(main_1_out_17), .out_18(main_1_out_18),
    .out_19(main_1_out_19), .out_20(main_1_out_20), .out_21(main_1_out_21), .out_22(main_1_out_22),
    .out_23(main_1_out_23), .out_24(main_1_out_24), .out_25(main_1_out_25), .out_26(main_1_out_26),
    .out_27(main_1_out_27), .out_28(main_1_out_28), .out_29(main_1_out_29), .out_30(main_1_out_30),
    .out_31(main_1_out_31), .out_32(main_1_out_32), .out_33(main_1_out_33), .out_34(main_1_out_34),
    .out_35(main_1_out_35), .out_36(main_1_out_36), .out_37(main_1_out_37), .out_38(main_1_out_38),
    .out_39(main_1_out_39), .out_40(main_1_out_40), .player_fails(main_1_player_fails),
    .ai_fails(main_1_ai_fails), .one(main_1_one), .hundred(main_1_hundred), .ten(main_1_ten),
    .btn_input_name(button_1_out), .I_O_data_read(main_1_i_o_data_read), .f1_write(main_1_f1_write),
    .cdm8_clk(main_1_cdm8_clk), .clear_name_screen(main_1_clear_name_screen), .is_valid(main_1_is_valid),
    .clear_kbd(main_1_clear_kbd), .kbd_enable(main_1_kbd_enable), .kbd_data(keyboard_1_data),
    .kbd_is_ready(keyboard_1_avail));
  DotMatrix #(.inputtype("row"), .matrixcols(32), .matrixrows(30)) dotmatrix_2 (
    .row0(main_1_out_8), .row1(main_1_out_10), .row2(main_1_out_11), .row3(main_1_out_13),
    .row4(main_1_out_14), .row5(main_1_out_15), .row6(main_1_out_16), .row7(main_1_out_17),
    .row8(main_1_out_18), .row9(main_1_out_19), .row10(main_1_out_20), .row11(main_1_out_21),
    .row12(main_1_out_22), .row13(main_1_out_23), .row14(main_1_out_24), .row15(main_1_out_25),
    .row16(main_1_out_26), .row17(main_1_out_27), .row18(main_1_out_28), .row19(main_1_out_29),
    .row20(main_1_out_30), .row21(main_1_out_31), .row22(main_1_out_32), .row23(main_1_out_33),
    .row24(main_1_out_34), .row25(main_1_out_35), .row26(main_1_out_36), .row27(main_1_out_37),
    .row28(main_1_out_38), .row29(main_1_out_39));
  Button button_1 (.out(button_1_out));
  DotMatrix #(.inputtype("row"), .matrixcols(32), .matrixrows(1)) dotmatrix_3 (.row0(main_1_out_40));
  Button button_2 (.out(L));
  Button button_3 (.out(R));
  Button button_4 (.out(Reset));
  Hex_Digit_Display hex_digit_display_1 (.value(main_1_hundred));  // open: dp
  LED led_1 ();  // open: in
  LED led_2 ();  // open: in
  Hex_Digit_Display hex_digit_display_2 (.value(main_1_ai_fails));  // open: dp
  Hex_Digit_Display hex_digit_display_3 (.value(main_1_player_fails));  // open: dp
  Hex_Digit_Display hex_digit_display_4 (.value(main_1_one));  // open: dp
  Hex_Digit_Display hex_digit_display_5 (.value(main_1_ten));  // open: dp
  TTY #(.rows(7), .cols(22), .trigger("falling")) tty_1 (
    .data(main_1_i_o_data_read), .clk(main_1_cdm8_clk), .we(main_1_f1_write));  // open: clr
  TTY #(.rows(1), .cols(22)) tty_2 (
    .data(keyboard_1_data), .clk(main_1_cdm8_clk), .we(main_1_is_valid), .clr(main_1_clear_name_screen));
  Keyboard keyboard_1 (
    .clk(main_1_cdm8_clk), .re(main_1_kbd_enable), .clr(main_1_clear_kbd), .avail(keyboard_1_avail),
    .data(keyboard_1_data));

  // Notes on the sheet:
  //   PLAYER
  //   AI
  //   PLAYER_SCORE
endmodule

module main (
  input  btn_left,
  input  btn_right,
  input  btn_reset,
  input  [6:0] kbd_data,
  input  kbd_is_ready,
  input  btn_input_name,
  output [31:0] out_7,
  output [31:0] out_8,
  output [3:0] player_fails,
  output [31:0] out_10,
  output [31:0] out_11,
  output [3:0] ai_fails,
  output [31:0] out_13,
  output [31:0] out_14,
  output [31:0] out_15,
  output [31:0] out_16,
  output [31:0] out_17,
  output [31:0] out_18,
  output [31:0] out_19,
  output [31:0] out_20,
  output [31:0] out_21,
  output [31:0] out_22,
  output [31:0] out_23,
  output [31:0] out_24,
  output [31:0] out_25,
  output [31:0] out_26,
  output [31:0] out_27,
  output [31:0] out_28,
  output [31:0] out_29,
  output [31:0] out_30,
  output [31:0] out_31,
  output [31:0] out_32,
  output [31:0] out_33,
  output [31:0] out_34,
  output [31:0] out_35,
  output [31:0] out_36,
  output [31:0] out_37,
  output [31:0] out_38,
  output [31:0] out_39,
  output [31:0] out_40,
  output [3:0] hundred,
  output [3:0] ten,
  output [3:0] one,
  output cdm8_clk,
  output clear_name_screen,
  output clear_kbd,
  output [6:0] I_O_data_read,
  output f1_write,
  output is_valid,
  output kbd_enable
);

  wire and_2_out, and_4_out, and_5_out, and_6_out, and_7_out, and_8_out, and_9_out, and_11_out, and_12_out,
       and_13_out, and_14_out, and_16_out, arbiter_1_iack_2, arbiter_1_vec, buff_sel,
       cdm_8_mark5_1_data_inst, code, comparator_1_eq, comparator_2_eq, comparator_3_eq, comparator_4_eq,
       comparator_5_eq, comparator_6_eq, comparator_7_eq, comparator_8_eq, comparator_9_eq, comparator_10_eq,
       comparator_11_eq, counter_1_carry, counter_2_carry, counter_3_carry, d_ff_4_q, data, dX, dY,
       dy_1_hit_any, EVENT_HIT_AI_hit_x, EVENT_HIT_AI_hit_x_1, EVENT_HIT_AI_hit_x_1_2, EVENT_HIT_AI_hit_x_2,
       EVENT_HIT_AI_hit_x_2_2, EVENT_HIT_PLAYER_hit_x, EVENT_HIT_PLAYER_hit_x_1, EVENT_HIT_PLAYER_hit_x_1_2,
       EVENT_HIT_PLAYER_hit_x_2, EVENT_HIT_PLAYER_hit_x_2_2, freeze, game_active, game_clk, hit_ai,
       hit_player, I_O_sel, IAck, init_table, input_enable, interrupt_start, IRQ, is_valid_t, kbd_sel, mem,
       multiplexer_3_out, name_is_valid, not_1_out, not_2_out, not_3_out, not_4_out, or_5_out, or_6_out,
       player_loser, RAM, rd_wr, set_name;
  wire [0:0] d_ff_2_q;
  wire [1:0] priority_encoder_1_out;
  wire [2:0] vec;
  wire [3:0] counter_2_q, counter_3_q, I_O_addr;
  wire [4:0] AI_ai_x, AI_ai_x_1, AI_ai_x_1_2, ball_x, ball_y, player_1_player_x_1, player_1_player_x_1_2,
       player_x, slope_x, slope_y;
  wire [5:0] counter_1_q;
  wire [7:0] bit_extender_5_out, bit_extender_6_out, bit_extender_7_out, bit_extender_9_out, buff_addr,
       buff_data, cdm_8_mark5_1_data_out, cdm_8_mark5_1_pc, cdm_8_mark5_1_ps, cdm_8_mark5_1_r0,
       cdm_8_mark5_1_r1, cdm_8_mark5_1_r2, cdm_8_mark5_1_r3, cdm_8_mark5_1_sp, controlled_buffer_2_out,
       divider_1_out, divider_1_rem, divider_2_out, divider_2_rem, game_speed, I_O_data_read_t, init_addr,
       init_data, kbd_addr, kbd_data_t, multiplexer_1_out, multiplexer_2_out, player_score, register_1_q;
  wire [7:4] cdm_8_mark5_1_addr;
  wire [31:0] AI_ai_screen_pixel, ball_1_out_10, ball_1_out_41, player_1_player_screen_pixel;

  clock_frequency_divider CLOCK (.game_speed(game_speed), .game_clk(game_clk), .cdm8_clk(cdm8_clk));
  ai AI (
    .game_clk(game_clk), .game_active(game_active), .ball_x(ball_x), .ball_y(ball_y), .ball_dx(dX),
    .ball_dy(dY), .player_x(player_x), .ai_screen_pixel(AI_ai_screen_pixel), .ai_x(AI_ai_x),
    .ai_x_1(AI_ai_x_1), .ai_x_1_2(AI_ai_x_1_2));
  ball ball_1 (
    .dX(dX), .dY(dY), .game_active(game_active), .game_clk(game_clk), .ball_x(ball_x), .out_18(out_17),
    .out_19(out_18), .out_20(out_19), .out_21(out_20), .out_22(out_21), .out_23(out_22), .out_24(out_23),
    .out_25(out_24), .ball_y(ball_y), .slope_x(slope_x), .slope_y(slope_y), .out_26(out_25), .out_27(out_26),
    .out_28(out_27), .out_29(out_28), .out_30(out_29), .out_31(out_30), .out_32(out_31), .out_33(out_32),
    .out_34(out_33), .out_35(out_34), .out_36(out_35), .out_37(out_36), .out_38(out_37), .out_39(out_38),
    .out_40(out_39), .out_41(ball_1_out_41), .out_10(ball_1_out_10), .out_11(out_8), .out_12(out_10),
    .out_13(out_11), .out_14(out_13), .out_15(out_14), .out_16(out_15), .out_17(out_16), .freeze(freeze),
    .player_x(player_x));
  player player_1 (
    .btn_left(btn_left), .btn_right(btn_right), .game_active(game_active), .game_clk(game_clk),
    .player_screen_pixel(player_1_player_screen_pixel), .player_x(player_x),
    .player_x_1(player_1_player_x_1), .player_x_1_2(player_1_player_x_1_2));
  // Probe on cdm_8_mark5_1_r2
  // Probe on cdm_8_mark5_1_r1
  // Probe on cdm_8_mark5_1_r0
  // Probe on cdm_8_mark5_1_r3
  // Probe on cdm_8_mark5_1_ps
  // Probe on cdm_8_mark5_1_sp
  // Probe on cdm_8_mark5_1_pc
  collision_check EVENT_HIT_AI (
    .player_x(AI_ai_x), .player_x_1(AI_ai_x_1), .player_x_1_2(AI_ai_x_1_2), .ball_x(ball_x), .ball_y(ball_y),
    .coordinate_to_check(5'b00001), .hit_x(EVENT_HIT_AI_hit_x), .hit_x_1(EVENT_HIT_AI_hit_x_1),
    .hit_x_1_2(EVENT_HIT_AI_hit_x_1_2), .hit_x_2(EVENT_HIT_AI_hit_x_2), .hit_x_2_2(EVENT_HIT_AI_hit_x_2_2));
  assign out_7 = AI_ai_screen_pixel | ball_1_out_10;  // OR_Gate or_1, 32 bits wide
  assign out_40 = ball_1_out_41 | player_1_player_screen_pixel;  // OR_Gate or_2, 32 bits wide
  collision_check EVENT_HIT_PLAYER (
    .player_x(player_x), .player_x_1(player_1_player_x_1), .player_x_1_2(player_1_player_x_1_2),
    .ball_x(ball_x), .ball_y(ball_y), .coordinate_to_check(5'b11110), .hit_x(EVENT_HIT_PLAYER_hit_x),
    .hit_x_1(EVENT_HIT_PLAYER_hit_x_1), .hit_x_1_2(EVENT_HIT_PLAYER_hit_x_1_2),
    .hit_x_2(EVENT_HIT_PLAYER_hit_x_2), .hit_x_2_2(EVENT_HIT_PLAYER_hit_x_2_2));
  Decoder decoder_1 (.out0(code), .out1(data), .sel(cdm_8_mark5_1_data_inst), .en(mem));
  Pull_Resistor pull_resistor_1 (.node(data));
  Pull_Resistor pull_resistor_2 (.node(code));
  CdM_8_mark5 cdm_8_mark5_1 (
    .clock(cdm8_clk), .addr({cdm_8_mark5_1_addr, I_O_addr}), .mem_read(rd_wr), .mem_cycle(mem),
    .data_inst(cdm_8_mark5_1_data_inst), .data_out(cdm_8_mark5_1_data_out),
    .data_in(controlled_buffer_2_out), .r0(cdm_8_mark5_1_r0), .r1(cdm_8_mark5_1_r1), .r2(cdm_8_mark5_1_r2),
    .r3(cdm_8_mark5_1_r3), .PC(cdm_8_mark5_1_pc), .SP(cdm_8_mark5_1_sp), .PS(cdm_8_mark5_1_ps), .IAck(IAck),
    .IRQ(IRQ), .vec(vec));
  assign I_O_data_read_t = not_1_out ? cdm_8_mark5_1_data_out : 8'bz;  // Controlled_Buffer controlled_buffer_1
  not not_1 (not_1_out, rd_wr);
  assign controlled_buffer_2_out = rd_wr ? I_O_data_read_t : 8'bz;  // Controlled_Buffer controlled_buffer_2
  or or_3 (hit_ai, EVENT_HIT_AI_hit_x, EVENT_HIT_AI_hit_x_1, EVENT_HIT_AI_hit_x_1_2, EVENT_HIT_AI_hit_x_2, EVENT_HIT_AI_hit_x_2_2);
  Multiplexer #(.select(2), .width(8), .enable("false")) multiplexer_1 (
    .in0({cdm_8_mark5_1_addr, I_O_addr}), .in1(init_addr), .in2(buff_addr), .out(multiplexer_1_out),
    .sel(priority_encoder_1_out));  // open: in3
  Priority_Encoder #(.select(2)) priority_encoder_1 (
    .in0(1'b1), .in1(init_table), .in2(set_name), .out(priority_encoder_1_out));  // open: in3, gs, en_out, en_in
  or or_4 (hit_player, EVENT_HIT_PLAYER_hit_x, EVENT_HIT_PLAYER_hit_x_1, EVENT_HIT_PLAYER_hit_x_1_2, EVENT_HIT_PLAYER_hit_x_2, EVENT_HIT_PLAYER_hit_x_2_2);
  freeze u_FREEZE (
    .game_clk(game_clk), .hit_x(EVENT_HIT_PLAYER_hit_x), .hit_x_1(EVENT_HIT_PLAYER_hit_x_1),
    .hit_x_1_2(EVENT_HIT_PLAYER_hit_x_1_2), .btn_left(btn_left), .btn_right(btn_right), .freeze(freeze));
  dX dx_1 (
    .game_clk(game_clk), .hit_ai_x(EVENT_HIT_AI_hit_x), .hit_ai_x_1(EVENT_HIT_AI_hit_x_1),
    .hit_ai_x_1_2(EVENT_HIT_AI_hit_x_1_2), .hit_ai_x_2(EVENT_HIT_AI_hit_x_2),
    .hit_ai_x_2_2(EVENT_HIT_AI_hit_x_2_2), .hit_player_x(EVENT_HIT_PLAYER_hit_x),
    .hit_player_x_1(EVENT_HIT_PLAYER_hit_x_1), .hit_player_x_1_2(EVENT_HIT_PLAYER_hit_x_1_2),
    .hit_player_x_2(EVENT_HIT_PLAYER_hit_x_2), .hit_player_x_2_2(EVENT_HIT_PLAYER_hit_x_2_2),
    .btn_left(btn_left), .btn_right(btn_right), .freeze(freeze), .ball_x(ball_x), .dX(dX));
  dY dy_1 (.hit_ai(hit_ai), .hit_player(hit_player), .game_active(game_active), .hit_any(dy_1_hit_any), .dY(dY));
  game_active game_active_1 (
    .ball_y(ball_y), .btn_left(btn_left), .btn_right(btn_right), .btn_reset(btn_reset), .game_clk(game_clk),
    .name_is_valid(name_is_valid), .player_fails(player_fails), .ai_fails(ai_fails),
    .player_loser(player_loser), .game_active(game_active), .interrupt_start(interrupt_start));
  player_score_game_speed player_score_game_speed_1 (
    .hit_player(hit_player), .f1_wrtie(f1_write), .game_clk(game_clk), .game_speed(game_speed),
    .player_score(player_score), .btn_reset(btn_reset));
  Divider divider_1 (.a(player_score), .b(8'h64), .out(divider_1_out), .rem(divider_1_rem));  // open: upper
  Multiplexer #(.select(2), .width(8), .enable("false")) multiplexer_2 (
    .in0(I_O_data_read_t), .in1(init_data), .in2(buff_data), .out(multiplexer_2_out),
    .sel(priority_encoder_1_out));  // open: in3
  Bit_Extender #(.out_width(4)) bit_extender_1 (.in(divider_1_out), .out(hundred));
  Bit_Extender #(.out_width(4)) bit_extender_2 (.in(divider_2_out), .out(ten));
  Divider divider_2 (.a(divider_1_rem), .b(8'ha), .out(divider_2_out), .rem(divider_2_rem));  // open: upper
  Bresenham BRESENHAM (
    .hit_ai_x_1(EVENT_HIT_AI_hit_x_1), .hit_ai_x_1_2(EVENT_HIT_AI_hit_x_1_2),
    .hit_ai_x_2(EVENT_HIT_AI_hit_x_2), .hit_ai_x_2_2(EVENT_HIT_AI_hit_x_2_2),
    .hit_player_x_1(EVENT_HIT_PLAYER_hit_x_1), .hit_player_x_1_2(EVENT_HIT_PLAYER_hit_x_1_2),
    .hit_player_x_2(EVENT_HIT_PLAYER_hit_x_2), .hit_player_x_2_2(EVENT_HIT_PLAYER_hit_x_2_2),
    .hit_any(dy_1_hit_any), .game_clk(game_clk), .game_active(game_active), .slope_x(slope_x),
    .slope_y(slope_y));
  Bit_Extender #(.out_width(4)) bit_extender_3 (.in(divider_2_rem), .out(one));
  not not_2 (not_2_out, rd_wr);
  or or_5 (or_5_out, not_2_out, init_table);
  Multiplexer #(.select(2), .enable("false")) multiplexer_3 (
    .in0(RAM), .in1(init_table), .in2(buff_sel), .out(multiplexer_3_out), .sel(priority_encoder_1_out));  // open: in3
  and and_1 (I_O_sel, cdm_8_mark5_1_addr[4], cdm_8_mark5_1_addr[5], cdm_8_mark5_1_addr[6], cdm_8_mark5_1_addr[7], data);
  not not_3 (not_3_out, or_5_out);
  Comparator #(.mode("unsigned")) comparator_1 (
    .a(multiplexer_1_out), .b({8{1'b0}}), .eq(comparator_1_eq));  // open: gt, lt
  and and_2 (and_2_out, or_5_out, comparator_1_eq, input_enable);
  and and_3 (RAM, ~I_O_sel, data);  // AND_Gate
  ROM rom_1 (.addr({cdm_8_mark5_1_addr, I_O_addr}), .data(I_O_data_read_t), .sel(code));
  RAM #(.bus("separate")) ram_1 (
    .addr(multiplexer_1_out), .din(multiplexer_2_out), .data(I_O_data_read_t), .str(or_5_out),
    .sel(multiplexer_3_out), .clk(cdm8_clk), .ld(not_3_out));  // open: clr
  Register register_1 (.D(multiplexer_2_out), .en(and_2_out), .Q(register_1_q), .clk(cdm8_clk));  // open: clr
  Comparator #(.mode("unsigned")) comparator_2 (.a(register_1_q), .b({8{1'b0}}), .eq(comparator_2_eq));  // open: gt, lt
  Comparator #(.mode("unsigned")) comparator_3 (.a(register_1_q), .b(8'h20), .eq(comparator_3_eq));  // open: gt, lt
  Comparator #(.mode("unsigned")) comparator_4 (.a(register_1_q), .b(8'h5f), .eq(comparator_4_eq));  // open: gt, lt
  nor nor_1 (name_is_valid, comparator_2_eq, comparator_3_eq, comparator_4_eq);
  Comparator #(.width(4), .mode("unsigned")) comparator_5 (
    .a(I_O_addr), .b(4'b0100), .eq(comparator_5_eq));  // open: gt, lt
  Comparator #(.width(4), .mode("unsigned")) comparator_6 (
    .a(I_O_addr), .b(4'b0001), .eq(comparator_6_eq));  // open: gt, lt
  Comparator #(.width(4), .mode("unsigned")) comparator_7 (
    .a(I_O_addr), .b(4'b0010), .eq(comparator_7_eq));  // open: gt, lt
  Comparator #(.width(4), .mode("unsigned")) comparator_8 (
    .a(I_O_addr), .b(4'b0011), .eq(comparator_8_eq));  // open: gt, lt
  Comparator #(.width(4), .mode("unsigned")) comparator_9 (
    .a(I_O_addr), .b(4'b0101), .eq(comparator_9_eq));  // open: gt, lt
  D_Flip_Flop d_ff_1 (
    .clk(cdm8_clk), .D(1'b1), .Q(init_table), .en(not_4_out), .reset(counter_1_carry));  // open: Qn, preset
  not not_4 (not_4_out, counter_1_carry);
  and and_4 (and_4_out, comparator_5_eq, I_O_sel);
  Bit_Extender #(.out_width(7)) bit_extender_4 (.in(I_O_data_read_t), .out(I_O_data_read));
  and and_5 (and_5_out, comparator_6_eq, I_O_sel);
  LED led_1 (.in(and_5_out));
  and and_6 (and_6_out, I_O_sel, comparator_7_eq);
  and and_7 (and_7_out, I_O_sel, comparator_8_eq);
  and and_8 (and_8_out, I_O_sel, comparator_9_eq);
  and and_9 (and_9_out, ~rd_wr, and_4_out);  // AND_Gate
  and and_10 (f1_write, ~rd_wr, and_5_out);  // AND_Gate
  and and_11 (and_11_out, ~rd_wr, and_6_out);  // AND_Gate
  assign I_O_data_read_t = and_12_out ? player_score : 8'bz;  // Controlled_Buffer controlled_buffer_3
  and and_12 (and_12_out, rd_wr, and_7_out);
  assign bit_extender_5_out = {{7{1'b0}}, init_table};  // Bit_Extender bit_extender_5
  assign I_O_data_read_t = and_13_out ? bit_extender_5_out : 8'bz;  // Controlled_Buffer controlled_buffer_4
  and and_13 (and_13_out, rd_wr, and_8_out);
  assign bit_extender_6_out = {{2{1'b0}}, counter_1_q};  // Bit_Extender bit_extender_6
  Counter #(.width(6), .max('h2c), .ongoal("stay")) counter_1 (
    .count(init_table), .Q(counter_1_q), .carry(counter_1_carry), .clk(cdm8_clk));  // open: load, D, clr
  D_Flip_Flop #(.trigger("falling")) d_ff_2 (
    .clk(cdm8_clk), .D(I_O_data_read_t[0]), .Q(d_ff_2_q[0]), .en(and_11_out));  // open: Qn, preset, reset
  Adder adder_1 (.a(bit_extender_6_out), .b(8'h10), .out(init_addr));  // open: cin, cout
  D_Flip_Flop #(.trigger("falling")) d_ff_3 (
    .clk(cdm8_clk), .D(I_O_data_read_t[0]), .Q(input_enable), .en(and_9_out));  // open: Qn, preset, reset
  assign I_O_data_read_t = and_14_out ? {player_loser, {6{1'b0}}, d_ff_2_q[0]} : 8'bz;  // Controlled_Buffer controlled_buffer_5
  and and_14 (and_14_out, rd_wr, and_6_out);
  ROM rom_2 (.addr(bit_extender_6_out), .data(init_data), .sel(1'b1));
  assign bit_extender_7_out = {{1{1'b0}}, kbd_data};  // Bit_Extender bit_extender_7
  is_valid is_valid_1 (.kbd_symbol(kbd_data), .is_valid(is_valid_t));
  and and_15 (kbd_sel, kbd_is_ready, is_valid_t);
  and and_16 (and_16_out, d_ff_2_q[0], player_loser);
  Comparator #(.mode("unsigned")) comparator_10 (
    .a(bit_extender_7_out), .b(8'h8), .eq(comparator_10_eq));  // open: gt, lt
  assign vec = arbiter_1_vec ? 3'b100 : 3'bz;  // Controlled_Buffer controlled_buffer_6
  Multiplexer #(.width(8), .enable("false")) multiplexer_4 (
    .in0(bit_extender_7_out), .in1({8{1'b0}}), .out(kbd_data_t), .sel(comparator_10_eq));
  Counter #(.width(4), .max('h8), .ongoal("stay"), .trigger("falling")) counter_2 (
    .load(comparator_10_eq), .Q(counter_2_q), .carry(counter_2_carry), .clk(kbd_sel), .clr(clear_kbd));  // open: D, count
  arbiter arbiter_1 (
    .IReq_2(IRQ), .IAck(IAck), .IReq(arbiter_1_iack_2), .IAck_2(arbiter_1_iack_2), .vec(arbiter_1_vec),
    .req(and_16_out), .done(and_12_out), .clock(cdm8_clk));
  and and_17 (clear_name_screen, input_enable, btn_input_name);
  Comparator #(.mode("unsigned")) comparator_11 (
    .a(bit_extender_7_out), .b(8'ha), .eq(comparator_11_eq));  // open: gt, lt
  assign kbd_addr = {{4{1'b0}}, counter_2_q};  // Bit_Extender bit_extender_8
  and and_18 (interrupt_start, IAck, arbiter_1_vec);
  S_R_Flip_Flop s_r_ff_1 (
    .S(clear_name_screen), .clk(cdm8_clk), .R(comparator_11_eq), .Q(set_name), .Qn(clear_kbd),
    .reset(or_6_out));  // open: preset, en
  or or_6 (or_6_out, comparator_11_eq, player_loser, counter_2_carry);
  not not_5 (kbd_enable, clear_kbd);
  D_Flip_Flop d_ff_4 (
    .clk(clear_name_screen), .D(clear_name_screen), .Q(d_ff_4_q), .reset(counter_3_carry));  // open: Qn, preset, en
  Counter #(.width(4), .max('h8), .ongoal("stay")) counter_3 (
    .count(clear_name_screen), .Q(counter_3_q), .carry(counter_3_carry), .clk(cdm8_clk), .clr(clear_kbd));  // open: load, D
  and and_19 (is_valid, kbd_enable, is_valid_t);
  assign bit_extender_9_out = {{4{1'b0}}, counter_3_q};  // Bit_Extender bit_extender_9
  Multiplexer #(.enable("false")) multiplexer_5 (.in0(kbd_sel), .in1(d_ff_4_q), .out(buff_sel), .sel(d_ff_4_q));
  Multiplexer #(.width(8), .enable("false")) multiplexer_6 (
    .in0(kbd_addr), .in1(bit_extender_9_out), .out(buff_addr), .sel(d_ff_4_q));
  Multiplexer #(.width(8), .enable("false")) multiplexer_7 (
    .in0(kbd_data_t), .in1({8{1'b0}}), .out(buff_data), .sel(d_ff_4_q));
  // also tied to GND on the sheet: arbiter_1_iack_2

  // Other names for the same wires on the sheet: I_O_data_write[7:0] = I_O_data_read_t; L = btn_left; R = btn_right;
  //   Reset = btn_reset

  // Notes on the sheet:
  //   PLAYER
  //   GAME_LOGIC
  //   MATRIX
  //   ldi r0, 0xf0
  //   ldi r1, 1
  //   st r0, r1
  //   status = 10000000b  если символ готов 
  //   hit_any
  //   GAME_ACTIVE
  //   PLAYER_SCORE | GAME_SPEED
  //   PLAYER_SCORE_TO_SCREEN
  //   status = 00000001b  если прерывания разрешены 
  //   status = 10000001b  если и символ готов, и прерывания разрешены
  //   Чтобы разрешить прерывания от клавиатуры, программа должна записать 1 в бит 0 регистра 0xf0
  //   instr_mem
  //   data_mem
  //   contents of rom_1 (hex, n*v repeats v):
  //   d0 f5 b1 5 e0 8 ee 2 cd f0 d0 3d d1 10 d2 5 a e0 1e a1 d3 0 a7 8c d3 9 1d 8a ee 10 d1 1 d0 f2 a1 d0
  //   f4 a1 c1 d1 2e c1 d1 80 c1 d9 c5 d5 ee 2f ce d0 0 d1 f4 a4 d0 f3 b1 d0 3d d2 42 72 e0 50 b2 bb 77 ec
  //   4a 8c ee 4e d6 59 ee 50 ee 3d d6 81 d0 1 d1 f4 a4 cf d9 d2 41 bb ad c0 c1 c2 c3 d 8d d0 0 d2 8 a e0
  //   71 b3 a7 8c 8d 8a ee 67 c7 c6 c5 c4 78 e0 7f 9 89 b5 a9 8a ee 75 a3 d7 d0 3d d3 5 f e0 ae b2 c2 ba
  //   c0 c3 d6 b2 c7 c4 d1 f1 d2 20 a6 c6 8e c0 c3 d3 8 f e0 a5 b8 a4 8e 8b ee 9c c7 c4 d2 a a6 8c 8b ee
  //   85 d2 a a6 d7 d1 f1 d0 0 d3 64 7b eb c0 3b e 8c ee b6 d3 30 13 a7 d0 0 d3 a 7b eb d0 3b e 8c ee c6
  //   d3 30 13 a7 d3 30 1b a7 d7 31*0 32
  //   0xf2  -> status register 
  //   0xf3  -> data register 
  //   contents of rom_2 (hex, n*v repeats v):
  //   0 49 72 74 65 67 6f 76 0 0 4e 61 7a 61 72 6f 76 0 0 42 6f 6e 64 61 72 65 76 0 49 76 61 6e 6f 76 0 0
  //   0 50 65 74 72 6f 76
  //   ВВЕСТИ ИМЯ
  //   vec == 4
  //   cleaning
endmodule

module clock_frequency_divider (
  input  [7:0] game_speed,
  output game_clk,
  output cdm8_clk
);

  wire counter_1_carry;

  Clock clock_1 (.out(cdm8_clk));
  Counter #(.ongoal("load")) counter_1 (
    .load(1'b1), .D(game_speed), .count(1'b1), .carry(counter_1_carry), .clk(cdm8_clk));  // open: Q, clr
  T_Flip_Flop t_ff_1 (.clk(counter_1_carry), .T(1'b1), .Q(game_clk), .en(1'b1));  // open: Qn, preset, reset
  LED led_1 (.in(game_clk));
endmodule

module player (
  input  btn_left,
  input  btn_right,
  input  game_clk,
  input  game_active,
  output [31:0] player_screen_pixel,
  output [4:0] player_x,
  output [4:0] player_x_1,
  output [4:0] player_x_1_2
);

  wire and_1_out, and_2_out, comparator_1_eq, comparator_2_eq, not_1_out;
  wire [4:0] multiplexer_1_out, multiplexer_2_out, multiplexer_3_out;
  wire [31:0] decoder_1_out0, shifter_1_out, shifter_2_out;

  Multiplexer #(.width(5), .enable("false")) multiplexer_1 (
    .in0(multiplexer_3_out), .in1(5'b01111), .out(multiplexer_1_out), .sel(not_1_out));
  not not_1 (not_1_out, game_active);
  Register #(.width(5), .trigger("falling")) X (.D(multiplexer_1_out), .Q(player_x), .clk(game_clk));  // open: en, clr
  Decoder #(.select(5), .enable("false")) decoder_1 (
    .out0(decoder_1_out0[0]), .out1(decoder_1_out0[1]), .out2(decoder_1_out0[2]), .out3(decoder_1_out0[3]),
    .out4(decoder_1_out0[4]), .out5(decoder_1_out0[5]), .out6(decoder_1_out0[6]), .out7(decoder_1_out0[7]),
    .out8(decoder_1_out0[8]), .out9(decoder_1_out0[9]), .out10(decoder_1_out0[10]),
    .out11(decoder_1_out0[11]), .out12(decoder_1_out0[12]), .out13(decoder_1_out0[13]),
    .out14(decoder_1_out0[14]), .out15(decoder_1_out0[15]), .out16(decoder_1_out0[16]),
    .out17(decoder_1_out0[17]), .out18(decoder_1_out0[18]), .out19(decoder_1_out0[19]),
    .out20(decoder_1_out0[20]), .out21(decoder_1_out0[21]), .out22(decoder_1_out0[22]),
    .out23(decoder_1_out0[23]), .out24(decoder_1_out0[24]), .out25(decoder_1_out0[25]),
    .out26(decoder_1_out0[26]), .out27(decoder_1_out0[27]), .out28(decoder_1_out0[28]),
    .out29(decoder_1_out0[29]), .out30(decoder_1_out0[30]), .out31(decoder_1_out0[31]), .sel(player_x));
  Shifter #(.width(32)) shifter_1 (.in(decoder_1_out0), .\dist (5'b00001), .out(shifter_1_out));
  Shifter #(.width(32), .shift("lr")) shifter_2 (.in(decoder_1_out0), .\dist (5'b00001), .out(shifter_2_out));
  Adder #(.width(5)) adder_1 (.a(player_x), .b(5'b00001), .out(player_x_1));  // open: cin, cout
  Subtractor #(.width(5)) subtractor_1 (.a(player_x), .b(5'b00001), .out(player_x_1_2));  // open: bin, bout
  Comparator #(.width(5), .mode("unsigned")) comparator_1 (
    .a(player_x), .b(5'b11110), .eq(comparator_1_eq));  // open: gt, lt
  Comparator #(.width(5), .mode("unsigned")) comparator_2 (
    .a(player_x), .b(5'b00001), .eq(comparator_2_eq));  // open: gt, lt
  assign player_screen_pixel = shifter_1_out | decoder_1_out0 | shifter_2_out;  // OR_Gate or_1, 32 bits wide
  Multiplexer #(.width(5), .enable("false")) multiplexer_2 (
    .in0(player_x), .in1(player_x_1), .out(multiplexer_2_out), .sel(and_1_out));
  and and_1 (and_1_out, btn_left, ~comparator_1_eq);  // AND_Gate
  and and_2 (and_2_out, btn_right, ~comparator_2_eq);  // AND_Gate
  Multiplexer #(.width(5), .enable("false")) multiplexer_3 (
    .in0(multiplexer_2_out), .in1(player_x_1_2), .out(multiplexer_3_out), .sel(and_2_out));
endmodule

module ai (
  input  [4:0] ball_x,
  input  [4:0] ball_y,
  input  ball_dx,
  input  ball_dy,
  input  [4:0] player_x,
  input  game_clk,
  input  game_active,
  output [31:0] ai_screen_pixel,
  output [4:0] ai_x,
  output [4:0] ai_x_1,
  output [4:0] ai_x_1_2
);

  wire and_1_out, and_2_out, btn_left, btn_right, comparator_1_eq, comparator_2_eq, comparator_4_gt,
       comparator_5_lt, not_1_out;
  wire [4:0] adder_3_out, bit_extender_3_out, multiplexer_2_out, multiplexer_5_out, multiplexer_6_out,
       multiplexer_7_out, multiplexer_8_out, subtractor_5_out;
  wire [7:0] adder_1_out, bit_extender_1_out, bit_extender_2_out, multiplexer_1_out, multiplexer_3_out,
       multiplexer_4_out, subtractor_1_out, subtractor_2_out, subtractor_4_out;
  wire [31:0] decoder_1_out0, shifter_1_out, shifter_2_out;

  assign bit_extender_1_out = {{3{1'b0}}, ball_x};  // Bit_Extender bit_extender_1
  assign bit_extender_2_out = {{3{1'b0}}, ball_y};  // Bit_Extender bit_extender_2
  Adder adder_1 (.a(bit_extender_1_out), .b(bit_extender_2_out), .out(adder_1_out));  // open: cin, cout
  Subtractor subtractor_1 (.a(bit_extender_1_out), .b(bit_extender_2_out), .out(subtractor_1_out));  // open: bin, bout
  not not_1 (not_1_out, game_active);
  Multiplexer #(.width(8), .enable("false")) multiplexer_1 (
    .in0(adder_1_out), .in1(subtractor_1_out), .out(multiplexer_1_out), .sel(ball_dx));
  Multiplexer #(.width(5), .enable("false")) multiplexer_2 (
    .in0(multiplexer_6_out), .in1(5'b01111), .out(multiplexer_2_out), .sel(not_1_out));
  Subtractor subtractor_2 (.a({8{1'b0}}), .b(multiplexer_1_out), .out(subtractor_2_out));  // open: bin, bout
  Decoder #(.select(5), .enable("false")) decoder_1 (
    .out0(decoder_1_out0[0]), .out1(decoder_1_out0[1]), .out2(decoder_1_out0[2]), .out3(decoder_1_out0[3]),
    .out4(decoder_1_out0[4]), .out5(decoder_1_out0[5]), .out6(decoder_1_out0[6]), .out7(decoder_1_out0[7]),
    .out8(decoder_1_out0[8]), .out9(decoder_1_out0[9]), .out10(decoder_1_out0[10]),
    .out11(decoder_1_out0[11]), .out12(decoder_1_out0[12]), .out13(decoder_1_out0[13]),
    .out14(decoder_1_out0[14]), .out15(decoder_1_out0[15]), .out16(decoder_1_out0[16]),
    .out17(decoder_1_out0[17]), .out18(decoder_1_out0[18]), .out19(decoder_1_out0[19]),
    .out20(decoder_1_out0[20]), .out21(decoder_1_out0[21]), .out22(decoder_1_out0[22]),
    .out23(decoder_1_out0[23]), .out24(decoder_1_out0[24]), .out25(decoder_1_out0[25]),
    .out26(decoder_1_out0[26]), .out27(decoder_1_out0[27]), .out28(decoder_1_out0[28]),
    .out29(decoder_1_out0[29]), .out30(decoder_1_out0[30]), .out31(decoder_1_out0[31]), .sel(ai_x));
  Register #(.width(5), .trigger("falling")) register_1 (
    .D(multiplexer_2_out), .Q(ai_x), .clk(game_clk));  // open: en, clr
  Multiplexer #(.width(8), .enable("false")) multiplexer_3 (
    .in0(multiplexer_1_out), .in1(subtractor_2_out), .out(multiplexer_3_out), .sel(multiplexer_1_out[7]));
  Shifter #(.width(32)) shifter_1 (.in(decoder_1_out0), .\dist (5'b00001), .out(shifter_1_out));
  Shifter #(.width(32), .shift("lr")) shifter_2 (.in(decoder_1_out0), .\dist (5'b00001), .out(shifter_2_out));
  Adder #(.width(5)) adder_2 (.a(ai_x), .b(5'b00001), .out(ai_x_1));  // open: cin, cout
  Subtractor #(.width(5)) subtractor_3 (.a(ai_x), .b(5'b00001), .out(ai_x_1_2));  // open: bin, bout
  Comparator #(.width(5), .mode("unsigned")) comparator_1 (
    .a(ai_x), .b(5'b11110), .eq(comparator_1_eq));  // open: gt, lt
  Comparator #(.width(5), .mode("unsigned")) comparator_2 (
    .a(ai_x), .b(5'b00001), .eq(comparator_2_eq));  // open: gt, lt
  Comparator #(.width(5), .mode("unsigned")) comparator_3 (
    .a(multiplexer_8_out), .b(ai_x), .lt(btn_right));  // open: gt, eq
  Multiplexer #(.width(8), .enable("false")) multiplexer_4 (
    .in0(multiplexer_3_out), .in1(subtractor_4_out), .out(multiplexer_4_out), .sel(comparator_4_gt));
  Subtractor subtractor_4 (.a(8'h3e), .b(multiplexer_3_out), .out(subtractor_4_out));  // open: bin, bout
  Comparator #(.mode("unsigned")) comparator_4 (
    .a(multiplexer_3_out), .b(8'h1f), .gt(comparator_4_gt));  // open: eq, lt
  assign ai_screen_pixel = shifter_1_out | decoder_1_out0 | shifter_2_out;  // OR_Gate or_1, 32 bits wide
  Multiplexer #(.width(5), .enable("false")) multiplexer_5 (
    .in0(ai_x), .in1(ai_x_1), .out(multiplexer_5_out), .sel(and_1_out));
  and and_1 (and_1_out, btn_left, ~comparator_1_eq);  // AND_Gate
  and and_2 (and_2_out, btn_right, ~comparator_2_eq);  // AND_Gate
  Bit_Extender #(.out_width(5)) bit_extender_3 (.in(multiplexer_4_out), .out(bit_extender_3_out));
  Multiplexer #(.width(5), .enable("false")) multiplexer_6 (
    .in0(multiplexer_5_out), .in1(ai_x_1_2), .out(multiplexer_6_out), .sel(and_2_out));
  Subtractor #(.width(5)) subtractor_5 (
    .a(bit_extender_3_out), .b(5'b00001), .out(subtractor_5_out));  // open: bin, bout
  Adder #(.width(5)) adder_3 (.a(bit_extender_3_out), .b(5'b00001), .out(adder_3_out));  // open: cin, cout
  Comparator #(.width(5), .mode("unsigned")) comparator_5 (
    .a(bit_extender_3_out), .b(player_x), .lt(comparator_5_lt));  // open: gt, eq
  Comparator #(.width(5), .mode("unsigned")) comparator_6 (
    .a(multiplexer_8_out), .b(ai_x_1), .gt(btn_left));  // open: eq, lt
  Multiplexer #(.width(5), .enable("false")) multiplexer_7 (
    .in0(subtractor_5_out), .in1(adder_3_out), .out(multiplexer_7_out), .sel(comparator_5_lt));
  Multiplexer #(.width(5), .enable("false")) multiplexer_8 (
    .in0(5'b01111), .in1(multiplexer_7_out), .out(multiplexer_8_out), .sel(ball_dy));

  // Notes on the sheet:
  //   Ricochet off the RIGHT wall
  //   Ricochet off the LEFT wall
  //   Pred_X
endmodule

module collision_check (
  input  [4:0] player_x,
  input  [4:0] player_x_1,
  input  [4:0] player_x_1_2,
  input  [4:0] ball_x,
  input  [4:0] ball_y,
  input  [4:0] coordinate_to_check,
  output hit_x,
  output hit_x_1,
  output hit_x_1_2,
  output hit_x_2,
  output hit_x_2_2
);

  wire comparator_1_eq, comparator_2_eq, comparator_3_eq, comparator_4_eq, comparator_5_lt, comparator_6_eq,
       comparator_7_eq, comparator_8_gt;
  wire [4:0] adder_1_out, subtractor_1_out;

  Adder #(.width(5)) adder_1 (.a(player_x), .b(5'b00010), .out(adder_1_out));  // open: cin, cout
  Subtractor #(.width(5)) subtractor_1 (.a(player_x), .b(5'b00010), .out(subtractor_1_out));  // open: bin, bout
  Comparator #(.width(5), .mode("unsigned")) comparator_1 (
    .a(player_x), .b(ball_x), .eq(comparator_1_eq));  // open: gt, lt
  Comparator #(.width(5), .mode("unsigned")) comparator_2 (
    .a(player_x_1), .b(ball_x), .eq(comparator_2_eq));  // open: gt, lt
  Comparator #(.width(5), .mode("unsigned")) comparator_3 (
    .a(player_x_1_2), .b(ball_x), .eq(comparator_3_eq));  // open: gt, lt
  Comparator #(.width(5)) comparator_4 (.a(ball_y), .b(coordinate_to_check), .eq(comparator_4_eq));  // open: gt, lt
  Comparator #(.width(5), .mode("unsigned")) comparator_5 (
    .a(player_x), .b(5'b11110), .lt(comparator_5_lt));  // open: gt, eq
  Comparator #(.width(5), .mode("unsigned")) comparator_6 (
    .a(adder_1_out), .b(ball_x), .eq(comparator_6_eq));  // open: gt, lt
  Comparator #(.width(5), .mode("unsigned")) comparator_7 (
    .a(subtractor_1_out), .b(ball_x), .eq(comparator_7_eq));  // open: gt, lt
  Comparator #(.width(5), .mode("unsigned")) comparator_8 (
    .a(player_x), .b(5'b00001), .gt(comparator_8_gt));  // open: eq, lt
  and and_1 (hit_x, comparator_1_eq, comparator_4_eq);
  and and_2 (hit_x_1, comparator_2_eq, comparator_4_eq);
  and and_3 (hit_x_1_2, comparator_3_eq, comparator_4_eq);
  and and_4 (hit_x_2, comparator_5_lt, comparator_6_eq, comparator_4_eq);
  and and_5 (hit_x_2_2, comparator_7_eq, comparator_4_eq);
endmodule

module ball (
  input  dX,
  input  dY,
  input  [4:0] slope_x,
  input  [4:0] slope_y,
  input  freeze,
  input  [4:0] player_x,
  input  game_clk,
  input  game_active,
  output [4:0] ball_x,
  output [31:0] out_10,
  output [31:0] out_11,
  output [31:0] out_12,
  output [31:0] out_13,
  output [31:0] out_14,
  output [31:0] out_15,
  output [31:0] out_16,
  output [31:0] out_17,
  output [31:0] out_18,
  output [31:0] out_19,
  output [31:0] out_20,
  output [31:0] out_21,
  output [31:0] out_22,
  output [31:0] out_23,
  output [31:0] out_24,
  output [31:0] out_25,
  output [31:0] out_26,
  output [31:0] out_27,
  output [31:0] out_28,
  output [31:0] out_29,
  output [31:0] out_30,
  output [31:0] out_31,
  output [31:0] out_32,
  output [31:0] out_33,
  output [31:0] out_34,
  output [31:0] out_35,
  output [31:0] out_36,
  output [31:0] out_37,
  output [31:0] out_38,
  output [31:0] out_39,
  output [31:0] out_40,
  output [31:0] out_41,
  output [4:0] ball_y
);

  wire adder_1_cout, adder_2_cout, and_1_out, decoder_2_out0, decoder_2_out1, decoder_2_out2, decoder_2_out3,
       decoder_2_out4, decoder_2_out5, decoder_2_out6, decoder_2_out7, decoder_2_out8, decoder_2_out9,
       decoder_2_out10, decoder_2_out11, decoder_2_out12, decoder_2_out13, decoder_2_out14, decoder_2_out15,
       decoder_2_out16, decoder_2_out17, decoder_2_out18, decoder_2_out19, decoder_2_out20, decoder_2_out21,
       decoder_2_out22, decoder_2_out23, decoder_2_out24, decoder_2_out25, decoder_2_out26, decoder_2_out27,
       decoder_2_out28, decoder_2_out29, decoder_2_out30, decoder_2_out31, not_1_out, not_2_out, or_1_out,
       or_2_out;
  wire [4:0] adder_1_out, adder_2_out, adder_3_out, adder_4_out, Error_Reg_X_q, Error_Reg_Y_q,
       multiplexer_1_out, multiplexer_2_out, multiplexer_3_out, multiplexer_4_out, multiplexer_5_out,
       subtractor_1_out, subtractor_2_out;
  wire [31:0] decoder_1_out0;

  not not_1 (not_1_out, game_active);
  not not_2 (not_2_out, game_active);
  Register #(.width(5)) Error_Reg_X (.D(adder_1_out), .Q(Error_Reg_X_q), .clk(game_clk), .clr(not_1_out));  // open: en
  Register #(.width(5)) Error_Reg_Y (.D(adder_2_out), .Q(Error_Reg_Y_q), .clk(game_clk), .clr(not_2_out));  // open: en
  Multiplexer #(.width(5), .enable("false")) multiplexer_1 (
    .in0(multiplexer_4_out), .in1(5'b01111), .out(multiplexer_1_out), .sel(not_1_out));
  or or_1 (or_1_out, not_1_out, adder_1_cout);
  Adder #(.width(5)) adder_1 (.a(Error_Reg_X_q), .b(slope_x), .out(adder_1_out), .cout(adder_1_cout));  // open: cin
  Multiplexer #(.width(5), .enable("false")) multiplexer_2 (
    .in0(multiplexer_5_out), .in1(5'b01111), .out(multiplexer_2_out), .sel(not_2_out));
  or or_2 (or_2_out, not_2_out, adder_2_cout);
  Adder #(.width(5)) adder_2 (.a(Error_Reg_Y_q), .b(slope_y), .out(adder_2_out), .cout(adder_2_cout));  // open: cin
  Multiplexer #(.width(5), .enable("false")) multiplexer_3 (
    .in0(multiplexer_1_out), .in1(player_x), .out(multiplexer_3_out), .sel(freeze));
  and and_1 (and_1_out, or_2_out, ~freeze);  // AND_Gate
  Register #(.width(5)) X (.D(multiplexer_3_out), .en(or_1_out), .Q(ball_x), .clk(game_clk));  // open: clr
  Register #(.width(5)) Y (.D(multiplexer_2_out), .en(and_1_out), .Q(ball_y), .clk(game_clk));  // open: clr
  Adder #(.width(5)) adder_3 (.a(ball_x), .b(5'b00001), .out(adder_3_out));  // open: cin, cout
  Subtractor #(.width(5)) subtractor_1 (.a(ball_x), .b(5'b00001), .out(subtractor_1_out));  // open: bin, bout
  Adder #(.width(5)) adder_4 (.a(ball_y), .b(5'b00001), .out(adder_4_out));  // open: cin, cout
  Subtractor #(.width(5)) subtractor_2 (.a(ball_y), .b(5'b00001), .out(subtractor_2_out));  // open: bin, bout
  Multiplexer #(.width(5), .enable("false")) multiplexer_4 (
    .in0(adder_3_out), .in1(subtractor_1_out), .out(multiplexer_4_out), .sel(dX));
  Multiplexer #(.width(5), .enable("false")) multiplexer_5 (
    .in0(adder_4_out), .in1(subtractor_2_out), .out(multiplexer_5_out), .sel(dY));
  Decoder #(.select(5), .enable("false")) decoder_1 (
    .out0(decoder_1_out0[0]), .out1(decoder_1_out0[1]), .out2(decoder_1_out0[2]), .out3(decoder_1_out0[3]),
    .out4(decoder_1_out0[4]), .out5(decoder_1_out0[5]), .out6(decoder_1_out0[6]), .out7(decoder_1_out0[7]),
    .out8(decoder_1_out0[8]), .out9(decoder_1_out0[9]), .out10(decoder_1_out0[10]),
    .out11(decoder_1_out0[11]), .out12(decoder_1_out0[12]), .out13(decoder_1_out0[13]),
    .out14(decoder_1_out0[14]), .out15(decoder_1_out0[15]), .out16(decoder_1_out0[16]),
    .out17(decoder_1_out0[17]), .out18(decoder_1_out0[18]), .out19(decoder_1_out0[19]),
    .out20(decoder_1_out0[20]), .out21(decoder_1_out0[21]), .out22(decoder_1_out0[22]),
    .out23(decoder_1_out0[23]), .out24(decoder_1_out0[24]), .out25(decoder_1_out0[25]),
    .out26(decoder_1_out0[26]), .out27(decoder_1_out0[27]), .out28(decoder_1_out0[28]),
    .out29(decoder_1_out0[29]), .out30(decoder_1_out0[30]), .out31(decoder_1_out0[31]), .sel(ball_x));
  Decoder #(.select(5), .enable("false")) decoder_2 (
    .out0(decoder_2_out0), .out1(decoder_2_out1), .out2(decoder_2_out2), .out3(decoder_2_out3),
    .out4(decoder_2_out4), .out5(decoder_2_out5), .out6(decoder_2_out6), .out7(decoder_2_out7),
    .out8(decoder_2_out8), .out9(decoder_2_out9), .out10(decoder_2_out10), .out11(decoder_2_out11),
    .out12(decoder_2_out12), .out13(decoder_2_out13), .out14(decoder_2_out14), .out15(decoder_2_out15),
    .out16(decoder_2_out16), .out17(decoder_2_out17), .out18(decoder_2_out18), .out19(decoder_2_out19),
    .out20(decoder_2_out20), .out21(decoder_2_out21), .out22(decoder_2_out22), .out23(decoder_2_out23),
    .out24(decoder_2_out24), .out25(decoder_2_out25), .out26(decoder_2_out26), .out27(decoder_2_out27),
    .out28(decoder_2_out28), .out29(decoder_2_out29), .out30(decoder_2_out30), .out31(decoder_2_out31),
    .sel(ball_y));
  assign out_10 = decoder_2_out0 ? decoder_1_out0 : 32'bz;  // Controlled_Buffer controlled_buffer_1
  assign out_11 = decoder_2_out1 ? decoder_1_out0 : 32'bz;  // Controlled_Buffer controlled_buffer_2
  assign out_12 = decoder_2_out2 ? decoder_1_out0 : 32'bz;  // Controlled_Buffer controlled_buffer_3
  assign out_13 = decoder_2_out3 ? decoder_1_out0 : 32'bz;  // Controlled_Buffer controlled_buffer_4
  assign out_14 = decoder_2_out4 ? decoder_1_out0 : 32'bz;  // Controlled_Buffer controlled_buffer_5
  assign out_15 = decoder_2_out5 ? decoder_1_out0 : 32'bz;  // Controlled_Buffer controlled_buffer_6
  assign out_16 = decoder_2_out6 ? decoder_1_out0 : 32'bz;  // Controlled_Buffer controlled_buffer_7
  assign out_17 = decoder_2_out7 ? decoder_1_out0 : 32'bz;  // Controlled_Buffer controlled_buffer_8
  assign out_18 = decoder_2_out8 ? decoder_1_out0 : 32'bz;  // Controlled_Buffer controlled_buffer_9
  assign out_19 = decoder_2_out9 ? decoder_1_out0 : 32'bz;  // Controlled_Buffer controlled_buffer_10
  assign out_20 = decoder_2_out10 ? decoder_1_out0 : 32'bz;  // Controlled_Buffer controlled_buffer_11
  assign out_21 = decoder_2_out11 ? decoder_1_out0 : 32'bz;  // Controlled_Buffer controlled_buffer_12
  assign out_22 = decoder_2_out12 ? decoder_1_out0 : 32'bz;  // Controlled_Buffer controlled_buffer_13
  assign out_23 = decoder_2_out13 ? decoder_1_out0 : 32'bz;  // Controlled_Buffer controlled_buffer_14
  assign out_24 = decoder_2_out14 ? decoder_1_out0 : 32'bz;  // Controlled_Buffer controlled_buffer_15
  assign out_25 = decoder_2_out15 ? decoder_1_out0 : 32'bz;  // Controlled_Buffer controlled_buffer_16
  assign out_26 = decoder_2_out16 ? decoder_1_out0 : 32'bz;  // Controlled_Buffer controlled_buffer_17
  assign out_27 = decoder_2_out17 ? decoder_1_out0 : 32'bz;  // Controlled_Buffer controlled_buffer_18
  assign out_28 = decoder_2_out18 ? decoder_1_out0 : 32'bz;  // Controlled_Buffer controlled_buffer_19
  assign out_29 = decoder_2_out19 ? decoder_1_out0 : 32'bz;  // Controlled_Buffer controlled_buffer_20
  assign out_30 = decoder_2_out20 ? decoder_1_out0 : 32'bz;  // Controlled_Buffer controlled_buffer_21
  assign out_31 = decoder_2_out21 ? decoder_1_out0 : 32'bz;  // Controlled_Buffer controlled_buffer_22
  assign out_32 = decoder_2_out22 ? decoder_1_out0 : 32'bz;  // Controlled_Buffer controlled_buffer_23
  assign out_33 = decoder_2_out23 ? decoder_1_out0 : 32'bz;  // Controlled_Buffer controlled_buffer_24
  assign out_34 = decoder_2_out24 ? decoder_1_out0 : 32'bz;  // Controlled_Buffer controlled_buffer_25
  assign out_35 = decoder_2_out25 ? decoder_1_out0 : 32'bz;  // Controlled_Buffer controlled_buffer_26
  assign out_36 = decoder_2_out26 ? decoder_1_out0 : 32'bz;  // Controlled_Buffer controlled_buffer_27
  assign out_37 = decoder_2_out27 ? decoder_1_out0 : 32'bz;  // Controlled_Buffer controlled_buffer_28
  assign out_38 = decoder_2_out28 ? decoder_1_out0 : 32'bz;  // Controlled_Buffer controlled_buffer_29
  assign out_39 = decoder_2_out29 ? decoder_1_out0 : 32'bz;  // Controlled_Buffer controlled_buffer_30
  assign out_40 = decoder_2_out30 ? decoder_1_out0 : 32'bz;  // Controlled_Buffer controlled_buffer_31
  assign out_41 = decoder_2_out31 ? decoder_1_out0 : 32'bz;  // Controlled_Buffer controlled_buffer_32
  Pull_Resistor pull_resistor_1 (.node(out_40));
  Pull_Resistor pull_resistor_2 (.node(out_38));
  Pull_Resistor pull_resistor_3 (.node(out_36));
  Pull_Resistor pull_resistor_4 (.node(out_39));
  Pull_Resistor pull_resistor_5 (.node(out_41));
  Pull_Resistor pull_resistor_6 (.node(out_34));
  Pull_Resistor pull_resistor_7 (.node(out_37));
  Pull_Resistor pull_resistor_8 (.node(out_35));
  Pull_Resistor pull_resistor_9 (.node(out_27));
  Pull_Resistor pull_resistor_10 (.node(out_26));
  Pull_Resistor pull_resistor_11 (.node(out_28));
  Pull_Resistor pull_resistor_12 (.node(out_32));
  Pull_Resistor pull_resistor_13 (.node(out_33));
  Pull_Resistor pull_resistor_14 (.node(out_29));
  Pull_Resistor pull_resistor_15 (.node(out_31));
  Pull_Resistor pull_resistor_16 (.node(out_30));
  Pull_Resistor pull_resistor_17 (.node(out_20));
  Pull_Resistor pull_resistor_18 (.node(out_21));
  Pull_Resistor pull_resistor_19 (.node(out_25));
  Pull_Resistor pull_resistor_20 (.node(out_19));
  Pull_Resistor pull_resistor_21 (.node(out_18));
  Pull_Resistor pull_resistor_22 (.node(out_22));
  Pull_Resistor pull_resistor_23 (.node(out_24));
  Pull_Resistor pull_resistor_24 (.node(out_23));
  Pull_Resistor pull_resistor_25 (.node(out_10));
  Pull_Resistor pull_resistor_26 (.node(out_11));
  Pull_Resistor pull_resistor_27 (.node(out_16));
  Pull_Resistor pull_resistor_28 (.node(out_14));
  Pull_Resistor pull_resistor_29 (.node(out_12));
  Pull_Resistor pull_resistor_30 (.node(out_15));
  Pull_Resistor pull_resistor_31 (.node(out_17));
  Pull_Resistor pull_resistor_32 (.node(out_13));

  // Other names for the same wires on the sheet: player_y[4:0] = player_x
endmodule

module dX (
  input  hit_ai_x,
  input  hit_ai_x_1,
  input  hit_ai_x_1_2,
  input  hit_ai_x_2,
  input  hit_ai_x_2_2,
  input  hit_player_x,
  input  hit_player_x_1,
  input  hit_player_x_1_2,
  input  hit_player_x_2,
  input  hit_player_x_2_2,
  input  btn_left,
  input  btn_right,
  input  freeze,
  input  [4:0] ball_x,
  input  game_clk,
  output dX
);

  wire and_1_out, and_2_out, comparator_1_eq, comparator_2_eq, d_ff_1_q, not_1_out, or_1_out, or_2_out,
       or_3_out, or_4_out, or_5_out, or_6_out, s_r_ff_1_q, s_r_ff_2_q;
  wire [2:0] priority_encoder_1_out;

  or or_1 (or_1_out, hit_ai_x, hit_player_x);
  or or_2 (or_2_out, hit_ai_x_1, hit_ai_x_2, hit_player_x_1, hit_player_x_2);
  or or_3 (or_3_out, hit_ai_x_1_2, hit_ai_x_2_2, hit_player_x_1_2, hit_player_x_2_2);
  or or_4 (or_4_out, or_2_out, or_3_out);
  and and_1 (and_1_out, btn_left, freeze);
  not not_1 (not_1_out, freeze);
  and and_2 (and_2_out, freeze, btn_right);
  S_R_Flip_Flop #(.trigger("falling")) s_r_ff_1 (
    .S(and_1_out), .clk(game_clk), .R(not_1_out), .Q(s_r_ff_1_q));  // open: Qn, preset, reset, en
  S_R_Flip_Flop #(.trigger("falling")) s_r_ff_2 (
    .S(and_2_out), .clk(game_clk), .R(not_1_out), .Q(s_r_ff_2_q));  // open: Qn, preset, reset, en
  Comparator #(.width(5), .mode("unsigned")) comparator_1 (
    .a(ball_x), .b({5{1'b0}}), .eq(comparator_1_eq));  // open: gt, lt
  or or_5 (or_5_out, comparator_1_eq, comparator_2_eq);
  Comparator #(.width(5), .mode("unsigned")) comparator_2 (
    .a(ball_x), .b({5{1'b1}}), .eq(comparator_2_eq));  // open: gt, lt
  or or_6 (or_6_out, or_1_out, or_4_out, s_r_ff_1_q, s_r_ff_2_q, or_5_out);
  D_Flip_Flop #(.trigger("falling")) d_ff_1 (.clk(or_6_out), .D(dX), .Q(d_ff_1_q));  // open: Qn, preset, en, reset
  Priority_Encoder priority_encoder_1 (
    .in0(1'b1), .in1(or_2_out), .in2(or_3_out), .in3(s_r_ff_1_q), .in4(s_r_ff_2_q), .in5(comparator_2_eq),
    .in6(comparator_1_eq), .out(priority_encoder_1_out));  // open: in7, en_in, gs, en_out
  Multiplexer #(.select(3), .enable("false")) multiplexer_1 (
    .in0(d_ff_1_q), .in1(1'b0), .in2(1'b1), .in3(1'b0), .in4(1'b1), .in5(1'b1), .in6(1'b0), .out(dX),
    .sel(priority_encoder_1_out));  // open: in7

  // Notes on the sheet:
  //   right_hit_any
  //   center_hit_any
  //   left_hit_any
  //   EVENT_HIT_RIGHT_WALL
  //   EVENT_HIT_LEFT_WALL
endmodule

module dY (
  input  hit_ai,
  input  hit_player,
  input  game_active,
  output hit_any,
  output dY
);

  wire d_ff_1_q, not_1_out;

  or or_1 (hit_any, hit_ai, hit_player);
  D_Flip_Flop #(.trigger("falling")) d_ff_1 (
    .clk(hit_any), .D(dY), .Q(d_ff_1_q), .en(game_active), .reset(not_1_out));  // open: Qn, preset
  not not_1 (not_1_out, game_active);
  Multiplexer #(.select(2), .enable("false")) multiplexer_1 (
    .in0(d_ff_1_q), .in1(1'b0), .in2(1'b1), .in3(1'b0), .out(dY), .sel({hit_player, hit_ai}));
endmodule

module Bresenham (
  input  hit_ai_x_1,
  input  hit_ai_x_1_2,
  input  hit_ai_x_2,
  input  hit_ai_x_2_2,
  input  hit_player_x_1,
  input  hit_player_x_1_2,
  input  hit_player_x_2,
  input  hit_player_x_2_2,
  input  hit_any,
  input  game_clk,
  input  game_active,
  output [4:0] slope_x,
  output [4:0] slope_y
);

  wire not_1_out;
  wire [1:0] Angle_Reg_q, or_1_out;

  or or_1 (or_1_out[0], hit_ai_x_1, hit_ai_x_1_2, hit_player_x_1, hit_player_x_1_2);
  or or_2 (or_1_out[1], hit_ai_x_2, hit_ai_x_2_2, hit_player_x_2, hit_player_x_2_2);
  Register #(.width(2)) Angle_Reg (.D(or_1_out), .en(hit_any), .Q(Angle_Reg_q), .clk(game_clk), .clr(not_1_out));
  not not_1 (not_1_out, game_active);
  Multiplexer #(.select(2), .width(5), .enable("false")) multiplexer_1 (
    .in0(5'b01000), .in1(5'b10000), .in2({5{1'b1}}), .out(slope_x), .sel(Angle_Reg_q));  // open: in3
  Multiplexer #(.select(2), .width(5), .enable("false")) multiplexer_2 (
    .in0({5{1'b1}}), .in1(5'b10000), .in2(5'b01000), .out(slope_y), .sel(Angle_Reg_q));  // open: in3

  // Notes on the sheet:
  //   border_hit
  //   corner_hit
endmodule

module freeze (
  input  game_clk,
  input  hit_x,
  input  hit_x_1,
  input  hit_x_1_2,
  input  btn_left,
  input  btn_right,
  output freeze
);

  wire and_1_out, and_2_out, d_ff_1_qn, or_1_out, or_2_out, shift_register_1_q0, shift_register_1_q1,
       shift_register_1_q2, shift_register_1_q3, shift_register_1_q4, shift_register_1_q5,
       shift_register_1_q6, shift_register_1_q7;

  or or_1 (or_1_out, hit_x, hit_x_1, hit_x_1_2);
  and and_1 (and_1_out, or_1_out, or_2_out);
  or or_2 (or_2_out, btn_left, btn_right);
  D_Flip_Flop #(.trigger("falling")) d_ff_1 (
    .clk(game_clk), .D(and_1_out), .Qn(d_ff_1_qn));  // open: Q, preset, en, reset
  and and_2 (and_2_out, d_ff_1_qn, and_1_out);
  Shift_Register #(.trigger("falling")) shift_register_1 (
    .shift(1'b1), .in(and_2_out), .clk(game_clk), .q0(shift_register_1_q0), .q1(shift_register_1_q1),
    .q2(shift_register_1_q2), .q3(shift_register_1_q3), .q4(shift_register_1_q4), .q5(shift_register_1_q5),
    .q6(shift_register_1_q6), .q7(shift_register_1_q7));  // open: out, load, clr, d0, d1, d2, d3, d4, d5, d6, d7
  or or_3 (freeze, shift_register_1_q7, shift_register_1_q6, shift_register_1_q5, shift_register_1_q4, shift_register_1_q3, shift_register_1_q2, shift_register_1_q1, shift_register_1_q0);
endmodule

module is_valid (
  input  [6:0] kbd_symbol,
  output is_valid
);

  wire and_1_out, and_2_out, comparator_1_eq, comparator_2_eq, comparator_3_eq, comparator_4_gt,
       comparator_5_lt, comparator_6_gt, comparator_7_lt;

  Comparator #(.width(7), .mode("unsigned")) comparator_1 (
    .a(kbd_symbol), .b(7'b0100000), .eq(comparator_1_eq));  // open: gt, lt
  Comparator #(.width(7), .mode("unsigned")) comparator_2 (
    .a(kbd_symbol), .b(7'b1011111), .eq(comparator_2_eq));  // open: gt, lt
  Comparator #(.width(7), .mode("unsigned")) comparator_3 (
    .a(kbd_symbol), .b(7'b0001000), .eq(comparator_3_eq));  // open: gt, lt
  Comparator #(.width(7), .mode("unsigned")) comparator_4 (
    .a(kbd_symbol), .b(7'b1000000), .gt(comparator_4_gt));  // open: eq, lt
  Comparator #(.width(7), .mode("unsigned")) comparator_5 (
    .a(kbd_symbol), .b(7'b1011011), .lt(comparator_5_lt));  // open: gt, eq
  Comparator #(.width(7), .mode("unsigned")) comparator_6 (
    .a(kbd_symbol), .b(7'b1100000), .gt(comparator_6_gt));  // open: eq, lt
  Comparator #(.width(7), .mode("unsigned")) comparator_7 (
    .a(kbd_symbol), .b(7'b1111011), .lt(comparator_7_lt));  // open: gt, eq
  and and_1 (and_1_out, comparator_4_gt, comparator_5_lt);
  and and_2 (and_2_out, comparator_6_gt, comparator_7_lt);
  or or_1 (is_valid, comparator_1_eq, comparator_2_eq, comparator_3_eq, and_1_out, and_2_out);

  // Notes on the sheet:
  //   Пробел
  //   Нижнее подчеркивание
  //   Стереть
  //   A-Z
  //   a-z
endmodule

module game_active (
  input  [4:0] ball_y,
  input  btn_left,
  input  btn_right,
  input  btn_reset,
  input  interrupt_start,
  input  name_is_valid,
  input  game_clk,
  output [3:0] player_fails,
  output [3:0] ai_fails,
  output player_loser,
  output game_active
);

  wire and_1_out, comparator_1_eq, comparator_2_eq, comparator_3_eq, comparator_4_eq, not_1_out, not_2_out,
       or_1_out, or_2_out, or_3_out, or_4_out, or_5_out, xnor_1_out, xnor_2_out;

  Comparator #(.width(5), .mode("unsigned")) comparator_1 (
    .a(ball_y), .b({5{1'b0}}), .eq(comparator_1_eq));  // open: gt, lt
  Comparator #(.width(5), .mode("unsigned")) comparator_2 (
    .a(ball_y), .b({5{1'b1}}), .eq(comparator_2_eq));  // open: gt, lt
  or or_1 (or_1_out, comparator_1_eq, comparator_2_eq);
  not not_1 (not_1_out, btn_left);
  not not_2 (not_2_out, btn_right);
  or or_2 (or_2_out, or_1_out, btn_reset);
  xnor xnor_1 (xnor_1_out, btn_left, not_1_out);
  or or_3 (or_3_out, xnor_1_out, xnor_2_out);
  xnor xnor_2 (xnor_2_out, btn_right, not_2_out);
  and and_1 (and_1_out, name_is_valid, or_3_out);
  S_R_Flip_Flop #(.trigger("high")) s_r_ff_1 (
    .S(and_1_out), .clk(game_clk), .R(or_2_out), .Q(game_active));  // open: Qn, preset, reset, en
  Counter #(.width(4), .max('hf)) counter_1 (
    .Q(player_fails), .clk(comparator_1_eq), .clr(or_5_out));  // open: load, D, count, carry
  Counter #(.width(4), .max('hf)) counter_2 (
    .Q(ai_fails), .clk(comparator_2_eq), .clr(or_5_out));  // open: load, D, count, carry
  Comparator #(.width(4), .mode("unsigned")) comparator_3 (
    .a(player_fails), .b(4'b0101), .eq(comparator_3_eq));  // open: gt, lt
  or or_4 (or_4_out, comparator_3_eq, comparator_4_eq);
  Comparator #(.width(4), .mode("unsigned")) comparator_4 (
    .a(4'b0101), .b(ai_fails), .eq(comparator_4_eq));  // open: gt, lt
  or or_5 (or_5_out, btn_reset, or_4_out);
  D_Flip_Flop d_ff_1 (.clk(or_4_out), .D(or_4_out), .Q(player_loser), .reset(interrupt_start));  // open: Qn, preset, en

  // Other names for the same wires on the sheet: L = btn_left; R = btn_right; Reset = btn_reset

  // Notes on the sheet:
  //   EVENT_HIT_TOP_WALL
  //   EVENT_HIT_BOTTOM_WALL
endmodule

module player_score_game_speed (
  input  hit_player,
  input  f1_wrtie,
  input  btn_reset,
  input  game_clk,
  output [7:0] game_speed,
  output [7:0] player_score
);

  wire and_1_out, counter_2_carry, d_ff_1_qn, not_1_out, or_1_out, s_r_ff_1_q;
  wire [2:0] counter_3_q;

  not not_1 (not_1_out, hit_player);
  S_R_Flip_Flop #(.trigger("falling")) s_r_ff_1 (
    .S(hit_player), .clk(game_clk), .R(not_1_out), .Q(s_r_ff_1_q));  // open: Qn, preset, reset, en
  Counter counter_1 (.Q(player_score), .clk(s_r_ff_1_q), .clr(or_1_out));  // open: load, D, count, carry
  Counter #(.width(4), .max('h5)) counter_2 (
    .carry(counter_2_carry), .clk(s_r_ff_1_q), .clr(or_1_out));  // open: load, D, count, Q
  or or_1 (or_1_out, f1_wrtie, btn_reset);
  D_Flip_Flop #(.trigger("falling")) d_ff_1 (
    .clk(game_clk), .D(counter_2_carry), .Qn(d_ff_1_qn));  // open: Q, preset, en, reset
  and and_1 (and_1_out, d_ff_1_qn, counter_2_carry);
  Counter #(.width(3), .max('h7), .ongoal("stay")) counter_3 (
    .count(and_1_out), .Q(counter_3_q), .clk(game_clk), .clr(or_1_out));  // open: load, D, carry
  Multiplexer #(.select(3), .width(8), .enable("false")) multiplexer_1 (
    .in0(8'h40), .in1(8'h38), .in2(8'h35), .in3(8'h30), .in4(8'h28), .in5(8'h25), .in6(8'h20), .in7(8'h15),
    .out(game_speed), .sel(counter_3_q));
endmodule

module test (
  output [3:0] player_fails,
  output [3:0] ai_fails,
  output [3:0] hundred,
  output [3:0] ten,
  output [3:0] one
);

  wire and_3_out, and_4_out, and_5_out, and_6_out, and_7_out, and_8_out, and_9_out, and_11_out, and_12_out,
       and_13_out, and_14_out, and_15_out, and_17_out, and_18_out, arbiter_1_iack_2, arbiter_1_vec, buff_sel,
       button_4_out, cdm8_clk, cdm_8_mark5_1_data_inst, code, comparator_1_eq, comparator_2_eq,
       comparator_3_eq, comparator_4_eq, comparator_5_eq, comparator_6_eq, comparator_7_eq, comparator_8_eq,
       comparator_9_eq, comparator_10_eq, counter_1_carry, counter_2_carry, counter_3_carry, d_ff_3_q,
       d_ff_4_qn, d_ff_5_q, data, dX, dY, dy_1_hit_any, EVENT_HIT_AI_hit_x, EVENT_HIT_AI_hit_x_1,
       EVENT_HIT_AI_hit_x_1_2, EVENT_HIT_AI_hit_x_2, EVENT_HIT_AI_hit_x_2_2, EVENT_HIT_PLAYER_hit_x,
       EVENT_HIT_PLAYER_hit_x_1, EVENT_HIT_PLAYER_hit_x_1_2, EVENT_HIT_PLAYER_hit_x_2,
       EVENT_HIT_PLAYER_hit_x_2_2, f1_write, freeze, game_active, game_clk, hit_ai, hit_player, I_O_sel,
       IAck, init_table, interrupt_start, IRQ, is_valid, kbd_sel, keyboard_1_avail, L, mem,
       multiplexer_3_out, name, name_is_valid, not_1_out, not_2_out, not_3_out, not_4_out, or_5_out,
       or_6_out, player_loser, R, RAM, rd_wr, Reset;
  wire [0:0] d_ff_2_q;
  wire [1:0] priority_encoder_1_out;
  wire [2:0] vec;
  wire [3:0] counter_2_q, counter_3_q, I_O_addr;
  wire [4:0] AI_ai_x, AI_ai_x_1, AI_ai_x_1_2, ball_x, ball_y, player_1_player_x_1, player_1_player_x_1_2,
       player_x, slope_x, slope_y;
  wire [5:0] counter_1_q;
  wire [6:0] bit_extender_5_out, keyboard_1_data;
  wire [7:0] bit_extender_4_out, bit_extender_6_out, bit_extender_7_out, bit_extender_9_out, buff_addr,
       buff_data, cdm_8_mark5_1_data_out, cdm_8_mark5_1_pc, cdm_8_mark5_1_ps, cdm_8_mark5_1_r0,
       cdm_8_mark5_1_r1, cdm_8_mark5_1_r2, cdm_8_mark5_1_r3, cdm_8_mark5_1_sp, controlled_buffer_2_out,
       divider_1_out, divider_1_rem, divider_2_out, divider_2_rem, game_speed, I_O_data_read, init_addr,
       init_data, kbd_addr, kbd_data, multiplexer_1_out, multiplexer_2_out, player_score, register_1_q;
  wire [7:4] cdm_8_mark5_1_addr;
  wire [31:0] AI_ai_screen_pixel, ball_1_out_10, ball_1_out_11, ball_1_out_12, ball_1_out_13, ball_1_out_14,
       ball_1_out_15, ball_1_out_16, ball_1_out_17, ball_1_out_18, ball_1_out_19, ball_1_out_20,
       ball_1_out_21, ball_1_out_22, ball_1_out_23, ball_1_out_24, ball_1_out_25, ball_1_out_26,
       ball_1_out_27, ball_1_out_28, ball_1_out_29, ball_1_out_30, ball_1_out_31, ball_1_out_32,
       ball_1_out_33, ball_1_out_34, ball_1_out_35, ball_1_out_36, ball_1_out_37, ball_1_out_38,
       ball_1_out_39, ball_1_out_40, ball_1_out_41, or_1_out, or_2_out, player_1_player_screen_pixel;

  // Probe on cdm_8_mark5_1_r3
  // Probe on cdm_8_mark5_1_r2
  // Probe on cdm_8_mark5_1_r1
  // Probe on cdm_8_mark5_1_pc
  // Probe on cdm_8_mark5_1_r0
  clock_frequency_divider CLOCK (.game_speed(game_speed), .game_clk(game_clk), .cdm8_clk(cdm8_clk));
  ai AI (
    .game_clk(game_clk), .game_active(game_active), .ball_x(ball_x), .ball_y(ball_y), .ball_dx(dX),
    .ball_dy(dY), .player_x(player_x), .ai_screen_pixel(AI_ai_screen_pixel), .ai_x(AI_ai_x),
    .ai_x_1(AI_ai_x_1), .ai_x_1_2(AI_ai_x_1_2));
  ball ball_1 (
    .dX(dX), .dY(dY), .game_active(game_active), .game_clk(game_clk), .ball_x(ball_x),
    .out_18(ball_1_out_18), .out_19(ball_1_out_19), .out_20(ball_1_out_20), .out_21(ball_1_out_21),
    .out_22(ball_1_out_22), .out_23(ball_1_out_23), .out_24(ball_1_out_24), .out_25(ball_1_out_25),
    .ball_y(ball_y), .slope_x(slope_x), .slope_y(slope_y), .out_26(ball_1_out_26), .out_27(ball_1_out_27),
    .out_28(ball_1_out_28), .out_29(ball_1_out_29), .out_30(ball_1_out_30), .out_31(ball_1_out_31),
    .out_32(ball_1_out_32), .out_33(ball_1_out_33), .out_34(ball_1_out_34), .out_35(ball_1_out_35),
    .out_36(ball_1_out_36), .out_37(ball_1_out_37), .out_38(ball_1_out_38), .out_39(ball_1_out_39),
    .out_40(ball_1_out_40), .out_41(ball_1_out_41), .out_10(ball_1_out_10), .out_11(ball_1_out_11),
    .out_12(ball_1_out_12), .out_13(ball_1_out_13), .out_14(ball_1_out_14), .out_15(ball_1_out_15),
    .out_16(ball_1_out_16), .out_17(ball_1_out_17), .freeze(freeze), .player_x(player_x));
  player player_1 (
    .btn_left(L), .btn_right(R), .game_active(game_active), .game_clk(game_clk),
    .player_screen_pixel(player_1_player_screen_pixel), .player_x(player_x),
    .player_x_1(player_1_player_x_1), .player_x_1_2(player_1_player_x_1_2));
  // Probe on cdm_8_mark5_1_ps
  Decoder decoder_1 (.out0(code), .out1(data), .sel(cdm_8_mark5_1_data_inst), .en(mem));
  // Probe on cdm_8_mark5_1_sp
  CdM_8_mark5 cdm_8_mark5_1 (
    .clock(cdm8_clk), .addr({cdm_8_mark5_1_addr, I_O_addr}), .mem_read(rd_wr), .mem_cycle(mem),
    .data_inst(cdm_8_mark5_1_data_inst), .data_out(cdm_8_mark5_1_data_out),
    .data_in(controlled_buffer_2_out), .r0(cdm_8_mark5_1_r0), .r1(cdm_8_mark5_1_r1), .r2(cdm_8_mark5_1_r2),
    .r3(cdm_8_mark5_1_r3), .PC(cdm_8_mark5_1_pc), .SP(cdm_8_mark5_1_sp), .PS(cdm_8_mark5_1_ps), .IAck(IAck),
    .IRQ(IRQ), .vec(vec));
  assign I_O_data_read = not_1_out ? cdm_8_mark5_1_data_out : 8'bz;  // Controlled_Buffer controlled_buffer_1
  not not_1 (not_1_out, rd_wr);
  assign controlled_buffer_2_out = rd_wr ? I_O_data_read : 8'bz;  // Controlled_Buffer controlled_buffer_2
  Pull_Resistor pull_resistor_1 (.node(code));
  Pull_Resistor pull_resistor_2 (.node(data));
  collision_check EVENT_HIT_AI (
    .player_x(AI_ai_x), .player_x_1(AI_ai_x_1), .player_x_1_2(AI_ai_x_1_2), .ball_x(ball_x), .ball_y(ball_y),
    .coordinate_to_check(5'b00001), .hit_x(EVENT_HIT_AI_hit_x), .hit_x_1(EVENT_HIT_AI_hit_x_1),
    .hit_x_1_2(EVENT_HIT_AI_hit_x_1_2), .hit_x_2(EVENT_HIT_AI_hit_x_2), .hit_x_2_2(EVENT_HIT_AI_hit_x_2_2));
  assign or_1_out = AI_ai_screen_pixel | ball_1_out_10;  // OR_Gate or_1, 32 bits wide
  DotMatrix #(.inputtype("row"), .matrixcols(32), .matrixrows(1)) dotmatrix_1 (.row0(or_1_out));
  DotMatrix #(.inputtype("row"), .matrixcols(32), .matrixrows(30)) dotmatrix_2 (
    .row0(ball_1_out_11), .row1(ball_1_out_12), .row2(ball_1_out_13), .row3(ball_1_out_14),
    .row4(ball_1_out_15), .row5(ball_1_out_16), .row6(ball_1_out_17), .row7(ball_1_out_18),
    .row8(ball_1_out_19), .row9(ball_1_out_20), .row10(ball_1_out_21), .row11(ball_1_out_22),
    .row12(ball_1_out_23), .row13(ball_1_out_24), .row14(ball_1_out_25), .row15(ball_1_out_26),
    .row16(ball_1_out_27), .row17(ball_1_out_28), .row18(ball_1_out_29), .row19(ball_1_out_30),
    .row20(ball_1_out_31), .row21(ball_1_out_32), .row22(ball_1_out_33), .row23(ball_1_out_34),
    .row24(ball_1_out_35), .row25(ball_1_out_36), .row26(ball_1_out_37), .row27(ball_1_out_38),
    .row28(ball_1_out_39), .row29(ball_1_out_40));
  DotMatrix #(.inputtype("row"), .matrixcols(32), .matrixrows(1)) dotmatrix_3 (.row0(or_2_out));
  assign or_2_out = ball_1_out_41 | player_1_player_screen_pixel;  // OR_Gate or_2, 32 bits wide
  collision_check EVENT_HIT_PLAYER (
    .player_x(player_x), .player_x_1(player_1_player_x_1), .player_x_1_2(player_1_player_x_1_2),
    .ball_x(ball_x), .ball_y(ball_y), .coordinate_to_check(5'b11110), .hit_x(EVENT_HIT_PLAYER_hit_x),
    .hit_x_1(EVENT_HIT_PLAYER_hit_x_1), .hit_x_1_2(EVENT_HIT_PLAYER_hit_x_1_2),
    .hit_x_2(EVENT_HIT_PLAYER_hit_x_2), .hit_x_2_2(EVENT_HIT_PLAYER_hit_x_2_2));
  Priority_Encoder #(.select(2)) priority_encoder_1 (
    .in0(1'b1), .in1(init_table), .in2(name), .out(priority_encoder_1_out));  // open: in3, gs, en_out, en_in
  Multiplexer #(.select(2), .width(8), .enable("false")) multiplexer_1 (
    .in0({cdm_8_mark5_1_addr, I_O_addr}), .in1(init_addr), .in2(buff_addr), .out(multiplexer_1_out),
    .sel(priority_encoder_1_out));  // open: in3
  or or_3 (hit_ai, EVENT_HIT_AI_hit_x, EVENT_HIT_AI_hit_x_1, EVENT_HIT_AI_hit_x_1_2, EVENT_HIT_AI_hit_x_2, EVENT_HIT_AI_hit_x_2_2);
  Button button_1 (.out(R));
  Button button_2 (.out(L));
  Button button_3 (.out(Reset));
  Multiplexer #(.select(2), .width(8), .enable("false")) multiplexer_2 (
    .in0(I_O_data_read), .in1(init_data), .in2(buff_data), .out(multiplexer_2_out),
    .sel(priority_encoder_1_out));  // open: in3
  or or_4 (hit_player, EVENT_HIT_PLAYER_hit_x, EVENT_HIT_PLAYER_hit_x_1, EVENT_HIT_PLAYER_hit_x_1_2, EVENT_HIT_PLAYER_hit_x_2, EVENT_HIT_PLAYER_hit_x_2_2);
  or or_5 (or_5_out, ~rd_wr, init_table);  // OR_Gate
  freeze u_FREEZE (
    .game_clk(game_clk), .hit_x(EVENT_HIT_PLAYER_hit_x), .hit_x_1(EVENT_HIT_PLAYER_hit_x_1),
    .hit_x_1_2(EVENT_HIT_PLAYER_hit_x_1_2), .btn_left(L), .btn_right(R), .freeze(freeze));
  and and_1 (I_O_sel, cdm_8_mark5_1_addr[4], cdm_8_mark5_1_addr[5], cdm_8_mark5_1_addr[6], cdm_8_mark5_1_addr[7], data);
  Multiplexer #(.select(2), .enable("false")) multiplexer_3 (
    .in0(RAM), .in1(init_table), .in2(buff_sel), .out(multiplexer_3_out), .sel(priority_encoder_1_out));  // open: in3
  Comparator #(.mode("unsigned")) comparator_1 (
    .a(multiplexer_1_out), .b({8{1'b0}}), .eq(comparator_1_eq));  // open: gt, lt
  dX dx_1 (
    .game_clk(game_clk), .hit_ai_x(EVENT_HIT_AI_hit_x), .hit_ai_x_1(EVENT_HIT_AI_hit_x_1),
    .hit_ai_x_1_2(EVENT_HIT_AI_hit_x_1_2), .hit_ai_x_2(EVENT_HIT_AI_hit_x_2),
    .hit_ai_x_2_2(EVENT_HIT_AI_hit_x_2_2), .hit_player_x(EVENT_HIT_PLAYER_hit_x),
    .hit_player_x_1(EVENT_HIT_PLAYER_hit_x_1), .hit_player_x_1_2(EVENT_HIT_PLAYER_hit_x_1_2),
    .hit_player_x_2(EVENT_HIT_PLAYER_hit_x_2), .hit_player_x_2_2(EVENT_HIT_PLAYER_hit_x_2_2), .btn_left(L),
    .btn_right(R), .freeze(freeze), .ball_x(ball_x), .dX(dX));
  dY dy_1 (.hit_ai(hit_ai), .hit_player(hit_player), .game_active(game_active), .hit_any(dy_1_hit_any), .dY(dY));
  game_active game_active_1 (
    .ball_y(ball_y), .btn_left(L), .btn_right(R), .btn_reset(Reset), .game_clk(game_clk),
    .name_is_valid(name_is_valid), .player_fails(player_fails), .ai_fails(ai_fails),
    .player_loser(player_loser), .game_active(game_active), .interrupt_start(interrupt_start));
  player_score_game_speed player_score_game_speed_1 (
    .hit_player(hit_player), .f1_wrtie(f1_write), .game_clk(game_clk), .game_speed(game_speed),
    .player_score(player_score), .btn_reset(Reset));
  Divider divider_1 (.a(player_score), .b(8'h64), .out(divider_1_out), .rem(divider_1_rem));  // open: upper
  Divider divider_2 (.a(divider_1_rem), .b(8'ha), .out(divider_2_out), .rem(divider_2_rem));  // open: upper
  and and_2 (RAM, ~I_O_sel, data);  // AND_Gate
  ROM rom_1 (.addr({cdm_8_mark5_1_addr, I_O_addr}), .data(I_O_data_read), .sel(code));
  RAM #(.bus("separate")) ram_1 (
    .addr(multiplexer_1_out), .din(multiplexer_2_out), .data(I_O_data_read), .str(or_5_out),
    .sel(multiplexer_3_out), .clk(cdm8_clk), .ld(not_2_out));  // open: clr
  not not_2 (not_2_out, or_5_out);
  Register register_1 (.D(multiplexer_2_out), .en(and_3_out), .Q(register_1_q), .clk(cdm8_clk));  // open: clr
  and and_3 (and_3_out, or_5_out, comparator_1_eq, d_ff_3_q);
  Bit_Extender #(.out_width(4)) bit_extender_1 (.in(divider_1_out), .out(hundred));
  Bit_Extender #(.out_width(4)) bit_extender_2 (.in(divider_2_out), .out(ten));
  Comparator #(.mode("unsigned")) comparator_2 (.a(register_1_q), .b({8{1'b0}}), .eq(comparator_2_eq));  // open: gt, lt
  Comparator #(.mode("unsigned")) comparator_3 (.a(register_1_q), .b(8'h20), .eq(comparator_3_eq));  // open: gt, lt
  Comparator #(.mode("unsigned")) comparator_4 (.a(register_1_q), .b(8'h5f), .eq(comparator_4_eq));  // open: gt, lt
  Bresenham BRESENHAM (
    .hit_ai_x_1(EVENT_HIT_AI_hit_x_1), .hit_ai_x_1_2(EVENT_HIT_AI_hit_x_1_2),
    .hit_ai_x_2(EVENT_HIT_AI_hit_x_2), .hit_ai_x_2_2(EVENT_HIT_AI_hit_x_2_2),
    .hit_player_x_1(EVENT_HIT_PLAYER_hit_x_1), .hit_player_x_1_2(EVENT_HIT_PLAYER_hit_x_1_2),
    .hit_player_x_2(EVENT_HIT_PLAYER_hit_x_2), .hit_player_x_2_2(EVENT_HIT_PLAYER_hit_x_2_2),
    .hit_any(dy_1_hit_any), .game_clk(game_clk), .game_active(game_active), .slope_x(slope_x),
    .slope_y(slope_y));
  Bit_Extender #(.out_width(4)) bit_extender_3 (.in(divider_2_rem), .out(one));
  nor nor_1 (name_is_valid, comparator_2_eq, comparator_3_eq, comparator_4_eq);
  Comparator #(.width(4), .mode("unsigned")) comparator_5 (
    .a(I_O_addr), .b(4'b0100), .eq(comparator_5_eq));  // open: gt, lt
  Comparator #(.width(4), .mode("unsigned")) comparator_6 (
    .a(I_O_addr), .b(4'b0001), .eq(comparator_6_eq));  // open: gt, lt
  Comparator #(.width(4), .mode("unsigned")) comparator_7 (
    .a(I_O_addr), .b(4'b0010), .eq(comparator_7_eq));  // open: gt, lt
  Comparator #(.width(4), .mode("unsigned")) comparator_8 (
    .a(I_O_addr), .b(4'b0011), .eq(comparator_8_eq));  // open: gt, lt
  Comparator #(.width(4), .mode("unsigned")) comparator_9 (
    .a(I_O_addr), .b(4'b0101), .eq(comparator_9_eq));  // open: gt, lt
  D_Flip_Flop d_ff_1 (
    .clk(cdm8_clk), .D(1'b1), .Q(init_table), .en(not_3_out), .reset(counter_1_carry));  // open: Qn, preset
  not not_3 (not_3_out, counter_1_carry);
  and and_4 (and_4_out, comparator_5_eq, I_O_sel);
  LED led_1 (.in(and_5_out));
  and and_5 (and_5_out, comparator_6_eq, I_O_sel);
  and and_6 (and_6_out, I_O_sel, comparator_7_eq);
  and and_7 (and_7_out, I_O_sel, comparator_8_eq);
  and and_8 (and_8_out, I_O_sel, comparator_9_eq);
  and and_9 (and_9_out, ~rd_wr, and_4_out);  // AND_Gate
  and and_10 (f1_write, ~rd_wr, and_5_out);  // AND_Gate
  and and_11 (and_11_out, ~rd_wr, and_6_out);  // AND_Gate
  and and_12 (and_12_out, rd_wr, and_7_out);
  assign bit_extender_4_out = {{7{1'b0}}, init_table};  // Bit_Extender bit_extender_4
  and and_13 (and_13_out, rd_wr, and_8_out);
  Counter #(.width(6), .max('h2c), .ongoal("stay")) counter_1 (
    .count(init_table), .Q(counter_1_q), .carry(counter_1_carry), .clk(cdm8_clk));  // open: load, D, clr
  Bit_Extender #(.out_width(7)) bit_extender_5 (.in(I_O_data_read), .out(bit_extender_5_out));
  TTY #(.rows(7), .cols(22), .trigger("falling")) tty_1 (
    .data(bit_extender_5_out), .clk(cdm8_clk), .we(f1_write));  // open: clr
  TTY #(.rows(1), .cols(22)) tty_2 (.data(keyboard_1_data), .clk(cdm8_clk), .we(and_14_out), .clr(and_18_out));
  and and_14 (and_14_out, not_4_out, is_valid);
  Keyboard keyboard_1 (
    .clk(cdm8_clk), .re(not_4_out), .clr(d_ff_4_qn), .avail(keyboard_1_avail), .data(keyboard_1_data));
  not not_4 (not_4_out, d_ff_4_qn);
  D_Flip_Flop #(.trigger("falling")) d_ff_2 (
    .clk(cdm8_clk), .D(I_O_data_read[0]), .Q(d_ff_2_q[0]), .en(and_11_out));  // open: Qn, preset, reset
  assign I_O_data_read = and_12_out ? player_score : 8'bz;  // Controlled_Buffer controlled_buffer_3
  assign I_O_data_read = and_13_out ? bit_extender_4_out : 8'bz;  // Controlled_Buffer controlled_buffer_4
  assign bit_extender_6_out = {{2{1'b0}}, counter_1_q};  // Bit_Extender bit_extender_6
  Adder adder_1 (.a(bit_extender_6_out), .b(8'h10), .out(init_addr));  // open: cin, cout
  D_Flip_Flop #(.trigger("falling")) d_ff_3 (
    .clk(cdm8_clk), .D(I_O_data_read[0]), .Q(d_ff_3_q), .en(and_9_out));  // open: Qn, preset, reset
  assign I_O_data_read = and_15_out ? {player_loser, {6{1'b0}}, d_ff_2_q[0]} : 8'bz;  // Controlled_Buffer controlled_buffer_5
  and and_15 (and_15_out, rd_wr, and_6_out);
  is_valid is_valid_1 (.kbd_symbol(keyboard_1_data), .is_valid(is_valid));
  and and_16 (kbd_sel, keyboard_1_avail, is_valid);
  ROM rom_2 (.addr(bit_extender_6_out), .data(init_data), .sel(1'b1));
  assign bit_extender_7_out = {{1{1'b0}}, keyboard_1_data};  // Bit_Extender bit_extender_7
  and and_17 (and_17_out, d_ff_2_q[0], player_loser);
  Multiplexer #(.width(8), .enable("false")) multiplexer_4 (
    .in0(bit_extender_7_out), .in1({8{1'b0}}), .out(kbd_data), .sel(comparator_10_eq));
  Comparator #(.mode("unsigned")) comparator_10 (
    .a(bit_extender_7_out), .b(8'h8), .eq(comparator_10_eq));  // open: gt, lt
  Counter #(.width(4), .max('h8), .ongoal("stay"), .trigger("falling")) counter_2 (
    .load(comparator_10_eq), .Q(counter_2_q), .carry(counter_2_carry), .clk(kbd_sel), .clr(d_ff_4_qn));  // open: D, count
  Button button_4 (.out(button_4_out));
  assign vec = arbiter_1_vec ? 3'b100 : 3'bz;  // Controlled_Buffer controlled_buffer_6
  arbiter arbiter_1 (
    .IReq_2(IRQ), .IAck(IAck), .IReq(arbiter_1_iack_2), .IAck_2(arbiter_1_iack_2), .vec(arbiter_1_vec),
    .req(and_17_out), .done(and_12_out), .clock(cdm8_clk));
  and and_18 (and_18_out, d_ff_3_q, button_4_out);
  assign kbd_addr = {{4{1'b0}}, counter_2_q};  // Bit_Extender bit_extender_8
  and and_19 (interrupt_start, IAck, arbiter_1_vec);
  D_Flip_Flop d_ff_4 (
    .clk(and_18_out), .D(and_18_out), .Q(name), .Qn(d_ff_4_qn), .reset(or_6_out));  // open: preset, en
  or or_6 (or_6_out, player_loser, counter_2_carry);
  D_Flip_Flop d_ff_5 (.clk(and_18_out), .D(and_18_out), .Q(d_ff_5_q), .reset(counter_3_carry));  // open: Qn, preset, en
  Counter #(.width(4), .max('h8), .ongoal("stay")) counter_3 (
    .count(and_18_out), .Q(counter_3_q), .carry(counter_3_carry), .clk(cdm8_clk), .clr(d_ff_4_qn));  // open: load, D
  assign bit_extender_9_out = {{4{1'b0}}, counter_3_q};  // Bit_Extender bit_extender_9
  Multiplexer #(.enable("false")) multiplexer_5 (.in0(kbd_sel), .in1(d_ff_5_q), .out(buff_sel), .sel(d_ff_5_q));
  Multiplexer #(.width(8), .enable("false")) multiplexer_6 (
    .in0(kbd_addr), .in1(bit_extender_9_out), .out(buff_addr), .sel(d_ff_5_q));
  Multiplexer #(.width(8), .enable("false")) multiplexer_7 (
    .in0(kbd_data), .in1({8{1'b0}}), .out(buff_data), .sel(d_ff_5_q));
  // also tied to GND on the sheet: arbiter_1_iack_2

  // Other names for the same wires on the sheet: I_O_data_write[7:0] = I_O_data_read

  // Notes on the sheet:
  //   PLAYER
  //   GAME_LOGIC
  //   ldi r0, 0xf0
  //   ldi r1, 1
  //   st r0, r1
  //   START / RESET
  //   status = 10000000b  если символ готов 
  //   status = 00000001b  если прерывания разрешены 
  //   status = 10000001b  если и символ готов, и прерывания разрешены
  //   Чтобы разрешить прерывания от клавиатуры, программа должна записать 1 в бит 0 регистра 0xf0
  //   hit_any
  //   GAME_ACTIVE
  //   PLAYER_SCORE | GAME_SPEED
  //   PLAYER_SCORE_TO_SCREEN
  //   instr_mem
  //   contents of rom_1 (hex, n*v repeats v):
  //   d0 f5 b1 5 e0 8 ee 2 cd f0 d0 3d d1 10 d2 5 a e0 1e a1 d3 0 a7 8c d3 9 1d 8a ee 10 d1 1 d0 f2 a1 d0
  //   f4 a1 c1 d1 2e c1 d1 80 c1 d9 c5 d5 ee 2f ce d0 0 d1 f4 a4 d0 f3 b1 d0 3d d2 42 72 e0 50 b2 bb 77 ec
  //   4a 8c ee 4e d6 59 ee 50 ee 3d d6 81 d0 1 d1 f4 a4 cf d9 d2 41 bb ad c0 c1 c2 c3 d 8d d0 0 d2 8 a e0
  //   71 b3 a7 8c 8d 8a ee 67 c7 c6 c5 c4 78 e0 7f 9 89 b5 a9 8a ee 75 a3 d7 d0 3d d3 5 f e0 ae b2 c2 ba
  //   c0 c3 d6 b2 c7 c4 d1 f1 d2 20 a6 c6 8e c0 c3 d3 8 f e0 a5 b8 a4 8e 8b ee 9c c7 c4 d2 a a6 8c 8b ee
  //   85 d2 a a6 d7 d1 f1 d0 0 d3 64 7b eb c0 3b e 8c ee b6 d3 30 13 a7 d0 0 d3 a 7b eb d0 3b e 8c ee c6
  //   d3 30 13 a7 d3 30 1b a7 d7 31*0 32
  //   data_mem
  //   0xf2  -> status register 
  //   0xf3  -> data register 
  //   contents of rom_2 (hex, n*v repeats v):
  //   0 49 72 74 65 67 6f 76 0 0 4e 61 7a 61 72 6f 76 0 0 42 6f 6e 64 61 72 65 76 0 49 76 61 6e 6f 76 0 0
  //   0 50 65 74 72 6f 76
  //   ВВЕСТИ ИМЯ
  //   vec == 4
  //   cleaning
endmodule

module test2 (
  output [31:0] out_1,
  output [31:0] out_2,
  output [3:0] player_fails,
  output [31:0] out_4,
  output [31:0] out_5,
  output [3:0] ai_fails,
  output [31:0] out_7,
  output [31:0] out_8,
  output [31:0] out_9,
  output [31:0] out_10,
  output [31:0] out_11,
  output [31:0] out_12,
  output [31:0] out_13,
  output [31:0] out_14,
  output [31:0] out_15,
  output [31:0] out_16,
  output [31:0] out_17,
  output [31:0] out_18,
  output [31:0] out_19,
  output [31:0] out_20,
  output [31:0] out_21,
  output [31:0] out_22,
  output [31:0] out_23,
  output [31:0] out_24,
  output [31:0] out_25,
  output [31:0] out_26,
  output [31:0] out_27,
  output [31:0] out_28,
  output [31:0] out_29,
  output [31:0] out_30,
  output [31:0] out_31,
  output [31:0] out_32,
  output [31:0] out_33,
  output [31:0] out_34,
  output [3:0] hundred,
  output [3:0] ten,
  output [3:0] one
);

  wire and_3_out, and_4_out, and_5_out, and_6_out, and_7_out, and_8_out, and_10_out, and_11_out, and_12_out,
       and_13_out, and_14_out, and_15_out, and_16_out, and_17_out, and_19_out, arbiter_1_iack_2,
       arbiter_1_vec, buff_sel, cdm8_clk, cdm_8_mark5_1_data_inst, code, comparator_1_eq, comparator_2_eq,
       comparator_3_eq, comparator_4_eq, comparator_5_eq, comparator_6_eq, comparator_7_eq, counter_1_carry,
       counter_2_carry, counter_3_carry, d_ff_1_qn, d_ff_4_qn, d_ff_5_q, d_ff_5_qn, data, dX, dY,
       dy_1_hit_any, EVENT_HIT_AI_hit_x, EVENT_HIT_AI_hit_x_1, EVENT_HIT_AI_hit_x_1_2, EVENT_HIT_AI_hit_x_2,
       EVENT_HIT_AI_hit_x_2_2, EVENT_HIT_PLAYER_hit_x, EVENT_HIT_PLAYER_hit_x_1, EVENT_HIT_PLAYER_hit_x_1_2,
       EVENT_HIT_PLAYER_hit_x_2, EVENT_HIT_PLAYER_hit_x_2_2, f1_write, freeze, game_active, game_clk, hit_ai,
       hit_player, I_O_sel, IAck, init_table, interrupt_start, IRQ, is_valid, kbd_sel, keyboard_1_avail, L,
       mem, multiplexer_3_out, name, not_1_out, not_2_out, not_3_out, not_4_out, or_5_out, or_6_out,
       player_loser, R, RAM, rd_wr, Reset, undriven_2;
  wire [0:0] d_ff_2_q;
  wire [1:0] priority_encoder_1_out;
  wire [2:0] vec;
  wire [3:0] counter_2_q, counter_3_q, I_O_addr, main_1_ai_fails, main_1_hundred, main_1_one,
       main_1_player_fails, main_1_ten;
  wire [4:0] AI_ai_x, AI_ai_x_1, AI_ai_x_1_2, ball_x, ball_y, player_1_player_x_1, player_1_player_x_1_2,
       player_x, slope_x, slope_y;
  wire [5:0] counter_1_q;
  wire [6:0] bit_extender_5_out, controlled_buffer_7_out, keyboard_1_data, undriven;
  wire [7:0] bit_extender_4_out, bit_extender_6_out, bit_extender_7_out, bit_extender_9_out, buff_addr,
       buff_data, cdm_8_mark5_1_data_out, cdm_8_mark5_1_pc, cdm_8_mark5_1_ps, cdm_8_mark5_1_r0,
       cdm_8_mark5_1_r1, cdm_8_mark5_1_r2, cdm_8_mark5_1_r3, cdm_8_mark5_1_sp, controlled_buffer_2_out,
       divider_1_out, divider_1_rem, divider_2_out, divider_2_rem, game_speed, I_O_data_read, init_addr,
       init_data, kbd_addr, kbd_data, multiplexer_1_out, multiplexer_2_out, player_score, register_1_q;
  wire [7:4] cdm_8_mark5_1_addr;
  wire [31:0] AI_ai_screen_pixel, ball_1_out_10, ball_1_out_41, main_1_out_7, main_1_out_8, main_1_out_10,
       main_1_out_11, main_1_out_13, main_1_out_14, main_1_out_15, main_1_out_16, main_1_out_17,
       main_1_out_18, main_1_out_19, main_1_out_20, main_1_out_21, main_1_out_22, main_1_out_23,
       main_1_out_24, main_1_out_25, main_1_out_26, main_1_out_27, main_1_out_28, main_1_out_29,
       main_1_out_30, main_1_out_31, main_1_out_32, main_1_out_33, main_1_out_34, main_1_out_35,
       main_1_out_36, main_1_out_37, main_1_out_38, main_1_out_39, main_1_out_40,
       player_1_player_screen_pixel;

  clock_frequency_divider CLOCK (.game_speed(game_speed), .game_clk(game_clk), .cdm8_clk(cdm8_clk));
  ai AI (
    .game_clk(game_clk), .game_active(game_active), .ball_x(ball_x), .ball_y(ball_y), .ball_dx(dX),
    .ball_dy(dY), .player_x(player_x), .ai_screen_pixel(AI_ai_screen_pixel), .ai_x(AI_ai_x),
    .ai_x_1(AI_ai_x_1), .ai_x_1_2(AI_ai_x_1_2));
  ball ball_1 (
    .dX(dX), .dY(dY), .game_active(game_active), .game_clk(game_clk), .ball_x(ball_x), .out_18(out_11),
    .out_19(out_12), .out_20(out_13), .out_21(out_14), .out_22(out_15), .out_23(out_16), .out_24(out_17),
    .out_25(out_18), .ball_y(ball_y), .slope_x(slope_x), .slope_y(slope_y), .out_26(out_19), .out_27(out_20),
    .out_28(out_21), .out_29(out_22), .out_30(out_23), .out_31(out_24), .out_32(out_25), .out_33(out_26),
    .out_34(out_27), .out_35(out_28), .out_36(out_29), .out_37(out_30), .out_38(out_31), .out_39(out_32),
    .out_40(out_33), .out_41(ball_1_out_41), .out_10(ball_1_out_10), .out_11(out_2), .out_12(out_4),
    .out_13(out_5), .out_14(out_7), .out_15(out_8), .out_16(out_9), .out_17(out_10), .freeze(freeze),
    .player_x(player_x));
  player player_1 (
    .btn_left(L), .btn_right(R), .game_active(game_active), .game_clk(game_clk),
    .player_screen_pixel(player_1_player_screen_pixel), .player_x(player_x),
    .player_x_1(player_1_player_x_1), .player_x_1_2(player_1_player_x_1_2));
  collision_check EVENT_HIT_AI (
    .player_x(AI_ai_x), .player_x_1(AI_ai_x_1), .player_x_1_2(AI_ai_x_1_2), .ball_x(ball_x), .ball_y(ball_y),
    .coordinate_to_check(5'b00001), .hit_x(EVENT_HIT_AI_hit_x), .hit_x_1(EVENT_HIT_AI_hit_x_1),
    .hit_x_1_2(EVENT_HIT_AI_hit_x_1_2), .hit_x_2(EVENT_HIT_AI_hit_x_2), .hit_x_2_2(EVENT_HIT_AI_hit_x_2_2));
  assign out_1 = AI_ai_screen_pixel | ball_1_out_10;  // OR_Gate or_1, 32 bits wide
  assign out_34 = ball_1_out_41 | player_1_player_screen_pixel;  // OR_Gate or_2, 32 bits wide
  collision_check EVENT_HIT_PLAYER (
    .player_x(player_x), .player_x_1(player_1_player_x_1), .player_x_1_2(player_1_player_x_1_2),
    .ball_x(ball_x), .ball_y(ball_y), .coordinate_to_check(5'b11110), .hit_x(EVENT_HIT_PLAYER_hit_x),
    .hit_x_1(EVENT_HIT_PLAYER_hit_x_1), .hit_x_1_2(EVENT_HIT_PLAYER_hit_x_1_2),
    .hit_x_2(EVENT_HIT_PLAYER_hit_x_2), .hit_x_2_2(EVENT_HIT_PLAYER_hit_x_2_2));
  // Probe on cdm_8_mark5_1_r0
  // Probe on cdm_8_mark5_1_r3
  // Probe on cdm_8_mark5_1_r2
  // Probe on cdm_8_mark5_1_r1
  // Probe on cdm_8_mark5_1_sp
  // Probe on cdm_8_mark5_1_pc
  or or_3 (hit_ai, EVENT_HIT_AI_hit_x, EVENT_HIT_AI_hit_x_1, EVENT_HIT_AI_hit_x_1_2, EVENT_HIT_AI_hit_x_2, EVENT_HIT_AI_hit_x_2_2);
  // Probe on cdm_8_mark5_1_ps
  Pull_Resistor pull_resistor_1 (.node(data));
  Decoder decoder_1 (.out0(code), .out1(data), .sel(cdm_8_mark5_1_data_inst), .en(mem));
  CdM_8_mark5 cdm_8_mark5_1 (
    .clock(cdm8_clk), .addr({cdm_8_mark5_1_addr, I_O_addr}), .mem_read(rd_wr), .mem_cycle(mem),
    .data_inst(cdm_8_mark5_1_data_inst), .data_out(cdm_8_mark5_1_data_out),
    .data_in(controlled_buffer_2_out), .r0(cdm_8_mark5_1_r0), .r1(cdm_8_mark5_1_r1), .r2(cdm_8_mark5_1_r2),
    .r3(cdm_8_mark5_1_r3), .PC(cdm_8_mark5_1_pc), .SP(cdm_8_mark5_1_sp), .PS(cdm_8_mark5_1_ps), .IAck(IAck),
    .IRQ(IRQ), .vec(vec));
  assign I_O_data_read = not_1_out ? cdm_8_mark5_1_data_out : 8'bz;  // Controlled_Buffer controlled_buffer_1
  not not_1 (not_1_out, rd_wr);
  assign controlled_buffer_2_out = rd_wr ? I_O_data_read : 8'bz;  // Controlled_Buffer controlled_buffer_2
  Pull_Resistor pull_resistor_2 (.node(code));
  or or_4 (hit_player, EVENT_HIT_PLAYER_hit_x, EVENT_HIT_PLAYER_hit_x_1, EVENT_HIT_PLAYER_hit_x_1_2, EVENT_HIT_PLAYER_hit_x_2, EVENT_HIT_PLAYER_hit_x_2_2);
  freeze u_FREEZE (
    .game_clk(game_clk), .hit_x(EVENT_HIT_PLAYER_hit_x), .hit_x_1(EVENT_HIT_PLAYER_hit_x_1),
    .hit_x_1_2(EVENT_HIT_PLAYER_hit_x_1_2), .btn_left(L), .btn_right(R), .freeze(freeze));
  Priority_Encoder #(.select(2)) priority_encoder_1 (
    .in0(1'b1), .in1(init_table), .in2(name), .out(priority_encoder_1_out));  // open: in3, gs, en_out, en_in
  dX dx_1 (
    .game_clk(game_clk), .hit_ai_x(EVENT_HIT_AI_hit_x), .hit_ai_x_1(EVENT_HIT_AI_hit_x_1),
    .hit_ai_x_1_2(EVENT_HIT_AI_hit_x_1_2), .hit_ai_x_2(EVENT_HIT_AI_hit_x_2),
    .hit_ai_x_2_2(EVENT_HIT_AI_hit_x_2_2), .hit_player_x(EVENT_HIT_PLAYER_hit_x),
    .hit_player_x_1(EVENT_HIT_PLAYER_hit_x_1), .hit_player_x_1_2(EVENT_HIT_PLAYER_hit_x_1_2),
    .hit_player_x_2(EVENT_HIT_PLAYER_hit_x_2), .hit_player_x_2_2(EVENT_HIT_PLAYER_hit_x_2_2), .btn_left(L),
    .btn_right(R), .freeze(freeze), .ball_x(ball_x), .dX(dX));
  dY dy_1 (.hit_ai(hit_ai), .hit_player(hit_player), .game_active(game_active), .hit_any(dy_1_hit_any), .dY(dY));
  game_active game_active_1 (
    .ball_y(ball_y), .btn_left(L), .btn_right(R), .btn_reset(Reset), .name_is_valid(interrupt_start),
    .player_fails(player_fails), .ai_fails(ai_fails), .player_loser(player_loser), .game_active(game_active),
    .interrupt_start(game_clk));  // open: game_clk
  player_score_game_speed player_score_game_speed_1 (
    .hit_player(hit_player), .f1_wrtie(f1_write), .game_clk(game_clk), .game_speed(game_speed),
    .player_score(player_score), .btn_reset(Reset));
  Divider divider_1 (.a(player_score), .b(8'h64), .out(divider_1_out), .rem(divider_1_rem));  // open: upper
  Multiplexer #(.select(2), .width(8), .enable("false")) multiplexer_1 (
    .in0({cdm_8_mark5_1_addr, I_O_addr}), .in1(init_addr), .in2(buff_addr), .out(multiplexer_1_out),
    .sel(priority_encoder_1_out));  // open: in3
  Bit_Extender #(.out_width(4)) bit_extender_1 (.in(divider_1_out), .out(hundred));
  Bit_Extender #(.out_width(4)) bit_extender_2 (.in(divider_2_out), .out(ten));
  Divider divider_2 (.a(divider_1_rem), .b(8'ha), .out(divider_2_out), .rem(divider_2_rem));  // open: upper
  Bresenham BRESENHAM (
    .hit_ai_x_1(EVENT_HIT_AI_hit_x_1), .hit_ai_x_1_2(EVENT_HIT_AI_hit_x_1_2),
    .hit_ai_x_2(EVENT_HIT_AI_hit_x_2), .hit_ai_x_2_2(EVENT_HIT_AI_hit_x_2_2),
    .hit_player_x_1(EVENT_HIT_PLAYER_hit_x_1), .hit_player_x_1_2(EVENT_HIT_PLAYER_hit_x_1_2),
    .hit_player_x_2(EVENT_HIT_PLAYER_hit_x_2), .hit_player_x_2_2(EVENT_HIT_PLAYER_hit_x_2_2),
    .hit_any(dy_1_hit_any), .game_clk(game_clk), .game_active(game_active), .slope_x(slope_x),
    .slope_y(slope_y));
  Bit_Extender #(.out_width(4)) bit_extender_3 (.in(divider_2_rem), .out(one));
  Multiplexer #(.select(2), .width(8), .enable("false")) multiplexer_2 (
    .in0(I_O_data_read), .in1(init_data), .in2(buff_data), .out(multiplexer_2_out),
    .sel(priority_encoder_1_out));  // open: in3
  or or_5 (or_5_out, ~rd_wr, init_table);  // OR_Gate
  Multiplexer #(.select(2), .enable("false")) multiplexer_3 (
    .in0(RAM), .in1(init_table), .in2(buff_sel), .out(multiplexer_3_out), .sel(priority_encoder_1_out));  // open: in3
  and and_1 (I_O_sel, cdm_8_mark5_1_addr[4], cdm_8_mark5_1_addr[5], cdm_8_mark5_1_addr[6], cdm_8_mark5_1_addr[7], data);
  ROM rom_1 (.addr({cdm_8_mark5_1_addr, I_O_addr}), .data(I_O_data_read), .sel(code));
  RAM #(.bus("separate")) ram_1 (
    .addr(multiplexer_1_out), .din(multiplexer_2_out), .data(I_O_data_read), .str(or_5_out),
    .sel(multiplexer_3_out), .clk(cdm8_clk), .ld(not_2_out));  // open: clr
  not not_2 (not_2_out, or_5_out);
  and and_2 (RAM, ~I_O_sel, data);  // AND_Gate
  main main_1 (
    .btn_left(L), .btn_right(R), .btn_reset(Reset), .out_7(main_1_out_7), .out_8(main_1_out_8),
    .out_10(main_1_out_10), .out_11(main_1_out_11), .out_13(main_1_out_13), .out_14(main_1_out_14),
    .out_15(main_1_out_15), .out_16(main_1_out_16), .out_17(main_1_out_17), .out_18(main_1_out_18),
    .out_19(main_1_out_19), .out_20(main_1_out_20), .out_21(main_1_out_21), .out_22(main_1_out_22),
    .out_23(main_1_out_23), .out_24(main_1_out_24), .out_25(main_1_out_25), .out_26(main_1_out_26),
    .out_27(main_1_out_27), .out_28(main_1_out_28), .out_29(main_1_out_29), .out_30(main_1_out_30),
    .out_31(main_1_out_31), .out_32(main_1_out_32), .out_33(main_1_out_33), .out_34(main_1_out_34),
    .out_35(main_1_out_35), .out_36(main_1_out_36), .out_37(main_1_out_37), .out_38(main_1_out_38),
    .out_39(main_1_out_39), .out_40(main_1_out_40), .player_fails(main_1_player_fails),
    .ai_fails(main_1_ai_fails), .one(main_1_one), .hundred(main_1_hundred), .ten(main_1_ten));  // open: btn_input_name, I_O_data_read, f1_write, cdm8_clk, clear_name_screen, is_valid, clear_kbd, kbd_enable, kbd_data, kbd_is_ready
  DotMatrix #(.inputtype("row"), .matrixcols(32), .matrixrows(1)) dotmatrix_1 (.row0(main_1_out_7));
  DotMatrix #(.inputtype("row"), .matrixcols(32), .matrixrows(30)) dotmatrix_2 (
    .row0(main_1_out_8), .row1(main_1_out_10), .row2(main_1_out_11), .row3(main_1_out_13),
    .row4(main_1_out_14), .row5(main_1_out_15), .row6(main_1_out_16), .row7(main_1_out_17),
    .row8(main_1_out_18), .row9(main_1_out_19), .row10(main_1_out_20), .row11(main_1_out_21),
    .row12(main_1_out_22), .row13(main_1_out_23), .row14(main_1_out_24), .row15(main_1_out_25),
    .row16(main_1_out_26), .row17(main_1_out_27), .row18(main_1_out_28), .row19(main_1_out_29),
    .row20(main_1_out_30), .row21(main_1_out_31), .row22(main_1_out_32), .row23(main_1_out_33),
    .row24(main_1_out_34), .row25(main_1_out_35), .row26(main_1_out_36), .row27(main_1_out_37),
    .row28(main_1_out_38), .row29(main_1_out_39));
  DotMatrix #(.inputtype("row"), .matrixcols(32), .matrixrows(1)) dotmatrix_3 (.row0(main_1_out_40));
  Comparator #(.width(4), .mode("unsigned")) comparator_1 (
    .a(I_O_addr), .b(4'b0100), .eq(comparator_1_eq));  // open: gt, lt
  Comparator #(.width(4), .mode("unsigned")) comparator_2 (
    .a(I_O_addr), .b(4'b0001), .eq(comparator_2_eq));  // open: gt, lt
  Comparator #(.width(4), .mode("unsigned")) comparator_3 (
    .a(I_O_addr), .b(4'b0010), .eq(comparator_3_eq));  // open: gt, lt
  Comparator #(.width(4), .mode("unsigned")) comparator_4 (
    .a(I_O_addr), .b(4'b0011), .eq(comparator_4_eq));  // open: gt, lt
  Comparator #(.width(4), .mode("unsigned")) comparator_5 (
    .a(I_O_addr), .b(4'b0101), .eq(comparator_5_eq));  // open: gt, lt
  D_Flip_Flop d_ff_1 (
    .clk(cdm8_clk), .D(1'b1), .Q(init_table), .Qn(d_ff_1_qn), .en(not_3_out), .reset(counter_1_carry));  // open: preset
  not not_3 (not_3_out, counter_1_carry);
  and and_3 (and_3_out, comparator_1_eq, I_O_sel);
  and and_4 (and_4_out, comparator_2_eq, I_O_sel);
  LED led_1 (.in(and_4_out));
  and and_5 (and_5_out, I_O_sel, comparator_3_eq);
  and and_6 (and_6_out, I_O_sel, comparator_4_eq);
  and and_7 (and_7_out, I_O_sel, comparator_5_eq);
  Button button_1 (.out(L));
  and and_8 (and_8_out, ~rd_wr, and_3_out);  // AND_Gate
  and and_9 (f1_write, ~rd_wr, and_4_out);  // AND_Gate
  and and_10 (and_10_out, ~rd_wr, and_5_out);  // AND_Gate
  and and_11 (and_11_out, rd_wr, and_6_out);
  assign bit_extender_4_out = {{7{1'b0}}, init_table};  // Bit_Extender bit_extender_4
  and and_12 (and_12_out, rd_wr, and_7_out);
  Counter #(.width(6), .max('h2c), .ongoal("stay")) counter_1 (
    .count(init_table), .Q(counter_1_q), .carry(counter_1_carry), .clk(cdm8_clk));  // open: load, D, clr
  Button button_2 (.out(R));
  Register register_1 (.D(I_O_data_read), .en(and_8_out), .Q(register_1_q), .clk(cdm8_clk));  // open: clr
  Bit_Extender #(.out_width(7)) bit_extender_5 (.in(I_O_data_read), .out(bit_extender_5_out));
  TTY #(.rows(7), .cols(22), .trigger("falling")) tty_1 (
    .data(bit_extender_5_out), .clk(cdm8_clk), .we(f1_write));  // open: clr
  TTY #(.rows(1), .cols(22)) tty_2 (.data(undriven), .clk(cdm8_clk), .clr(d_ff_4_qn));  // open: we
  and and_13 (and_13_out, not_4_out, is_valid);
  Keyboard keyboard_1 (.clk(cdm8_clk), .re(undriven_2), .avail(keyboard_1_avail), .data(keyboard_1_data));  // open: clr
  not not_4 (not_4_out, undriven_2);
  D_Flip_Flop #(.trigger("falling")) d_ff_2 (
    .clk(cdm8_clk), .D(I_O_data_read[0]), .Q(d_ff_2_q[0]), .en(and_10_out));  // open: Qn, preset, reset
  assign I_O_data_read = and_11_out ? player_score : 8'bz;  // Controlled_Buffer controlled_buffer_3
  assign I_O_data_read = and_12_out ? bit_extender_4_out : 8'bz;  // Controlled_Buffer controlled_buffer_4
  assign bit_extender_6_out = {{2{1'b0}}, counter_1_q};  // Bit_Extender bit_extender_6
  Adder adder_1 (.a(bit_extender_6_out), .b(8'h10), .out(init_addr));  // open: cin, cout
  Button button_3 (.out(Reset));
  assign I_O_data_read = and_14_out ? {player_loser, {6{1'b0}}, d_ff_2_q[0]} : 8'bz;  // Controlled_Buffer controlled_buffer_5
  and and_14 (and_14_out, rd_wr, and_5_out);
  and and_15 (and_15_out, keyboard_1_avail, is_valid);
  ROM rom_2 (.addr(bit_extender_6_out), .data(init_data), .sel(1'b1));
  LED led_2 ();  // open: in
  LED led_3 ();  // open: in
  Hex_Digit_Display hex_digit_display_1 (.value(main_1_player_fails));  // open: dp
  Hex_Digit_Display hex_digit_display_2 (.value(main_1_hundred));  // open: dp
  Hex_Digit_Display hex_digit_display_3 (.value(main_1_ten));  // open: dp
  is_valid is_valid_1 (.kbd_symbol(keyboard_1_data), .is_valid(is_valid));
  assign kbd_sel = d_ff_5_qn ? and_15_out : 1'bz;  // Controlled_Buffer controlled_buffer_6
  and and_16 (and_16_out, d_ff_2_q[0], player_loser);
  Hex_Digit_Display hex_digit_display_4 (.value(main_1_ai_fails));  // open: dp
  Hex_Digit_Display hex_digit_display_5 (.value(main_1_one));  // open: dp
  assign controlled_buffer_7_out = and_17_out ? keyboard_1_data : 7'bz;  // Controlled_Buffer controlled_buffer_7
  and and_17 (and_17_out, keyboard_1_avail, d_ff_5_qn);
  assign vec = arbiter_1_vec ? 3'b100 : 3'bz;  // Controlled_Buffer controlled_buffer_8
  arbiter arbiter_1 (
    .IReq_2(IRQ), .IAck(IAck), .IReq(arbiter_1_iack_2), .IAck_2(arbiter_1_iack_2), .vec(arbiter_1_vec),
    .req(and_16_out), .done(and_11_out), .clock(cdm8_clk));
  assign bit_extender_7_out = {{1{1'b0}}, controlled_buffer_7_out};  // Bit_Extender bit_extender_7
  and and_18 (interrupt_start, IAck, arbiter_1_vec);
  Multiplexer #(.width(8), .enable("false")) multiplexer_4 (
    .in0(bit_extender_7_out), .in1({8{1'b0}}), .out(kbd_data), .sel(comparator_6_eq));
  Comparator #(.mode("unsigned")) comparator_6 (
    .a(bit_extender_7_out), .b(8'h8), .eq(comparator_6_eq));  // open: gt, lt
  Counter #(.width(4), .max('h8), .ongoal("stay"), .trigger("falling")) counter_2 (
    .load(comparator_6_eq), .Q(counter_2_q), .carry(counter_2_carry), .clk(and_19_out), .clr(d_ff_4_qn));  // open: D, count
  and and_19 (and_19_out, counter_3_carry, and_15_out);
  D_Flip_Flop #(.trigger("falling")) d_ff_3 (.clk(keyboard_1_avail), .D(1'b1));  // open: Q, Qn, preset, en, reset
  Comparator #(.mode("unsigned")) comparator_7 (
    .a(bit_extender_7_out), .b(8'ha), .eq(comparator_7_eq));  // open: gt, lt
  assign kbd_addr = {{4{1'b0}}, counter_2_q};  // Bit_Extender bit_extender_8
  D_Flip_Flop d_ff_4 (
    .clk(keyboard_1_avail), .D(1'b1), .Q(name), .Qn(d_ff_4_qn), .reset(or_6_out));  // open: preset, en
  or or_6 (or_6_out, comparator_7_eq, player_loser, counter_2_carry);
  D_Flip_Flop d_ff_5 (
    .clk(keyboard_1_avail), .D(1'b1), .Q(d_ff_5_q), .Qn(d_ff_5_qn), .reset(counter_3_carry));  // open: preset, en
  Counter #(.width(4), .max('h8), .ongoal("stay")) counter_3 (
    .count(name), .Q(counter_3_q), .carry(counter_3_carry), .clk(cdm8_clk), .clr(d_ff_4_qn));  // open: load, D
  assign bit_extender_9_out = {{4{1'b0}}, counter_3_q};  // Bit_Extender bit_extender_9
  Multiplexer #(.enable("false")) multiplexer_5 (.in0(kbd_sel), .in1(d_ff_5_q), .out(buff_sel), .sel(d_ff_5_q));
  Multiplexer #(.width(8), .enable("false")) multiplexer_6 (
    .in0(kbd_addr), .in1(bit_extender_9_out), .out(buff_addr), .sel(d_ff_5_q));
  Multiplexer #(.width(8), .enable("false")) multiplexer_7 (
    .in0(kbd_data), .in1({8{1'b0}}), .out(buff_data), .sel(d_ff_5_q));
  // also tied to GND on the sheet: arbiter_1_iack_2

  // Other names for the same wires on the sheet: I_O_data_write[7:0] = I_O_data_read

  // Notes on the sheet:
  //   PLAYER
  //   GAME_LOGIC
  //   MATRIX
  //   GAME_ACTIVE
  //   PLAYER_SCORE | GAME_SPEED
  //   PLAYER_SCORE_TO_SCREEN
  //   ldi r0, 0xf0
  //   ldi r1, 1
  //   st r0, r1
  //   hit_any
  //   status = 10000000b  если символ готов 
  //   status = 00000001b  если прерывания разрешены 
  //   status = 10000001b  если и символ готов, и прерывания разрешены
  //   Чтобы разрешить прерывания от клавиатуры, программа должна записать 1 в бит 0 регистра 0xf0
  //   instr_mem
  //   contents of rom_1 (hex, n*v repeats v):
  //   d0 0 b0 d1 f4 a4 d0 f5 b1 5 e0 e ee 8 cd f0 d0 3d d1 10 d2 5 a e0 24 a1 d3 0 a7 8c d3 9 1d 8a ee 16
  //   d1 1 d0 f2 a1 c1 d1 31 c1 d1 80 c1 d9 c5 d5 ee 32 ce d0 f3 b1 d0 3d d2 42 72 e0 4e b2 bb 77 ec 48 8c
  //   ee 4c d6 52 ee 4e ee 3b d6 7a cf d9 d2 41 bb ad c0 c1 c2 c3 d 8d d0 0 d2 8 a e0 6a b3 a7 8c 8d 8a ee
  //   60 c7 c6 c5 c4 78 e0 78 9 89 b5 a9 8a ee 6e a3 d7 d0 3d d3 5 f e0 a7 b2 c2 ba c0 c3 d6 ab c7 c4 d1
  //   f1 d2 20 a6 c6 8e c0 c3 d3 8 f e0 9e b8 a4 8e 8b ee 95 c7 c4 d2 a a6 8c 8b ee 7e d2 a a6 d7 d1 f1 d0
  //   0 d3 64 7b eb b9 3b e 8c ee af d3 30 13 a7 d0 0 d3 a 7b eb c9 3b e 8c ee bf d3 30 13 a7 d3 30 1b a7
  //   d7 38*0 35
  //   data_mem
  //   0xf2  -> status register 
  //   0xf3  -> data register 
  //   START / RESET
  //   contents of rom_2 (hex, n*v repeats v):
  //   0 49 72 74 65 67 6f 76 0 0 4e 61 7a 61 72 6f 76 0 0 42 6f 6e 64 61 72 65 76 0 49 76 61 6e 6f 76 0 0
  //   0 50 65 74 72 6f 76
  //   PLAYER
  //   PLAYER_SCORE
  //   AI
  //   vec == 4
  //   ВВЕСТИ ИМЯ
  //   cleaning
endmodule
