// Logisim project Ьase17_8.0.circ as structural Verilog: 9 circuits, main circuit main
module main (
);

  wire and_1_out, and_4_out, and_5_out, and_6_out, and_7_out, and_8_out, and_9_out, and_10_out, and_11_out,
       and_12_out, and_13_out, and_14_out, and_16_out, and_17_out, and_18_out, arbiter_1_iack_2,
       arbiter_1_vec, buff_sel, button_4_out, cdm8_clk, cdm_8_mark5_1_data_inst, code, comparator_1_eq,
       comparator_2_eq, comparator_3_eq, comparator_4_eq, comparator_5_eq, comparator_6_eq, comparator_7_eq,
       comparator_8_eq, comparator_9_eq, comparator_10_eq, comparator_11_eq, comparator_12_eq,
       comparator_13_eq, comparator_14_gt, comparator_15_lt, comparator_16_gt, comparator_17_lt,
       comparator_18_eq, counter_3_carry, counter_6_carry, counter_7_carry, counter_8_carry, d_ff_2_q,
       d_ff_3_qn, d_ff_5_q, d_ff_6_q, data, dX, dY, EVENT_HIT_AI_hit_x, EVENT_HIT_AI_hit_x_1,
       EVENT_HIT_AI_hit_x_1_2, EVENT_HIT_AI_hit_x_2, EVENT_HIT_AI_hit_x_2_2, event_hit_player,
       EVENT_HIT_PLAYER_hit_x, EVENT_HIT_PLAYER_hit_x_1, EVENT_HIT_PLAYER_hit_x_1_2,
       EVENT_HIT_PLAYER_hit_x_2, EVENT_HIT_PLAYER_hit_x_2_2, freeze, game_active, game_clk, I_O_sel, IAck,
       init_table, IRQ, is_valid, kbd_sel, keyboard_1_avail, L, mem, multiplexer_3_out, name, not_1_out,
       not_2_out, not_3_out, not_4_out, not_5_out, not_6_out, not_7_out, not_8_out, not_9_out, not_10_out,
       or_1_out, or_2_out, or_5_out, or_7_out, or_8_out, or_9_out, or_10_out, or_11_out, or_13_out,
       or_15_out, or_16_out, or_18_out, or_19_out, or_20_out, or_21_out, or_22_out, or_24_out, player_loser,
       R, RAM, rd_wr, Reset, s_r_ff_2_q, s_r_ff_3_q, s_r_ff_4_q, s_r_ff_5_qn, xnor_1_out, xnor_2_out,
       xnor_3_out;
  wire [0:0] d_ff_4_q, or_6_out;
  wire [1:0] Angle_Reg_q, or_14_out, priority_encoder_1_out;
  wire [2:0] counter_5_q, priority_encoder_2_out, vec;
  wire [3:0] bit_extender_1_out, bit_extender_2_out, bit_extender_3_out, counter_1_q, counter_2_q,
       counter_6_q, counter_7_q, I_O_addr;
  wire [4:0] ai_1_ai_x, ai_1_ai_x_1, ai_1_ai_x_1_2, ball_1_ball_x, ball_1_ball_y, player_1_player_x_1,
       player_1_player_x_1_2, player_x, slope_x, slope_y;
  wire [5:0] counter_8_q;
  wire [6:0] bit_extender_4_out, keyboard_1_data;
  wire [7:0] bit_extender_5_out, bit_extender_7_out, bit_extender_8_out, buff_addr, buff_data,
       cdm_8_mark5_1_data_out, cdm_8_mark5_1_pc, cdm_8_mark5_1_ps, cdm_8_mark5_1_r0, cdm_8_mark5_1_r1,
       cdm_8_mark5_1_r2, cdm_8_mark5_1_r3, cdm_8_mark5_1_sp, controlled_buffer_2_out, divider_1_out,
       divider_1_rem, divider_2_out, divider_2_rem, I_O_data_read, init_addr, init_data, kbd_addr, kbd_data,
       multiplexer_1_out, multiplexer_2_out, player_score, speed;
  wire [7:4] cdm_8_mark5_1_addr;
  wire [31:0] ai_1_ai_screen_pixel, ball_1_out_10, ball_1_out_11, ball_1_out_12, ball_1_out_13,
       ball_1_out_14, ball_1_out_15, ball_1_out_16, ball_1_out_17, ball_1_out_18, ball_1_out_19,
       ball_1_out_20, ball_1_out_21, ball_1_out_22, ball_1_out_23, ball_1_out_24, ball_1_out_25,
       ball_1_out_26, ball_1_out_27, ball_1_out_28, ball_1_out_29, ball_1_out_30, ball_1_out_31,
       ball_1_out_32, ball_1_out_33, ball_1_out_34, ball_1_out_35, ball_1_out_36, ball_1_out_37,
       ball_1_out_38, ball_1_out_39, ball_1_out_40, ball_1_out_41, or_3_out, or_4_out,
       player_1_player_screen_pixel;

  clock_frequency_divider clock_frequency_divider_1 (.speed(speed), .game_clk(game_clk), .cdm8_clk(cdm8_clk));
  Comparator #(.width(5), .mode("unsigned")) comparator_1 (
    .a(ball_1_ball_y), .b({5{1'b0}}), .eq(comparator_1_eq));  // open: gt, lt
  or or_1 (or_1_out, comparator_1_eq, comparator_2_eq);
  Comparator #(.width(5), .mode("unsigned")) comparator_2 (
    .a(ball_1_ball_y), .b({5{1'b1}}), .eq(comparator_2_eq));  // open: gt, lt
  ai ai_1 (
    .Clk(game_clk), .game_active(game_active), .ball_x(ball_1_ball_x), .ball_y(ball_1_ball_y), .ball_dx(dX),
    .ball_dy(dY), .player_x(player_x), .ai_screen_pixel(ai_1_ai_screen_pixel), .ai_x(ai_1_ai_x),
    .ai_x_1(ai_1_ai_x_1), .ai_x_1_2(ai_1_ai_x_1_2));
  ball ball_1 (
    .dX(dX), .dY(dY), .game_active(game_active), .clk(game_clk), .ball_x(ball_1_ball_x),
    .out_18(ball_1_out_18), .out_19(ball_1_out_19), .out_20(ball_1_out_20), .out_21(ball_1_out_21),
    .out_22(ball_1_out_22), .out_23(ball_1_out_23), .out_24(ball_1_out_24), .out_25(ball_1_out_25),
    .ball_y(ball_1_ball_y), .slope_x(slope_x), .slope_y(slope_y), .out_26(ball_1_out_26),
    .out_27(ball_1_out_27), .out_28(ball_1_out_28), .out_29(ball_1_out_29), .out_30(ball_1_out_30),
    .out_31(ball_1_out_31), .out_32(ball_1_out_32), .out_33(ball_1_out_33), .out_34(ball_1_out_34),
    .out_35(ball_1_out_35), .out_36(ball_1_out_36), .out_37(ball_1_out_37), .out_38(ball_1_out_38),
    .out_39(ball_1_out_39), .out_40(ball_1_out_40), .out_41(ball_1_out_41), .out_10(ball_1_out_10),
    .out_11(ball_1_out_11), .out_12(ball_1_out_12), .out_13(ball_1_out_13), .out_14(ball_1_out_14),
    .out_15(ball_1_out_15), .out_16(ball_1_out_16), .out_17(ball_1_out_17), .freeze(freeze),
    .player_x(player_x));
  player player_1 (
    .btn_left(L), .btn_right(R), .game_active(game_active), .Clk(game_clk),
    .player_screen_pixel(player_1_player_screen_pixel), .player_x(player_x),
    .player_x_1(player_1_player_x_1), .player_x_1_2(player_1_player_x_1_2));
  not not_1 (not_1_out, L);
  not not_2 (not_2_out, R);
  or or_2 (or_2_out, or_1_out, Reset);
  // Probe on cdm_8_mark5_1_r1
  // Probe on cdm_8_mark5_1_r0
  assign or_3_out = ai_1_ai_screen_pixel | ball_1_out_10;  // OR_Gate or_3, 32 bits wide
  assign or_4_out = ball_1_out_41 | player_1_player_screen_pixel;  // OR_Gate or_4, 32 bits wide
  Divider divider_1 (.a(player_score), .b(8'h64), .out(divider_1_out), .rem(divider_1_rem));  // open: upper
  xnor xnor_1 (xnor_1_out, L, not_1_out);
  or or_5 (or_5_out, xnor_1_out, xnor_2_out);
  xnor xnor_2 (xnor_2_out, R, not_2_out);
  // Probe on cdm_8_mark5_1_r3
  // Probe on cdm_8_mark5_1_r2
  // Probe on cdm_8_mark5_1_sp
  // Probe on cdm_8_mark5_1_pc
  collisionCheck EVENT_HIT_AI (
    .player_x(ai_1_ai_x), .player_x_1(ai_1_ai_x_1), .player_x_1_2(ai_1_ai_x_1_2), .ball_x(ball_1_ball_x),
    .ball_y(ball_1_ball_y), .coordinate_to_check(5'b00001), .hit_x(EVENT_HIT_AI_hit_x),
    .hit_x_1(EVENT_HIT_AI_hit_x_1), .hit_x_1_2(EVENT_HIT_AI_hit_x_1_2), .hit_x_2(EVENT_HIT_AI_hit_x_2),
    .hit_x_2_2(EVENT_HIT_AI_hit_x_2_2));
  DotMatrix #(.inputtype("row"), .matrixcols(32), .matrixrows(1)) dotmatrix_1 (.row0(or_3_out));
  DotMatrix #(.inputtype("row"), .matrixcols(32), .matrixrows(30)) dotmatrix_2 (
    .row0(ball_1_out_11), .row1(ball_1_out_12), .row2(ball_1_out_13), .row3(ball_1_out_14),
    .row4(ball_1_out_15), .row5(ball_1_out_16), .row6(ball_1_out_17), .row7(ball_1_out_18),
    .row8(ball_1_out_19), .row9(ball_1_out_20), .row10(ball_1_out_21), .row11(ball_1_out_22),
    .row12(ball_1_out_23), .row13(ball_1_out_24), .row14(ball_1_out_25), .row15(ball_1_out_26),
    .row16(ball_1_out_27), .row17(ball_1_out_28), .row18(ball_1_out_29), .row19(ball_1_out_30),
    .row20(ball_1_out_31), .row21(ball_1_out_32), .row22(ball_1_out_33), .row23(ball_1_out_34),
    .row24(ball_1_out_35), .row25(ball_1_out_36), .row26(ball_1_out_37), .row27(ball_1_out_38),
    .row28(ball_1_out_39), .row29(ball_1_out_40));
  DotMatrix #(.inputtype("row"), .matrixcols(32), .matrixrows(1)) dotmatrix_3 (.row0(or_4_out));
  collisionCheck u_EVENT_HIT_PLAYER (
    .player_x(player_x), .player_x_1(player_1_player_x_1), .player_x_1_2(player_1_player_x_1_2),
    .ball_x(ball_1_ball_x), .ball_y(ball_1_ball_y), .coordinate_to_check(5'b11110),
    .hit_x(EVENT_HIT_PLAYER_hit_x), .hit_x_1(EVENT_HIT_PLAYER_hit_x_1),
    .hit_x_1_2(EVENT_HIT_PLAYER_hit_x_1_2), .hit_x_2(EVENT_HIT_PLAYER_hit_x_2),
    .hit_x_2_2(EVENT_HIT_PLAYER_hit_x_2_2));
  Hex_Digit_Display hex_digit_display_1 (.value(bit_extender_1_out));  // open: dp
  Bit_Extender #(.out_width(4)) bit_extender_1 (.in(divider_1_out), .out(bit_extender_1_out));
  Divider divider_2 (.a(divider_1_rem), .b(8'ha), .out(divider_2_out), .rem(divider_2_rem));  // open: upper
  Bit_Extender #(.out_width(4)) bit_extender_2 (.in(divider_2_out), .out(bit_extender_2_out));
  S_R_Flip_Flop #(.trigger("high")) s_r_ff_1 (
    .S(or_5_out), .clk(game_clk), .R(or_2_out), .Q(game_active));  // open: Qn, preset, reset, en
  Pull_Resistor pull_resistor_1 (.node(data));
  Decoder decoder_1 (.out0(code), .out1(data), .sel(cdm_8_mark5_1_data_inst), .en(mem));
  Pull_Resistor pull_resistor_2 (.node(code));
  // Probe on cdm_8_mark5_1_ps
  CdM_8_mark5 cdm_8_mark5_1 (
    .clock(cdm8_clk), .addr({cdm_8_mark5_1_addr, I_O_addr}), .mem_read(rd_wr), .mem_cycle(mem),
    .data_inst(cdm_8_mark5_1_data_inst), .data_out(cdm_8_mark5_1_data_out),
    .data_in(controlled_buffer_2_out), .r0(cdm_8_mark5_1_r0), .r1(cdm_8_mark5_1_r1), .r2(cdm_8_mark5_1_r2),
    .r3(cdm_8_mark5_1_r3), .PC(cdm_8_mark5_1_pc), .SP(cdm_8_mark5_1_sp), .PS(cdm_8_mark5_1_ps), .IAck(IAck),
    .IRQ(IRQ), .vec(vec));
  assign I_O_data_read = not_3_out ? cdm_8_mark5_1_data_out : 8'bz;  // Controlled_Buffer controlled_buffer_1
  not not_3 (not_3_out, rd_wr);
  assign controlled_buffer_2_out = rd_wr ? I_O_data_read : 8'bz;  // Controlled_Buffer controlled_buffer_2
  or or_6 (or_6_out[0], EVENT_HIT_AI_hit_x, EVENT_HIT_AI_hit_x_1, EVENT_HIT_AI_hit_x_1_2, EVENT_HIT_AI_hit_x_2, EVENT_HIT_AI_hit_x_2_2);
  Hex_Digit_Display hex_digit_display_2 (.value(bit_extender_2_out));  // open: dp
  Hex_Digit_Display hex_digit_display_3 (.value(bit_extender_3_out));  // open: dp
  Bit_Extender #(.out_width(4)) bit_extender_3 (.in(divider_2_rem), .out(bit_extender_3_out));
  Button button_1 (.out(R));
  Button button_2 (.out(L));
  LED led_1 ();  // open: in
  LED led_2 ();  // open: in
  Hex_Digit_Display hex_digit_display_4 (.value(counter_1_q));  // open: dp
  Counter #(.width(4), .max('hf)) counter_1 (
    .Q(counter_1_q), .clk(comparator_1_eq), .clr(or_8_out));  // open: load, D, count, carry
  Counter #(.width(4), .max('hf)) counter_2 (
    .Q(counter_2_q), .clk(comparator_2_eq), .clr(or_8_out));  // open: load, D, count, carry
  Priority_Encoder #(.select(2)) priority_encoder_1 (
    .in0(1'b1), .in1(init_table), .in2(name), .out(priority_encoder_1_out));  // open: in3, gs, en_out, en_in
  Button button_3 (.out(Reset));
  Hex_Digit_Display hex_digit_display_5 (.value(counter_2_q));  // open: dp
  Multiplexer #(.select(2), .width(8), .enable("false")) multiplexer_1 (
    .in0({cdm_8_mark5_1_addr, I_O_addr}), .in1(init_addr), .in2(buff_addr), .out(multiplexer_1_out),
    .sel(priority_encoder_1_out));  // open: in3
  Comparator #(.width(4), .mode("unsigned")) comparator_3 (
    .a(counter_1_q), .b(4'b0101), .eq(comparator_3_eq));  // open: gt, lt
  or or_7 (or_7_out, comparator_3_eq, comparator_4_eq);
  Comparator #(.width(4), .mode("unsigned")) comparator_4 (
    .a(counter_2_q), .b(4'b0101), .eq(comparator_4_eq));  // open: gt, lt
  or or_8 (or_8_out, Reset, or_7_out);
  D_Flip_Flop d_ff_1 (.clk(or_7_out), .D(or_7_out), .Q(player_loser), .reset(and_1_out));  // open: Qn, preset, en
  and and_1 (and_1_out, IAck, arbiter_1_vec);
  Multiplexer #(.select(2), .width(8), .enable("false")) multiplexer_2 (
    .in0(I_O_data_read), .in1(init_data), .in2(buff_data), .out(multiplexer_2_out),
    .sel(priority_encoder_1_out));  // open: in3
  or or_9 (or_9_out, EVENT_HIT_AI_hit_x, EVENT_HIT_PLAYER_hit_x);
  or or_10 (or_10_out, EVENT_HIT_AI_hit_x_1, EVENT_HIT_AI_hit_x_2, EVENT_HIT_PLAYER_hit_x_1, EVENT_HIT_PLAYER_hit_x_2);
  or or_11 (or_11_out, EVENT_HIT_AI_hit_x_1_2, EVENT_HIT_PLAYER_hit_x_1_2, EVENT_HIT_AI_hit_x_2_2, EVENT_HIT_PLAYER_hit_x_2_2);
  or or_12 (event_hit_player, EVENT_HIT_PLAYER_hit_x, EVENT_HIT_PLAYER_hit_x_1, EVENT_HIT_PLAYER_hit_x_1_2, EVENT_HIT_PLAYER_hit_x_2, EVENT_HIT_PLAYER_hit_x_2_2);
  freeze freeze_1 (
    .game_clk(game_clk), .hit_x(EVENT_HIT_PLAYER_hit_x), .hit_x_1(EVENT_HIT_PLAYER_hit_x_1),
    .hit_x_1_2(EVENT_HIT_PLAYER_hit_x_1_2), .btn_left(L), .btn_right(R), .freeze(freeze));
  or or_13 (or_13_out, EVENT_HIT_AI_hit_x_1, EVENT_HIT_PLAYER_hit_x_1);
  or or_14 (or_14_out[0], or_13_out, or_15_out);
  or or_15 (or_15_out, EVENT_HIT_AI_hit_x_1_2, EVENT_HIT_PLAYER_hit_x_1_2);
  or or_16 (or_16_out, EVENT_HIT_AI_hit_x_2, EVENT_HIT_PLAYER_hit_x_2);
  or or_17 (or_14_out[1], or_16_out, or_18_out);
  or or_18 (or_18_out, EVENT_HIT_AI_hit_x_2_2, EVENT_HIT_PLAYER_hit_x_2_2);
  or or_19 (or_19_out, or_6_out[0], event_hit_player);
  and and_2 (I_O_sel, cdm_8_mark5_1_addr[4], cdm_8_mark5_1_addr[5], cdm_8_mark5_1_addr[6], cdm_8_mark5_1_addr[7], data);
  not not_4 (not_4_out, rd_wr);
  Multiplexer #(.select(2), .enable("false")) multiplexer_3 (
    .in0(RAM), .in1(init_table), .in2(buff_sel), .out(multiplexer_3_out), .sel(priority_encoder_1_out));  // open: in3
  or or_20 (or_20_out, or_10_out, or_11_out);
  D_Flip_Flop #(.trigger("falling")) d_ff_2 (
    .clk(or_19_out), .D(dY), .Q(d_ff_2_q), .en(game_active), .reset(not_5_out));  // open: Qn, preset
  not not_5 (not_5_out, game_active);
  and and_3 (RAM, ~I_O_sel, data);  // AND_Gate
  ROM rom_1 (.addr({cdm_8_mark5_1_addr, I_O_addr}), .data(I_O_data_read), .sel(code));
  RAM #(.bus("separate")) ram_1 (
    .addr(multiplexer_1_out), .din(multiplexer_2_out), .data(I_O_data_read), .str(not_4_out),
    .sel(multiplexer_3_out), .clk(cdm8_clk), .ld(rd_wr));  // open: clr
  Register #(.width(2)) Angle_Reg (.D(or_14_out), .en(or_19_out), .Q(Angle_Reg_q), .clk(game_clk), .clr(not_6_out));
  not not_6 (not_6_out, game_active);
  Multiplexer #(.select(2), .enable("false")) multiplexer_4 (
    .in0(d_ff_2_q), .in1(1'b0), .in2(1'b1), .in3(1'b0), .out(dY), .sel({event_hit_player, or_6_out[0]}));
  Multiplexer #(.select(2), .width(5), .enable("false")) multiplexer_5 (
    .in0(5'b01000), .in1(5'b10000), .in2({5{1'b1}}), .out(slope_x), .sel(Angle_Reg_q));  // open: in3
  not not_7 (not_7_out, event_hit_player);
  Comparator #(.width(4), .mode("unsigned")) comparator_5 (
    .a(I_O_addr), .b(4'b0001), .eq(comparator_5_eq));  // open: gt, lt
  Comparator #(.width(4), .mode("unsigned")) comparator_6 (
    .a(I_O_addr), .b(4'b0010), .eq(comparator_6_eq));  // open: gt, lt
  Comparator #(.width(4), .mode("unsigned")) comparator_7 (
    .a(I_O_addr), .b(4'b0011), .eq(comparator_7_eq));  // open: gt, lt
  and and_4 (and_4_out, L, freeze);
  not not_8 (not_8_out, freeze);
  and and_5 (and_5_out, freeze, R);
  Multiplexer #(.select(2), .width(5), .enable("false")) multiplexer_6 (
    .in0({5{1'b1}}), .in1(5'b10000), .in2(5'b01000), .out(slope_y), .sel(Angle_Reg_q));  // open: in3
  Counter #(.width(4), .max('h5)) counter_3 (
    .carry(counter_3_carry), .clk(s_r_ff_2_q), .clr(and_9_out));  // open: load, D, count, Q
  Counter counter_4 (.Q(player_score), .clk(s_r_ff_2_q), .clr(and_9_out));  // open: load, D, count, carry
  S_R_Flip_Flop #(.trigger("falling")) s_r_ff_2 (
    .S(event_hit_player), .clk(game_clk), .R(not_7_out), .Q(s_r_ff_2_q));  // open: Qn, preset, reset, en
  LED led_3 (.in(and_6_out));
  and and_6 (and_6_out, comparator_5_eq, I_O_sel);
  and and_7 (and_7_out, comparator_6_eq, I_O_sel);
  and and_8 (and_8_out, comparator_7_eq, I_O_sel);
  Comparator #(.width(5), .mode("unsigned")) comparator_8 (
    .a(ball_1_ball_x), .b({5{1'b0}}), .eq(comparator_8_eq));  // open: gt, lt
  Comparator #(.width(5), .mode("unsigned")) comparator_9 (
    .a(ball_1_ball_x), .b({5{1'b1}}), .eq(comparator_9_eq));  // open: gt, lt
  D_Flip_Flop #(.trigger("falling")) d_ff_3 (
    .clk(game_clk), .D(counter_3_carry), .Qn(d_ff_3_qn));  // open: Q, preset, en, reset
  and and_9 (and_9_out, ~rd_wr, and_6_out);  // AND_Gate
  D_Flip_Flop #(.trigger("falling")) d_ff_4 (
    .clk(cdm8_clk), .D(I_O_data_read[0]), .Q(d_ff_4_q[0]), .en(and_10_out));  // open: Qn, preset, reset
  and and_10 (and_10_out, ~rd_wr, and_7_out);  // AND_Gate
  assign I_O_data_read = and_11_out ? player_score : 8'bz;  // Controlled_Buffer controlled_buffer_3
  and and_11 (and_11_out, rd_wr, and_8_out);
  or or_21 (or_21_out, or_9_out, or_20_out, s_r_ff_3_q, s_r_ff_4_q, or_22_out);
  S_R_Flip_Flop #(.trigger("falling")) s_r_ff_3 (
    .S(and_4_out), .clk(game_clk), .R(not_8_out), .Q(s_r_ff_3_q));  // open: Qn, preset, reset, en
  S_R_Flip_Flop #(.trigger("falling")) s_r_ff_4 (
    .S(and_5_out), .clk(game_clk), .R(not_8_out), .Q(s_r_ff_4_q));  // open: Qn, preset, reset, en
  or or_22 (or_22_out, comparator_8_eq, comparator_9_eq);
  and and_12 (and_12_out, d_ff_3_qn, counter_3_carry);
  Counter #(.width(3), .max('h7), .ongoal("stay")) counter_5 (
    .count(and_12_out), .Q(counter_5_q), .clk(game_clk), .clr(and_9_out));  // open: load, D, carry
  Bit_Extender #(.out_width(7)) bit_extender_4 (.in(I_O_data_read), .out(bit_extender_4_out));
  TTY #(.rows(7), .cols(22), .trigger("falling")) tty_1 (
    .data(bit_extender_4_out), .clk(cdm8_clk), .we(and_9_out));  // open: clr
  TTY #(.rows(1), .cols(22)) tty_2 (.data(keyboard_1_data), .clk(cdm8_clk), .we(and_13_out), .clr(button_4_out));
  and and_13 (and_13_out, not_9_out, is_valid);
  Keyboard keyboard_1 (
    .clk(cdm8_clk), .re(not_9_out), .clr(s_r_ff_5_qn), .avail(keyboard_1_avail), .data(keyboard_1_data));
  not not_9 (not_9_out, s_r_ff_5_qn);
  and and_14 (and_14_out, rd_wr, and_7_out);
  D_Flip_Flop #(.trigger("falling")) d_ff_5 (.clk(or_21_out), .D(dX), .Q(d_ff_5_q));  // open: Qn, preset, en, reset
  Priority_Encoder priority_encoder_2 (
    .in0(1'b1), .in1(or_10_out), .in2(or_11_out), .in3(s_r_ff_3_q), .in4(s_r_ff_4_q), .in5(comparator_9_eq),
    .in6(comparator_8_eq), .out(priority_encoder_2_out));  // open: in7, en_in, gs, en_out
  and and_15 (kbd_sel, keyboard_1_avail, is_valid);
  assign I_O_data_read = and_14_out ? {player_loser, {6{1'b0}}, d_ff_4_q[0]} : 8'bz;  // Controlled_Buffer controlled_buffer_4
  Multiplexer #(.select(3), .enable("false")) multiplexer_7 (
    .in0(d_ff_5_q), .in1(1'b0), .in2(1'b1), .in3(1'b0), .in4(1'b1), .in5(1'b1), .in6(1'b0), .out(dX),
    .sel(priority_encoder_2_out));  // open: in7
  // Probe on speed
  Multiplexer #(.select(3), .width(8), .enable("false")) multiplexer_8 (
    .in0(8'h40), .in1(8'h38), .in2(8'h35), .in3(8'h30), .in4(8'h28), .in5(8'h25), .in6(8'h20), .in7(8'h15),
    .out(speed), .sel(counter_5_q));
  and and_16 (and_16_out, d_ff_4_q[0], player_loser);
  assign bit_extender_5_out = {{1{1'b0}}, keyboard_1_data};  // Bit_Extender bit_extender_5
  Comparator #(.mode("unsigned")) comparator_10 (
    .a(bit_extender_5_out), .b(8'h8), .eq(comparator_10_eq));  // open: gt, lt
  Comparator #(.width(7), .mode("unsigned")) comparator_11 (
    .a(keyboard_1_data), .b(7'b0100000), .eq(comparator_11_eq));  // open: gt, lt
  Comparator #(.width(7), .mode("unsigned")) comparator_12 (
    .a(keyboard_1_data), .b(7'b1011111), .eq(comparator_12_eq));  // open: gt, lt
  Comparator #(.width(7), .mode("unsigned")) comparator_13 (
    .a(keyboard_1_data), .b(7'b0001000), .eq(comparator_13_eq));  // open: gt, lt
  Comparator #(.width(7), .mode("unsigned")) comparator_14 (
    .a(keyboard_1_data), .b(7'b1000000), .gt(comparator_14_gt));  // open: eq, lt
  Comparator #(.width(7), .mode("unsigned")) comparator_15 (
    .a(keyboard_1_data), .b(7'b1011011), .lt(comparator_15_lt));  // open: gt, eq
  Comparator #(.width(7), .mode("unsigned")) comparator_16 (
    .a(keyboard_1_data), .b(7'b1100000), .gt(comparator_16_gt));  // open: eq, lt
  Comparator #(.width(7), .mode("unsigned")) comparator_17 (
    .a(keyboard_1_data), .b(7'b1111011), .lt(comparator_17_lt));  // open: gt, eq
  Multiplexer #(.width(8), .enable("false")) multiplexer_9 (
    .in0(bit_extender_5_out), .in1({8{1'b0}}), .out(kbd_data), .sel(comparator_10_eq));
  Counter #(.width(4), .max('h8), .ongoal("stay"), .trigger("falling")) counter_6 (
    .load(comparator_10_eq), .Q(counter_6_q), .carry(counter_6_carry), .clk(kbd_sel), .clr(s_r_ff_5_qn));  // open: D, count
  or or_23 (is_valid, comparator_11_eq, comparator_12_eq, comparator_13_eq, and_17_out, and_18_out);
  and and_17 (and_17_out, comparator_14_gt, comparator_15_lt);
  and and_18 (and_18_out, comparator_16_gt, comparator_17_lt);
  not not_10 (not_10_out, Reset);
  xnor xnor_3 (xnor_3_out, Reset, not_10_out);
  Button button_4 (.out(button_4_out));
  S_R_Flip_Flop s_r_ff_5 (
    .S(button_4_out), .clk(cdm8_clk), .R(comparator_18_eq), .Q(name), .Qn(s_r_ff_5_qn), .reset(or_24_out));  // open: preset, en
  Comparator #(.mode("unsigned")) comparator_18 (
    .a(bit_extender_5_out), .b(8'ha), .eq(comparator_18_eq));  // open: gt, lt
  or or_24 (or_24_out, comparator_18_eq, player_loser, counter_6_carry);
  assign kbd_addr = {{4{1'b0}}, counter_6_q};  // Bit_Extender bit_extender_6
  assign vec = arbiter_1_vec ? 3'b100 : 3'bz;  // Controlled_Buffer controlled_buffer_5
  arbiter arbiter_1 (
    .IReq_2(IRQ), .IAck(IAck), .IReq(arbiter_1_iack_2), .IAck_2(arbiter_1_iack_2), .vec(arbiter_1_vec),
    .req(and_16_out), .done(and_11_out), .clock(cdm8_clk));
  S_R_Flip_Flop #(.trigger("high")) s_r_ff_6 (
    .S(xnor_3_out), .clk(cdm8_clk), .R(counter_8_carry), .Q(init_table), .reset(counter_8_carry));  // open: Qn, preset, en
  D_Flip_Flop d_ff_6 (
    .clk(button_4_out), .D(button_4_out), .Q(d_ff_6_q), .reset(counter_7_carry));  // open: Qn, preset, en
  Counter #(.width(4), .max('h8), .ongoal("stay")) counter_7 (
    .count(button_4_out), .Q(counter_7_q), .carry(counter_7_carry), .clk(cdm8_clk), .clr(s_r_ff_5_qn));  // open: load, D
  Counter #(.width(6), .max('h2c), .ongoal("stay")) counter_8 (
    .count(init_table), .Q(counter_8_q), .carry(counter_8_carry), .clk(cdm8_clk), .clr(xnor_3_out));  // open: load, D
  assign bit_extender_7_out = {{2{1'b0}}, counter_8_q};  // Bit_Extender bit_extender_7
  assign bit_extender_8_out = {{4{1'b0}}, counter_7_q};  // Bit_Extender bit_extender_8
  Adder adder_1 (.a(bit_extender_7_out), .b(8'h10), .out(init_addr));  // open: cin, cout
  Multiplexer #(.enable("false")) multiplexer_10 (.in0(kbd_sel), .in1(d_ff_6_q), .out(buff_sel), .sel(d_ff_6_q));
  Multiplexer #(.width(8), .enable("false")) multiplexer_11 (
    .in0(kbd_addr), .in1(bit_extender_8_out), .out(buff_addr), .sel(d_ff_6_q));
  Multiplexer #(.width(8), .enable("false")) multiplexer_12 (
    .in0(kbd_data), .in1({8{1'b0}}), .out(buff_data), .sel(d_ff_6_q));
  ROM rom_2 (.addr(bit_extender_7_out), .data(init_data), .sel(1'b1));
  // also tied to GND on the sheet: arbiter_1_iack_2

  // Other names for the same wires on the sheet: I_O_data_write[7:0] = I_O_data_read

  // Notes on the sheet:
  //   EVENT_HIT_TOP_WALL
  //   EVENT_HIT_BOTTOM_WALL
  //   PLAYER_SCORE
  //   PLAYER
  //   START / RESET
  //   AI
  //   ldi r0, 0xf0
  //   ldi r1, 1
  //   st r0, r1
  //   status = 10000000b  если символ готов 
  //   status = 00000001b  если прерывания разрешены 
  //   vec == 4
  //   status = 10000001b  если и символ готов, и прерывания разрешены
  //   right_hit_any
  //   Чтобы разрешить прерывания от клавиатуры, программа должна записать 1 в бит 0 регистра 0xf0
  //   center_hit_any
  //   left_hit_any
  //   border_hit
  //   corner_hit
  //   instr_mem
  //   contents of rom_1 (hex, n*v repeats v):
  //   cd f0 d0 3d d1 10 d2 5 a e0 16 a1 d3 0 a7 8c d3 9 1d 8a ee 8 d0 f0 d1 1 a1 d0 f2 a1 c1 d1 26 c1 d1
  //   80 c1 d9 c5 d5 ee 27 d4 ce d0 f3 b1 d0 3d d2 42 72 e0 44 b2 bb 77 ec 3e 8c ee 42 d6 48 ee 44 ee 31
  //   d6 70 cf d9 d2 41 bb ad c0 c1 c2 c3 d 8d d0 0 d2 8 a e0 60 b3 a7 8c 8d 8a ee 56 c7 c6 c5 c4 78 e0 6e
  //   9 89 b5 a9 8a ee 64 a3 d7 d0 3d d3 5 f e0 9d b2 c2 ba c0 c3 d6 a1 c7 c4 d1 f1 d2 20 a6 c6 8e c0 c3
  //   d3 8 f e0 94 b8 a4 8e 8b ee 8b c7 c4 d2 a a6 8c 8b ee 74 d2 a a6 d7 d1 f1 d0 0 d3 64 7b eb af 3b e
  //   8c ee a5 d3 30 13 a7 d0 0 d3 a 7b eb bf 3b e 8c ee b5 d3 30 13 a7 d3 30 1b a7 d7 44*0 2a 0 0 0 2b
  //   data_mem
  //   EVENT_HIT_RIGHT_WALL
  //   EVENT_HIT_LEFT_WALL
  //   0xf2  -> status register 
  //   0xf3  -> data register 
  //   Пробел
  //   Нижнее подчеркивание
  //   Стереть
  //   A-Z
  //   a-z
  //   ВВЕСТИ ИМЯ
  //   cleaning
  //   contents of rom_2 (hex, n*v repeats v):
  //   0 49 72 74 65 67 6f 76 0 0 4e 61 7a 61 72 6f 76 0 0 42 6f 6e 64 61 72 65 76 0 49 76 61 6e 6f 76 0 0
  //   0 50 65 74 72 6f 76
endmodule

module player (
  input  btn_left,
  input  btn_right,
  input  game_active,
  input  Clk,
  output [31:0] player_screen_pixel,
  output [4:0] player_x,
  output [4:0] player_x_1,
  output [4:0] player_x_1_2
);

  wire and_1_out, and_2_out, comparator_1_eq, comparator_2_eq, not_1_out;
  wire [4:0] multiplexer_1_out, multiplexer_2_out, multiplexer_3_out;
  wire [31:0] decoder_1_out0, shifter_1_out, shifter_2_out;

  not not_1 (not_1_out, game_active);
  Multiplexer #(.width(5), .enable("false")) multiplexer_1 (
    .in0(multiplexer_3_out), .in1(5'b01111), .out(multiplexer_1_out), .sel(not_1_out));
  Register #(.width(5), .trigger("falling")) X (.D(multiplexer_1_out), .Q(player_x), .clk(Clk));  // open: en, clr
  Decoder #(.select(5), .enable("false")) decoder_1 (
    .out0(decoder_1_out0[0]), .out1(decoder_1_out0[1]), .out2(decoder_1_out0[2]), .out3(decoder_1_out0[3]),
    .out4(decoder_1_out0[4]), .out5(decoder_1_out0[5]), .out6(decoder_1_out0[6]), .out7(decoder_1_out0[7]),
    .out8(decoder_1_out0[8]), .out9(decoder_1_out0[9]), .out10(decoder_1_out0[10]),
    .out11(decoder_1_out0[11]), .out12(decoder_1_out0[12]), .out13(decoder_1_out0[13]),
    .out14(decoder_1_out0[14]), .out15(decoder_1_out0[15]), .out16(decoder_1_out0[16]),
    .out17(decoder_1_out0[17]), .out18(decoder_1_out0[18]), .out19(decoder_1_out0[19]),
    .out20(decoder_1_out0[20]), .out21(decoder_1_out0[21]), .out22(decoder_1_out0[22]),
    .out23(decoder_1_out0[23]), .out24(decoder_1_out0[24]), .out25(decoder_1_out0[25]),
    .out26(decoder_1_out0[26]), .out27(decoder_1_out0[27]), .out28(decoder_1_out0[28]),
    .out29(decoder_1_out0[29]), .out30(decoder_1_out0[30]), .out31(decoder_1_out0[31]), .sel(player_x));
  Shifter #(.width(32)) shifter_1 (.in(decoder_1_out0), .\dist (5'b00001), .out(shifter_1_out));
  Shifter #(.width(32), .shift("lr")) shifter_2 (.in(decoder_1_out0), .\dist (5'b00001), .out(shifter_2_out));
  Adder #(.width(5)) adder_1 (.a(player_x), .b(5'b00001), .out(player_x_1));  // open: cin, cout
  Subtractor #(.width(5)) subtractor_1 (.a(player_x), .b(5'b00001), .out(player_x_1_2));  // open: bin, bout
  Comparator #(.width(5), .mode("unsigned")) comparator_1 (
    .a(player_x), .b(5'b11110), .eq(comparator_1_eq));  // open: gt, lt
  Comparator #(.width(5), .mode("unsigned")) comparator_2 (
    .a(player_x), .b(5'b00001), .eq(comparator_2_eq));  // open: gt, lt
  assign player_screen_pixel = shifter_1_out | decoder_1_out0 | shifter_2_out;  // OR_Gate or_1, 32 bits wide
  Multiplexer #(.width(5), .enable("false")) multiplexer_2 (
    .in0(player_x), .in1(player_x_1), .out(multiplexer_2_out), .sel(and_1_out));
  and and_1 (and_1_out, btn_left, ~comparator_1_eq);  // AND_Gate
  and and_2 (and_2_out, btn_right, ~comparator_2_eq);  // AND_Gate
  Multiplexer #(.width(5), .enable("false")) multiplexer_3 (
    .in0(multiplexer_2_out), .in1(player_x_1_2), .out(multiplexer_3_out), .sel(and_2_out));

  // Other names for the same wires on the sheet: Left = btn_left; Right = btn_right
endmodule

module ai (
  input  Clk,
  input  game_active,
  input  [4:0] ball_x,
  input  [4:0] ball_y,
  input  ball_dx,
  input  ball_dy,
  input  [4:0] player_x,
  output [31:0] ai_screen_pixel,
  output [4:0] ai_x,
  output [4:0] ai_x_1,
  output [4:0] ai_x_1_2
);

  wire and_1_out, and_2_out, comparator_1_gt, comparator_2_eq, comparator_3_eq, comparator_5_lt, Left,
       not_1_out, Right;
  wire [4:0] adder_3_out, bit_extender_3_out, multiplexer_2_out, multiplexer_5_out, multiplexer_6_out,
       multiplexer_7_out, multiplexer_8_out, subtractor_5_out;
  wire [7:0] adder_1_out, bit_extender_1_out, bit_extender_2_out, multiplexer_1_out, multiplexer_3_out,
       multiplexer_4_out, subtractor_1_out, subtractor_2_out, subtractor_3_out;
  wire [31:0] decoder_1_out0, shifter_1_out, shifter_2_out;

  assign bit_extender_1_out = {{3{1'b0}}, ball_x};  // Bit_Extender bit_extender_1
  assign bit_extender_2_out = {{3{1'b0}}, ball_y};  // Bit_Extender bit_extender_2
  Adder adder_1 (.a(bit_extender_1_out), .b(bit_extender_2_out), .out(adder_1_out));  // open: cin, cout
  Subtractor subtractor_1 (.a(bit_extender_1_out), .b(bit_extender_2_out), .out(subtractor_1_out));  // open: bin, bout
  not not_1 (not_1_out, game_active);
  Multiplexer #(.width(8), .enable("false")) multiplexer_1 (
    .in0(adder_1_out), .in1(subtractor_1_out), .out(multiplexer_1_out), .sel(ball_dx));
  Multiplexer #(.width(5), .enable("false")) multiplexer_2 (
    .in0(multiplexer_6_out), .in1(5'b01111), .out(multiplexer_2_out), .sel(not_1_out));
  Multiplexer #(.width(8), .enable("false")) multiplexer_3 (
    .in0(multiplexer_1_out), .in1(subtractor_2_out), .out(multiplexer_3_out), .sel(multiplexer_1_out[7]));
  Subtractor subtractor_2 (.a({8{1'b0}}), .b(multiplexer_1_out), .out(subtractor_2_out));  // open: bin, bout
  Decoder #(.select(5), .enable("false")) decoder_1 (
    .out0(decoder_1_out0[0]), .out1(decoder_1_out0[1]), .out2(decoder_1_out0[2]), .out3(decoder_1_out0[3]),
    .out4(decoder_1_out0[4]), .out5(decoder_1_out0[5]), .out6(decoder_1_out0[6]), .out7(decoder_1_out0[7]),
    .out8(decoder_1_out0[8]), .out9(decoder_1_out0[9]), .out10(decoder_1_out0[10]),
    .out11(decoder_1_out0[11]), .out12(decoder_1_out0[12]), .out13(decoder_1_out0[13]),
    .out14(decoder_1_out0[14]), .out15(decoder_1_out0[15]), .out16(decoder_1_out0[16]),
    .out17(decoder_1_out0[17]), .out18(decoder_1_out0[18]), .out19(decoder_1_out0[19]),
    .out20(decoder_1_out0[20]), .out21(decoder_1_out0[21]), .out22(decoder_1_out0[22]),
    .out23(decoder_1_out0[23]), .out24(decoder_1_out0[24]), .out25(decoder_1_out0[25]),
    .out26(decoder_1_out0[26]), .out27(decoder_1_out0[27]), .out28(decoder_1_out0[28]),
    .out29(decoder_1_out0[29]), .out30(decoder_1_out0[30]), .out31(decoder_1_out0[31]), .sel(ai_x));
  Register #(.width(5), .trigger("falling")) register_1 (.D(multiplexer_2_out), .Q(ai_x), .clk(Clk));  // open: en, clr
  Subtractor subtractor_3 (.a(8'h3e), .b(multiplexer_3_out), .out(subtractor_3_out));  // open: bin, bout
  Comparator #(.mode("unsigned")) comparator_1 (
    .a(multiplexer_3_out), .b(8'h1f), .gt(comparator_1_gt));  // open: eq, lt
  Shifter #(.width(32)) shifter_1 (.in(decoder_1_out0), .\dist (5'b00001), .out(shifter_1_out));
  Shifter #(.width(32), .shift("lr")) shifter_2 (.in(decoder_1_out0), .\dist (5'b00001), .out(shifter_2_out));
  Adder #(.width(5)) adder_2 (.a(ai_x), .b(5'b00001), .out(ai_x_1));  // open: cin, cout
  Subtractor #(.width(5)) subtractor_4 (.a(ai_x), .b(5'b00001), .out(ai_x_1_2));  // open: bin, bout
  Comparator #(.width(5), .mode("unsigned")) comparator_2 (
    .a(ai_x), .b(5'b11110), .eq(comparator_2_eq));  // open: gt, lt
  Comparator #(.width(5), .mode("unsigned")) comparator_3 (
    .a(ai_x), .b(5'b00001), .eq(comparator_3_eq));  // open: gt, lt
  Comparator #(.width(5), .mode("unsigned")) comparator_4 (
    .a(multiplexer_7_out), .b(ai_x), .lt(Right));  // open: gt, eq
  Multiplexer #(.width(8), .enable("false")) multiplexer_4 (
    .in0(multiplexer_3_out), .in1(subtractor_3_out), .out(multiplexer_4_out), .sel(comparator_1_gt));
  assign ai_screen_pixel = shifter_1_out | decoder_1_out0 | shifter_2_out;  // OR_Gate or_1, 32 bits wide
  Multiplexer #(.width(5), .enable("false")) multiplexer_5 (
    .in0(ai_x), .in1(ai_x_1), .out(multiplexer_5_out), .sel(and_1_out));
  and and_1 (and_1_out, Left, ~comparator_2_eq);  // AND_Gate
  and and_2 (and_2_out, Right, ~comparator_3_eq);  // AND_Gate
  Bit_Extender #(.out_width(5)) bit_extender_3 (.in(multiplexer_4_out), .out(bit_extender_3_out));
  Multiplexer #(.width(5), .enable("false")) multiplexer_6 (
    .in0(multiplexer_5_out), .in1(ai_x_1_2), .out(multiplexer_6_out), .sel(and_2_out));
  Subtractor #(.width(5)) subtractor_5 (
    .a(bit_extender_3_out), .b(5'b00001), .out(subtractor_5_out));  // open: bin, bout
  Adder #(.width(5)) adder_3 (.a(bit_extender_3_out), .b(5'b00001), .out(adder_3_out));  // open: cin, cout
  Comparator #(.width(5), .mode("unsigned")) comparator_5 (
    .a(bit_extender_3_out), .b(player_x), .lt(comparator_5_lt));  // open: gt, eq
  Comparator #(.width(5), .mode("unsigned")) comparator_6 (
    .a(multiplexer_7_out), .b(ai_x_1), .gt(Left));  // open: eq, lt
  Multiplexer #(.width(5), .enable("false")) multiplexer_7 (
    .in0(5'b01111), .in1(multiplexer_8_out), .out(multiplexer_7_out), .sel(ball_dy));
  Multiplexer #(.width(5), .enable("false")) multiplexer_8 (
    .in0(subtractor_5_out), .in1(adder_3_out), .out(multiplexer_8_out), .sel(comparator_5_lt));

  // Notes on the sheet:
  //   Ricochet off the RIGHT wall
  //   Ricochet off the LEFT wall
  //   Pred_X
endmodule

module ball (
  input  dX,
  input  dY,
  input  game_active,
  input  clk,
  input  [4:0] slope_x,
  input  [4:0] slope_y,
  input  freeze,
  input  [4:0] player_x,
  output [4:0] ball_x,
  output [31:0] out_10,
  output [31:0] out_11,
  output [31:0] out_12,
  output [31:0] out_13,
  output [31:0] out_14,
  output [31:0] out_15,
  output [31:0] out_16,
  output [31:0] out_17,
  output [31:0] out_18,
  output [31:0] out_19,
  output [31:0] out_20,
  output [31:0] out_21,
  output [31:0] out_22,
  output [31:0] out_23,
  output [31:0] out_24,
  output [31:0] out_25,
  output [31:0] out_26,
  output [31:0] out_27,
  output [31:0] out_28,
  output [31:0] out_29,
  output [31:0] out_30,
  output [31:0] out_31,
  output [31:0] out_32,
  output [31:0] out_33,
  output [31:0] out_34,
  output [31:0] out_35,
  output [31:0] out_36,
  output [31:0] out_37,
  output [31:0] out_38,
  output [31:0] out_39,
  output [31:0] out_40,
  output [31:0] out_41,
  output [4:0] ball_y
);

  wire adder_1_cout, adder_2_cout, and_1_out, decoder_2_out0, decoder_2_out1, decoder_2_out2, decoder_2_out3,
       decoder_2_out4, decoder_2_out5, decoder_2_out6, decoder_2_out7, decoder_2_out8, decoder_2_out9,
       decoder_2_out10, decoder_2_out11, decoder_2_out12, decoder_2_out13, decoder_2_out14, decoder_2_out15,
       decoder_2_out16, decoder_2_out17, decoder_2_out18, decoder_2_out19, decoder_2_out20, decoder_2_out21,
       decoder_2_out22, decoder_2_out23, decoder_2_out24, decoder_2_out25, decoder_2_out26, decoder_2_out27,
       decoder_2_out28, decoder_2_out29, decoder_2_out30, decoder_2_out31, not_1_out, not_2_out, or_1_out,
       or_2_out;
  wire [4:0] adder_1_out, adder_2_out, adder_3_out, adder_4_out, Error_Reg_X_q, Error_Reg_Y_q,
       multiplexer_1_out, multiplexer_2_out, multiplexer_3_out, multiplexer_4_out, multiplexer_5_out,
       subtractor_1_out, subtractor_2_out;
  wire [31:0] decoder_1_out0;

  not not_1 (not_1_out, game_active);
  not not_2 (not_2_out, game_active);
  Register #(.width(5)) Error_Reg_X (.D(adder_1_out), .Q(Error_Reg_X_q), .clk(clk), .clr(not_1_out));  // open: en
  Register #(.width(5)) Error_Reg_Y (.D(adder_2_out), .Q(Error_Reg_Y_q), .clk(clk), .clr(not_2_out));  // open: en
  Multiplexer #(.width(5), .enable("false")) multiplexer_1 (
    .in0(multiplexer_4_out), .in1(5'b01111), .out(multiplexer_1_out), .sel(not_1_out));
  or or_1 (or_1_out, not_1_out, adder_1_cout);
  Adder #(.width(5)) adder_1 (.a(Error_Reg_X_q), .b(slope_x), .out(adder_1_out), .cout(adder_1_cout));  // open: cin
  Multiplexer #(.width(5), .enable("false")) multiplexer_2 (
    .in0(multiplexer_5_out), .in1(5'b01111), .out(multiplexer_2_out), .sel(not_2_out));
  or or_2 (or_2_out, not_2_out, adder_2_cout);
  Adder #(.width(5)) adder_2 (.a(Error_Reg_Y_q), .b(slope_y), .out(adder_2_out), .cout(adder_2_cout));  // open: cin
  Multiplexer #(.width(5), .enable("false")) multiplexer_3 (
    .in0(multiplexer_1_out), .in1(player_x), .out(multiplexer_3_out), .sel(freeze));
  and and_1 (and_1_out, or_2_out, ~freeze);  // AND_Gate
  Register #(.width(5)) X (.D(multiplexer_3_out), .en(or_1_out), .Q(ball_x), .clk(clk));  // open: clr
  Register #(.width(5)) Y (.D(multiplexer_2_out), .en(and_1_out), .Q(ball_y), .clk(clk));  // open: clr
  Adder #(.width(5)) adder_3 (.a(ball_x), .b(5'b00001), .out(adder_3_out));  // open: cin, cout
  Subtractor #(.width(5)) subtractor_1 (.a(ball_x), .b(5'b00001), .out(subtractor_1_out));  // open: bin, bout
  Adder #(.width(5)) adder_4 (.a(ball_y), .b(5'b00001), .out(adder_4_out));  // open: cin, cout
  Subtractor #(.width(5)) subtractor_2 (.a(ball_y), .b(5'b00001), .out(subtractor_2_out));  // open: bin, bout
  Multiplexer #(.width(5), .enable("false")) multiplexer_4 (
    .in0(adder_3_out), .in1(subtractor_1_out), .out(multiplexer_4_out), .sel(dX));
  Multiplexer #(.width(5), .enable("false")) multiplexer_5 (
    .in0(adder_4_out), .in1(subtractor_2_out), .out(multiplexer_5_out), .sel(dY));
  Decoder #(.select(5), .enable("false")) decoder_1 (
    .out0(decoder_1_out0[0]), .out1(decoder_1_out0[1]), .out2(decoder_1_out0[2]), .out3(decoder_1_out0[3]),
    .out4(decoder_1_out0[4]), .out5(decoder_1_out0[5]), .out6(decoder_1_out0[6]), .out7(decoder_1_out0[7]),
    .out8(decoder_1_out0[8]), .out9(decoder_1_out0[9]), .out10(decoder_1_out0[10]),
    .out11(decoder_1_out0[11]), .out12(decoder_1_out0[12]), .out13(decoder_1_out0[13]),
    .out14(decoder_1_out0[14]), .out15(decoder_1_out0[15]), .out16(decoder_1_out0[16]),
    .out17(decoder_1_out0[17]), .out18(decoder_1_out0[18]), .out19(decoder_1_out0[19]),
    .out20(decoder_1_out0[20]), .out21(decoder_1_out0[21]), .out22(decoder_1_out0[22]),
    .out23(decoder_1_out0[23]), .out24(decoder_1_out0[24]), .out25(decoder_1_out0[25]),
    .out26(decoder_1_out0[26]), .out27(decoder_1_out0[27]), .out28(decoder_1_out0[28]),
    .out29(decoder_1_out0[29]), .out30(decoder_1_out0[30]), .out31(decoder_1_out0[31]), .sel(ball_x));
  Decoder #(.select(5), .enable("false")) decoder_2 (
    .out0(decoder_2_out0), .out1(decoder_2_out1), .out2(decoder_2_out2), .out3(decoder_2_out3),
    .out4(decoder_2_out4), .out5(decoder_2_out5), .out6(decoder_2_out6), .out7(decoder_2_out7),
    .out8(decoder_2_out8), .out9(decoder_2_out9), .out10(decoder_2_out10), .out11(decoder_2_out11),
    .out12(decoder_2_out12), .out13(decoder_2_out13), .out14(decoder_2_out14), .out15(decoder_2_out15),
    .out16(decoder_2_out16), .out17(decoder_2_out17), .out18(decoder_2_out18), .out19(decoder_2_out19),
    .out20(decoder_2_out20), .out21(decoder_2_out21), .out22(decoder_2_out22), .out23(decoder_2_out23),
    .out24(decoder_2_out24), .out25(decoder_2_out25), .out26(decoder_2_out26), .out27(decoder_2_out27),
    .out28(decoder_2_out28), .out29(decoder_2_out29), .out30(decoder_2_out30), .out31(decoder_2_out31),
    .sel(ball_y));
  assign out_10 = decoder_2_out0 ? decoder_1_out0 : 32'bz;  // Controlled_Buffer controlled_buffer_1
  assign out_11 = decoder_2_out1 ? decoder_1_out0 : 32'bz;  // Controlled_Buffer controlled_buffer_2
  assign out_12 = decoder_2_out2 ? decoder_1_out0 : 32'bz;  // Controlled_Buffer controlled_buffer_3
  assign out_13 = decoder_2_out3 ? decoder_1_out0 : 32'bz;  // Controlled_Buffer controlled_buffer_4
  assign out_14 = decoder_2_out4 ? decoder_1_out0 : 32'bz;  // Controlled_Buffer controlled_buffer_5
  assign out_15 = decoder_2_out5 ? decoder_1_out0 : 32'bz;  // Controlled_Buffer controlled_buffer_6
  assign out_16 = decoder_2_out6 ? decoder_1_out0 : 32'bz;  // Controlled_Buffer controlled_buffer_7
  assign out_17 = decoder_2_out7 ? decoder_1_out0 : 32'bz;  // Controlled_Buffer controlled_buffer_8
  assign out_18 = decoder_2_out8 ? decoder_1_out0 : 32'bz;  // Controlled_Buffer controlled_buffer_9
  assign out_19 = decoder_2_out9 ? decoder_1_out0 : 32'bz;  // Controlled_Buffer controlled_buffer_10
  assign out_20 = decoder_2_out10 ? decoder_1_out0 : 32'bz;  // Controlled_Buffer controlled_buffer_11
  assign out_21 = decoder_2_out11 ? decoder_1_out0 : 32'bz;  // Controlled_Buffer controlled_buffer_12
  assign out_22 = decoder_2_out12 ? decoder_1_out0 : 32'bz;  // Controlled_Buffer controlled_buffer_13
  assign out_23 = decoder_2_out13 ? decoder_1_out0 : 32'bz;  // Controlled_Buffer controlled_buffer_14
  assign out_24 = decoder_2_out14 ? decoder_1_out0 : 32'bz;  // Controlled_Buffer controlled_buffer_15
  assign out_25 = decoder_2_out15 ? decoder_1_out0 : 32'bz;  // Controlled_Buffer controlled_buffer_16
  assign out_26 = decoder_2_out16 ? decoder_1_out0 : 32'bz;  // Controlled_Buffer controlled_buffer_17
  assign out_27 = decoder_2_out17 ? decoder_1_out0 : 32'bz;  // Controlled_Buffer controlled_buffer_18
  assign out_28 = decoder_2_out18 ? decoder_1_out0 : 32'bz;  // Controlled_Buffer controlled_buffer_19
  assign out_29 = decoder_2_out19 ? decoder_1_out0 : 32'bz;  // Controlled_Buffer controlled_buffer_20
  assign out_30 = decoder_2_out20 ? decoder_1_out0 : 32'bz;  // Controlled_Buffer controlled_buffer_21
  assign out_31 = decoder_2_out21 ? decoder_1_out0 : 32'bz;  // Controlled_Buffer controlled_buffer_22
  assign out_32 = decoder_2_out22 ? decoder_1_out0 : 32'bz;  // Controlled_Buffer controlled_buffer_23
  assign out_33 = decoder_2_out23 ? decoder_1_out0 : 32'bz;  // Controlled_Buffer controlled_buffer_24
  assign out_34 = decoder_2_out24 ? decoder_1_out0 : 32'bz;  // Controlled_Buffer controlled_buffer_25
  assign out_35 = decoder_2_out25 ? decoder_1_out0 : 32'bz;  // Controlled_Buffer controlled_buffer_26
  assign out_36 = decoder_2_out26 ? decoder_1_out0 : 32'bz;  // Controlled_Buffer controlled_buffer_27
  assign out_37 = decoder_2_out27 ? decoder_1_out0 : 32'bz;  // Controlled_Buffer controlled_buffer_28
  assign out_38 = decoder_2_out28 ? decoder_1_out0 : 32'bz;  // Controlled_Buffer controlled_buffer_29
  assign out_39 = decoder_2_out29 ? decoder_1_out0 : 32'bz;  // Controlled_Buffer controlled_buffer_30
  assign out_40 = decoder_2_out30 ? decoder_1_out0 : 32'bz;  // Controlled_Buffer controlled_buffer_31
  assign out_41 = decoder_2_out31 ? decoder_1_out0 : 32'bz;  // Controlled_Buffer controlled_buffer_32
  Pull_Resistor pull_resistor_1 (.node(out_37));
  Pull_Resistor pull_resistor_2 (.node(out_35));
  Pull_Resistor pull_resistor_3 (.node(out_41));
  Pull_Resistor pull_resistor_4 (.node(out_34));
  Pull_Resistor pull_resistor_5 (.node(out_40));
  Pull_Resistor pull_resistor_6 (.node(out_38));
  Pull_Resistor pull_resistor_7 (.node(out_36));
  Pull_Resistor pull_resistor_8 (.node(out_39));
  Pull_Resistor pull_resistor_9 (.node(out_31));
  Pull_Resistor pull_resistor_10 (.node(out_30));
  Pull_Resistor pull_resistor_11 (.node(out_27));
  Pull_Resistor pull_resistor_12 (.node(out_26));
  Pull_Resistor pull_resistor_13 (.node(out_28));
  Pull_Resistor pull_resistor_14 (.node(out_32));
  Pull_Resistor pull_resistor_15 (.node(out_29));
  Pull_Resistor pull_resistor_16 (.node(out_33));
  Pull_Resistor pull_resistor_17 (.node(out_22));
  Pull_Resistor pull_resistor_18 (.node(out_25));
  Pull_Resistor pull_resistor_19 (.node(out_18));
  Pull_Resistor pull_resistor_20 (.node(out_20));
  Pull_Resistor pull_resistor_21 (.node(out_19));
  Pull_Resistor pull_resistor_22 (.node(out_24));
  Pull_Resistor pull_resistor_23 (.node(out_23));
  Pull_Resistor pull_resistor_24 (.node(out_21));
  Pull_Resistor pull_resistor_25 (.node(out_11));
  Pull_Resistor pull_resistor_26 (.node(out_10));
  Pull_Resistor pull_resistor_27 (.node(out_16));
  Pull_Resistor pull_resistor_28 (.node(out_15));
  Pull_Resistor pull_resistor_29 (.node(out_13));
  Pull_Resistor pull_resistor_30 (.node(out_12));
  Pull_Resistor pull_resistor_31 (.node(out_14));
  Pull_Resistor pull_resistor_32 (.node(out_17));

  // Other names for the same wires on the sheet: player_y[4:0] = player_x
endmodule

module collisionCheck (
  input  [4:0] player_x,
  input  [4:0] player_x_1,
  input  [4:0] player_x_1_2,
  input  [4:0] ball_x,
  input  [4:0] ball_y,
  input  [4:0] coordinate_to_check,
  output hit_x,
  output hit_x_1,
  output hit_x_1_2,
  output hit_x_2,
  output hit_x_2_2
);

  wire comparator_1_eq, comparator_2_eq, comparator_3_eq, comparator_4_eq, comparator_5_lt, comparator_6_eq,
       comparator_7_eq, comparator_8_gt;
  wire [4:0] adder_1_out, subtractor_1_out;

  Adder #(.width(5)) adder_1 (.a(player_x), .b(5'b00010), .out(adder_1_out));  // open: cin, cout
  Subtractor #(.width(5)) subtractor_1 (.a(player_x), .b(5'b00010), .out(subtractor_1_out));  // open: bin, bout
  Comparator #(.width(5), .mode("unsigned")) comparator_1 (
    .a(player_x), .b(ball_x), .eq(comparator_1_eq));  // open: gt, lt
  Comparator #(.width(5), .mode("unsigned")) comparator_2 (
    .a(player_x_1), .b(ball_x), .eq(comparator_2_eq));  // open: gt, lt
  Comparator #(.width(5), .mode("unsigned")) comparator_3 (
    .a(player_x_1_2), .b(ball_x), .eq(comparator_3_eq));  // open: gt, lt
  Comparator #(.width(5)) comparator_4 (.a(ball_y), .b(coordinate_to_check), .eq(comparator_4_eq));  // open: gt, lt
  Comparator #(.width(5), .mode("unsigned")) comparator_5 (
    .a(player_x), .b(5'b11110), .lt(comparator_5_lt));  // open: gt, eq
  Comparator #(.width(5), .mode("unsigned")) comparator_6 (
    .a(adder_1_out), .b(ball_x), .eq(comparator_6_eq));  // open: gt, lt
  Comparator #(.width(5), .mode("unsigned")) comparator_7 (
    .a(subtractor_1_out), .b(ball_x), .eq(comparator_7_eq));  // open: gt, lt
  Comparator #(.width(5), .mode("unsigned")) comparator_8 (
    .a(player_x), .b(5'b00001), .gt(comparator_8_gt));  // open: eq, lt
  and and_1 (hit_x, comparator_1_eq, comparator_4_eq);
  and and_2 (hit_x_1, comparator_2_eq, comparator_4_eq);
  and and_3 (hit_x_1_2, comparator_3_eq, comparator_4_eq);
  and and_4 (hit_x_2, comparator_5_lt, comparator_6_eq, comparator_4_eq);
  and and_5 (hit_x_2_2, comparator_7_eq, comparator_4_eq);
endmodule

module clock_frequency_divider (
  input  [7:0] speed,
  output game_clk,
  output cdm8_clk
);

  wire counter_1_carry;

  Clock clock_1 (.out(cdm8_clk));
  Counter #(.ongoal("load")) counter_1 (
    .load(1'b1), .D(speed), .count(1'b1), .carry(counter_1_carry), .clk(cdm8_clk));  // open: Q, clr
  T_Flip_Flop t_ff_1 (.clk(counter_1_carry), .T(1'b1), .Q(game_clk), .en(1'b1));  // open: Qn, preset, reset
  LED led_1 (.in(game_clk));
endmodule

module test (
);

  wire and_1_out, and_2_out, and_3_out, button_1_out, cdm8_clk, comparator_1_eq, counter_1_carry, init_table,
       not_1_out, not_2_out, or_1_out, R, rd_wr, undriven_2, xnor_1_out, xnor_2_out;
  wire [0:0] I_O_data_read;
  wire [3:0] undriven;
  wire [5:0] counter_1_q;
  wire [7:0] bit_extender_1_out, bit_extender_2_out, I_O_data_write, init_addr, init_data;

  Comparator #(.width(4), .mode("unsigned")) comparator_1 (
    .a(undriven), .b(4'b0100), .eq(comparator_1_eq));  // open: gt, lt
  Button button_1 (.out(button_1_out));
  not not_1 (not_1_out, button_1_out);
  not not_2 (not_2_out, R);
  and and_1 (and_1_out, undriven_2, comparator_1_eq);
  xnor xnor_1 (xnor_1_out, button_1_out, not_1_out);
  or or_1 (or_1_out, xnor_1_out, xnor_2_out);
  xnor xnor_2 (xnor_2_out, R, not_2_out);
  and and_2 (and_2_out, ~rd_wr, and_1_out);  // AND_Gate
  S_R_Flip_Flop s_r_ff_1 (
    .S(I_O_data_read[0]), .clk(cdm8_clk), .R(counter_1_carry), .Q(init_table), .reset(counter_1_carry),
    .en(and_2_out));  // open: Qn, preset
  assign bit_extender_1_out = {{7{1'b0}}, init_table};  // Bit_Extender bit_extender_1
  assign I_O_data_write = and_3_out ? bit_extender_1_out : 8'bz;  // Controlled_Buffer controlled_buffer_1
  and and_3 (and_3_out, rd_wr, and_1_out);
  Counter #(.width(6), .max('h2c), .ongoal("stay")) counter_1 (
    .count(init_table), .Q(counter_1_q), .carry(counter_1_carry), .clk(cdm8_clk), .clr(or_1_out));  // open: load, D
  assign bit_extender_2_out = {{2{1'b0}}, counter_1_q};  // Bit_Extender bit_extender_2
  Adder adder_1 (.a(bit_extender_2_out), .b(8'h10), .out(init_addr));  // open: cin, cout
  ROM rom_1 (.addr(bit_extender_2_out), .data(init_data), .sel(1'b1));

  // Notes on the sheet:
  //   DMA_ACTIVE
  //   contents of rom_1 (hex, n*v repeats v):
  //   0 49 72 74 65 67 6f 76 0 0 4e 61 7a 61 72 6f 76 0 0 42 6f 6e 64 61 72 65 76 0 49 76 61 6e 6f 76 0 0
  //   0 50 65 74 72 6f 76
endmodule

module freeze (
  input  game_clk,
  input  hit_x,
  input  hit_x_1,
  input  hit_x_1_2,
  input  btn_left,
  input  btn_right,
  output freeze
);

  wire and_1_out, and_2_out, d_ff_1_qn, or_1_out, or_2_out, shift_register_1_q0, shift_register_1_q1,
       shift_register_1_q2, shift_register_1_q3, shift_register_1_q4, shift_register_1_q5,
       shift_register_1_q6, shift_register_1_q7;

  or or_1 (or_1_out, hit_x, hit_x_1, hit_x_1_2);
  and and_1 (and_1_out, or_1_out, or_2_out);
  or or_2 (or_2_out, btn_left, btn_right);
  D_Flip_Flop #(.trigger("falling")) d_ff_1 (
    .clk(game_clk), .D(and_1_out), .Qn(d_ff_1_qn));  // open: Q, preset, en, reset
  and and_2 (and_2_out, d_ff_1_qn, and_1_out);
  Shift_Register #(.trigger("falling")) shift_register_1 (
    .shift(1'b1), .in(and_2_out), .clk(game_clk), .q0(shift_register_1_q0), .q1(shift_register_1_q1),
    .q2(shift_register_1_q2), .q3(shift_register_1_q3), .q4(shift_register_1_q4), .q5(shift_register_1_q5),
    .q6(shift_register_1_q6), .q7(shift_register_1_q7));  // open: out, load, clr, d0, d1, d2, d3, d4, d5, d6, d7
  or or_3 (freeze, shift_register_1_q7, shift_register_1_q6, shift_register_1_q5, shift_register_1_q4, shift_register_1_q3, shift_register_1_q2, shift_register_1_q1, shift_register_1_q0);
endmodule

module dX (
  input  game_clk,
  input  hit_ai_x,
  input  hit_ai_x_1,
  input  hit_ai_x_1_2,
  input  hit_ai_x_2,
  input  hit_ai_x_2_2,
  input  hit_player_x,
  input  hit_player_x_1,
  input  hit_player_x_1_2,
  input  hit_player_x_2,
  input  hit_player_x_2_2,
  input  btn_left,
  input  btn_right,
  input  freeze,
  input  [4:0] ball_x
);

  wire and_1_out, and_2_out, comparator_1_eq, comparator_2_eq, d_ff_1_q, dX, not_1_out, or_1_out, or_2_out,
       or_3_out, or_4_out, or_5_out, or_6_out, s_r_ff_1_q, s_r_ff_2_q;
  wire [2:0] priority_encoder_1_out;

  or or_1 (or_1_out, hit_ai_x, hit_player_x);
  or or_2 (or_2_out, hit_ai_x_1, hit_ai_x_2, hit_player_x_1, hit_player_x_2);
  or or_3 (or_3_out, hit_ai_x_1_2, hit_ai_x_2_2, hit_player_x_1_2, hit_player_x_2_2);
  or or_4 (or_4_out, or_2_out, or_3_out);
  and and_1 (and_1_out, btn_left, freeze);
  not not_1 (not_1_out, freeze);
  and and_2 (and_2_out, freeze, btn_right);
  S_R_Flip_Flop #(.trigger("falling")) s_r_ff_1 (
    .S(and_1_out), .clk(game_clk), .R(not_1_out), .Q(s_r_ff_1_q));  // open: Qn, preset, reset, en
  S_R_Flip_Flop #(.trigger("falling")) s_r_ff_2 (
    .S(and_2_out), .clk(game_clk), .R(not_1_out), .Q(s_r_ff_2_q));  // open: Qn, preset, reset, en
  Comparator #(.width(5), .mode("unsigned")) comparator_1 (
    .a(ball_x), .b({5{1'b0}}), .eq(comparator_1_eq));  // open: gt, lt
  or or_5 (or_5_out, comparator_1_eq, comparator_2_eq);
  Comparator #(.width(5), .mode("unsigned")) comparator_2 (
    .a(ball_x), .b({5{1'b1}}), .eq(comparator_2_eq));  // open: gt, lt
  or or_6 (or_6_out, or_1_out, or_4_out, s_r_ff_1_q, s_r_ff_2_q, or_5_out);
  D_Flip_Flop #(.trigger("falling")) d_ff_1 (.clk(or_6_out), .D(dX), .Q(d_ff_1_q));  // open: Qn, preset, en, reset
  Priority_Encoder priority_encoder_1 (
    .in0(1'b1), .in1(or_2_out), .in2(or_3_out), .in3(s_r_ff_1_q), .in4(s_r_ff_2_q), .in5(comparator_2_eq),
    .in6(comparator_1_eq), .out(priority_encoder_1_out));  // open: in7, en_in, gs, en_out
  Multiplexer #(.select(3), .enable("false")) multiplexer_1 (
    .in0(d_ff_1_q), .in1(1'b0), .in2(1'b1), .in3(1'b0), .in4(1'b1), .in5(1'b1), .in6(1'b0), .out(dX),
    .sel(priority_encoder_1_out));  // open: in7

  // Notes on the sheet:
  //   right_hit_any
  //   center_hit_any
  //   left_hit_any
  //   EVENT_HIT_RIGHT_WALL
  //   EVENT_HIT_LEFT_WALL
endmodule
